// Logisim project RandomSequence.circ as structural Verilog: 1 circuit, main circuit main
module main (
  input  in_1,
  input  in_2,
  input  in_3,
  input  in_4
);

  wire xor_1_out, xor_2_out, xor_3_out;
  wire [3:0] shrg4u_1_q0, shrg4u_2_q0;

  SHRG4U shrg4u_1 (
    .CLK(in_1), .CLR_L(in_2), .RIN(xor_3_out), .Q3(shrg4u_1_q0[3]), .Q2(shrg4u_1_q0[2]), .D3(1'b1),
    .D2(1'b0), .D1(1'b0), .Q1(shrg4u_1_q0[1]), .Q0(shrg4u_1_q0[0]), .D0(1'b0), .S1(in_4), .S0(in_3));  // open: LIN
  xor xor_1 (xor_1_out, shrg4u_1_q0[0], shrg4u_1_q0[1]);
  SHRG4U shrg4u_2 (
    .CLK(in_1), .CLR_L(in_2), .RIN(shrg4u_1_q0[0]), .Q3(shrg4u_2_q0[3]), .Q2(shrg4u_2_q0[2]), .D3(1'b0),
    .D2(1'b0), .D1(1'b0), .Q1(shrg4u_2_q0[1]), .Q0(shrg4u_2_q0[0]), .D0(1'b0), .S1(in_4), .S0(in_3));  // open: LIN
  xor xor_2 (xor_2_out, shrg4u_2_q0[3], shrg4u_1_q0[3]);
  Hex_Digit_Display hex_digit_display_1 (.value(shrg4u_1_q0));  // open: dp
  xor xor_3 (xor_3_out, xor_2_out, xor_1_out);
  Hex_Digit_Display hex_digit_display_2 (.value(shrg4u_2_q0));  // open: dp

  // Other names for the same wires on the sheet: Clk = in_1; CLR = in_2; S0 = in_3; S1 = in_4
endmodule
