// Logisim project mod_10.circ as structural Verilog: 1 circuit, main circuit main
module main (
  input  [3:0] in_1,
  input  in_2,
  input  in_3,
  input  in_4,
  input  in_5,
  input  in_6
);

  wire RCO;
  wire [3:0] cntr4u_1_q0;

  CNTR4U cntr4u_1 (
    .CLK(in_5), .LD(in_3), .CLR(RCO), .Q0(cntr4u_1_q0[0]), .Q1(cntr4u_1_q0[1]), .D0(in_1[0]), .D1(in_1[1]),
    .D2(in_1[2]), .Q2(cntr4u_1_q0[2]), .Q3(cntr4u_1_q0[3]), .D3(in_1[3]), .ENP(in_6), .ENT(in_4));  // open: RCO
  Comparator #(.width(4)) comparator_1 (.a(cntr4u_1_q0), .b(4'b1001), .eq(RCO));  // open: gt, lt

  // Other names for the same wires on the sheet: Clk = in_5; CLR = in_2; D[3:0] = in_1; ENP = in_6; ENT = in_4;
  //   LD = in_3
endmodule
