// Logisim project 32位乘法器.circ as structural Verilog: 4 circuits, main circuit main
module main (
  input  CLK,
  input  [31:0] X,
  input  [31:0] Y,
  input  Reset
);

  wire LOAD, not_1_out, or_1_out, STOP;
  wire [0:0] adder_1_out_2;
  wire [7:0] counter_1_q;
  wire [30:0] adder_1_out;
  wire [31:0] multiplexer_1_out, multiplexer_2_out, Zh, Zl;
  wire [31:31] adder_1_cout;

  Hex_Digit_Display hex_digit_display_1 (.value(X[31:28]));  // open: dp
  not not_1 (not_1_out, STOP);
  Multiplexer #(.width(32), .enable("false")) multiplexer_1 (
    .in0({32{1'b0}}), .in1(X), .out(multiplexer_1_out), .sel(Zl[0]));
  Hex_Digit_Display hex_digit_display_2 (.value(X[23:20]));  // open: dp
  Hex_Digit_Display hex_digit_display_3 (.value(X[27:24]));  // open: dp
  Adder #(.width(32)) adder_1 (
    .a(multiplexer_1_out), .b(Zh), .out({adder_1_out, adder_1_out_2[0]}), .cin(1'b0), .cout(adder_1_cout[31]));
  Hex_Digit_Display hex_digit_display_4 (.value(X[19:16]));  // open: dp
  Hex_Digit_Display hex_digit_display_5 (.value(X[15:12]));  // open: dp
  Register #(.width(32), .Select("low")) register_1 (
    .D({adder_1_cout[31], adder_1_out}), .en(not_1_out), .Q(Zh), .clk(CLK), .clr(Reset));
  Hex_Digit_Display hex_digit_display_6 (.value(X[11:8]));  // open: dp
  Hex_Digit_Display hex_digit_display_7 (.value(X[7:4]));  // open: dp
  Multiplexer #(.width(32), .enable("false")) multiplexer_2 (
    .in0({adder_1_out_2[0], Zl[31:1]}), .in1(Y), .out(multiplexer_2_out), .sel(LOAD));
  Hex_Digit_Display hex_digit_display_8 (.value(X[3:0]));  // open: dp
  Register #(.width(32), .Select("low")) u_Y (.D(multiplexer_2_out), .en(not_1_out), .Q(Zl), .clk(CLK), .clr(Reset));
  Hex_Digit_Display hex_digit_display_9 (.value(Y[27:24]));  // open: dp
  Hex_Digit_Display hex_digit_display_10 (.value(Y[31:28]));  // open: dp
  or or_1 (or_1_out, Reset, not_1_out);
  Hex_Digit_Display hex_digit_display_11 (.value(Y[23:20]));  // open: dp
  Hex_Digit_Display hex_digit_display_12 (.value(Y[19:16]));  // open: dp
  Counter counter_1 (
    .load(1'b0), .D({8{1'b0}}), .count(or_1_out), .Q(counter_1_q), .clk(CLK), .clr(Reset), .down(1'b0));  // open: carry, preset
  Hex_Digit_Display hex_digit_display_13 (.value(Y[11:8]));  // open: dp
  Hex_Digit_Display hex_digit_display_14 (.value(Y[15:12]));  // open: dp
  Comparator #(.mode("unsigned")) comparator_1 (.a(counter_1_q), .b({8{1'b0}}), .eq(LOAD));  // open: gt, lt
  Comparator #(.mode("unsigned")) comparator_2 (.a(counter_1_q), .b(8'h21), .eq(STOP));  // open: gt, lt
  Hex_Digit_Display hex_digit_display_15 (.value(Y[7:4]));  // open: dp
  Hex_Digit_Display hex_digit_display_16 (.value(Y[3:0]));  // open: dp
  Hex_Digit_Display hex_digit_display_17 (.value(Zh[31:28]));  // open: dp
  Hex_Digit_Display hex_digit_display_18 (.value(Zh[23:20]));  // open: dp
  Hex_Digit_Display hex_digit_display_19 (.value(Zh[27:24]));  // open: dp
  Hex_Digit_Display hex_digit_display_20 (.value(Zh[19:16]));  // open: dp
  Hex_Digit_Display hex_digit_display_21 (.value(Zh[15:12]));  // open: dp
  Hex_Digit_Display hex_digit_display_22 (.value(Zh[11:8]));  // open: dp
  Hex_Digit_Display hex_digit_display_23 (.value(Zh[7:4]));  // open: dp
  Hex_Digit_Display hex_digit_display_24 (.value(Zh[3:0]));  // open: dp
  Hex_Digit_Display hex_digit_display_25 (.value(Zl[31:28]));  // open: dp
  Hex_Digit_Display hex_digit_display_26 (.value(Zl[27:24]));  // open: dp
  Hex_Digit_Display hex_digit_display_27 (.value(Zl[23:20]));  // open: dp
  Hex_Digit_Display hex_digit_display_28 (.value(Zl[15:12]));  // open: dp
  Hex_Digit_Display hex_digit_display_29 (.value(Zl[19:16]));  // open: dp
  Hex_Digit_Display hex_digit_display_30 (.value(Zl[7:4]));  // open: dp
  Hex_Digit_Display hex_digit_display_31 (.value(Zl[11:8]));  // open: dp
  Hex_Digit_Display hex_digit_display_32 (.value(Zl[3:0]));  // open: dp

  // Other names for the same wires on the sheet: RST = Reset

  // Notes on the sheet:
  //   输入引脚
  //   P
  //   请勿修改引脚名称、电路名称及电路封装外观
  //   提示: 采用无符号数一位乘法实现4位二进制乘法器，禁止直接使用乘法器组件
  //   X
  //   输出引脚
  //   =
endmodule

module CNTR4U (
  input  CLK,
  input  LD,
  input  CLR,
  input  D0,
  input  D1,
  input  D2,
  input  D3,
  input  ENP,
  input  ENT,
  output Q0,
  output Q1,
  output Q2,
  output Q3,
  output RCO
);

  wire and_1_out, and_2_out, and_3_out, and_4_out, and_5_out, and_6_out, and_7_out, and_8_out, and_9_out,
       and_10_out, and_11_out, and_12_out, and_13_out, and_14_out, and_15_out, and_16_out, buffer_1_out,
       d_ff_1_qn, d_ff_2_qn, d_ff_3_qn, d_ff_4_qn, not_1_out, not_2_out, not_3_out, or_1_out, or_2_out,
       or_3_out, or_4_out, xor_1_out, xor_2_out, xor_3_out, xor_4_out;

  not not_1 (not_1_out, d_ff_1_qn);
  and and_1 (and_1_out, ~d_ff_2_qn, ~d_ff_1_qn);  // AND_Gate
  and and_2 (and_2_out, ~d_ff_3_qn, ~d_ff_2_qn, ~d_ff_1_qn);  // AND_Gate
  not not_2 (not_2_out, CLK);
  and and_3 (and_3_out, LD, ~buffer_1_out);  // AND_Gate
  buf buffer_1 (buffer_1_out, CLR);
  and and_4 (and_4_out, not_1_out, and_6_out);
  and and_5 (and_5_out, and_1_out, and_6_out);
  and and_6 (and_6_out, ENP, ENT);
  not not_3 (not_3_out, ENT);
  and and_7 (and_7_out, ~and_3_out, ~buffer_1_out);  // AND_Gate
  xor xor_1 (xor_1_out, and_6_out, ~d_ff_1_qn);  // XOR_Gate
  xor xor_2 (xor_2_out, and_4_out, ~d_ff_2_qn);  // XOR_Gate
  xor xor_3 (xor_3_out, and_5_out, ~d_ff_3_qn);  // XOR_Gate
  and and_8 (and_8_out, and_2_out, and_6_out);
  xor xor_4 (xor_4_out, and_8_out, ~d_ff_4_qn);  // XOR_Gate
  and and_9 (and_9_out, and_3_out, D0);
  and and_10 (and_10_out, and_7_out, xor_1_out);
  and and_11 (and_11_out, and_3_out, D1);
  and and_12 (and_12_out, and_7_out, xor_2_out);
  and and_13 (and_13_out, and_3_out, D2);
  and and_14 (and_14_out, and_7_out, xor_3_out);
  and and_15 (and_15_out, and_3_out, D3);
  and and_16 (and_16_out, and_7_out, xor_4_out);
  and and_17 (RCO, ~d_ff_4_qn, ~d_ff_3_qn, ~d_ff_2_qn, ~d_ff_1_qn, ~not_3_out);  // AND_Gate
  or or_1 (or_1_out, and_9_out, and_10_out);
  or or_2 (or_2_out, and_11_out, and_12_out);
  or or_3 (or_3_out, and_13_out, and_14_out);
  or or_4 (or_4_out, and_15_out, and_16_out);
  D_Flip_Flop #(.trigger("falling")) d_ff_1 (
    .clk(not_2_out), .D(or_1_out), .Q(Q0), .Qn(d_ff_1_qn));  // open: preset, reset
  D_Flip_Flop #(.trigger("falling")) d_ff_2 (
    .clk(not_2_out), .D(or_2_out), .Q(Q1), .Qn(d_ff_2_qn));  // open: preset, reset
  D_Flip_Flop #(.trigger("falling")) d_ff_3 (
    .clk(not_2_out), .D(or_3_out), .Q(Q2), .Qn(d_ff_3_qn));  // open: preset, reset
  D_Flip_Flop #(.trigger("falling")) d_ff_4 (
    .clk(not_2_out), .D(or_4_out), .Q(Q3), .Qn(d_ff_4_qn));  // open: preset, reset

  // Notes on the sheet:
  //   输入引脚
  //   请勿修改引脚名称、电路名称及电路封装外观
  //   提示：使用独立逻辑门实现4位二进制同步计数器，禁止直接使用计数器组件。
  //   输出引脚
endmodule

module ADDER4b (
  input  [3:0] X,
  input  [3:0] Y,
  input  Cin,
  output [3:0] F,
  output Cout
);

  wire fa_1_cout, fa_2_cout, fa_3_cout;
  wire [3:0] bit_extender_1_out, xor_1_out;

  assign bit_extender_1_out = {{3{Cin}}, Cin};  // Bit_Extender bit_extender_1
  Hex_Digit_Display hex_digit_display_1 (.value(X), .dp(1'b0));
  assign xor_1_out = bit_extender_1_out ^ Y;  // XOR_Gate xor_1, 4 bits wide
  Hex_Digit_Display hex_digit_display_2 (.value(xor_1_out), .dp(1'b0));
  FA fa_1 (.A(X[0]), .B(xor_1_out[0]), .Cin(Cin), .F(F[0]), .Cout(fa_1_cout));
  Hex_Digit_Display hex_digit_display_3 (.value(F), .dp(1'b0));
  FA fa_2 (.A(X[1]), .B(xor_1_out[1]), .Cin(fa_1_cout), .F(F[1]), .Cout(fa_2_cout));
  FA fa_3 (.A(X[2]), .B(xor_1_out[2]), .Cin(fa_2_cout), .F(F[2]), .Cout(fa_3_cout));
  FA fa_4 (.A(X[3]), .B(xor_1_out[3]), .Cin(fa_3_cout), .F(F[3]), .Cout(Cout));

  // Other names for the same wires on the sheet: SUM[3:0] = F; 操作数x[3:0] = X; 操作数y[3:0] = Y

  // Notes on the sheet:
  //   输入引脚
  //   +
  //   =
  //   请勿修改引脚名称、电路名称及电路封装外观
  //   提示：使用独立逻辑门及全加器FA子电路实现4位二进制数加减法器，禁止直接使用加减法器组件。
  //   输出引脚
endmodule

module FA (
  input  A,
  input  B,
  input  Cin,
  output F,
  output Cout
);

  wire and_1_out, and_2_out, and_3_out;

  xor xor_1 (F, A, B, Cin);
  and and_1 (and_1_out, A, B);
  and and_2 (and_2_out, B, Cin);
  and and_3 (and_3_out, A, Cin);
  or or_1 (Cout, and_1_out, and_2_out, and_3_out);

  // Notes on the sheet:
  //   全加器
endmodule
