// Logisim project 32位快速乘法器.circ as structural Verilog: 3 circuits, main circuit main
module main (
  input  [31:0] in_1,
  input  [31:0] in_2,
  output [31:0] out_3,
  output [31:0] out_4
);

  wire adder_1_cout, adder_2_cout, adder_3_cout;
  wire [31:0] adder_1_out, adder_3_out, mul16_1_out_3, mul16_2_out_3, mul16_3_out_3, mul16_4_out_3;

  // Probe on in_1
  MUL16 mul16_1 (.in_1(in_1[15:0]), .in_2(in_2[15:0]), .out_3(mul16_1_out_3));
  MUL16 mul16_2 (.in_1(in_1[15:0]), .in_2(in_2[31:16]), .out_3(mul16_2_out_3));
  MUL16 mul16_3 (.in_1(in_2[15:0]), .in_2(in_1[31:16]), .out_3(mul16_3_out_3));
  MUL16 mul16_4 (.in_1(in_1[31:16]), .in_2(in_2[31:16]), .out_3(mul16_4_out_3));
  // Probe on in_2
  Adder #(.width(32)) adder_1 (
    .a(mul16_1_out_3), .b({mul16_2_out_3[15:0], {16{1'b0}}}), .out(adder_1_out), .cout(adder_1_cout));  // open: cin
  Adder #(.width(32)) adder_2 (
    .a(adder_1_out), .b({mul16_3_out_3[15:0], {16{1'b0}}}), .out(out_4), .cin(adder_1_cout),
    .cout(adder_2_cout));
  Adder #(.width(32)) adder_3 (
    .a({{16{1'b0}}, mul16_2_out_3[31:16]}), .b({{16{1'b0}}, mul16_3_out_3[31:16]}), .out(adder_3_out),
    .cin(adder_2_cout), .cout(adder_3_cout));
  // Probe on out_3
  Adder #(.width(32)) adder_4 (.a(adder_3_out), .b(mul16_4_out_3), .out(out_3), .cin(adder_3_cout));  // open: cout
  // Probe on out_4

  // Other names for the same wires on the sheet: A[31:0] = in_1; B[31:0] = in_2; Result_H[31:0] = out_3;
  //   Result_L[31:0] = out_4
endmodule

module MUL8 (
  input  [7:0] in_1,
  input  [7:0] in_2,
  output [15:0] out_3
);

  wire [7:0] PP1;
  wire [8:1] PP2;
  wire [9:2] PP3;
  wire [10:3] PP4;
  wire [11:4] PP5;
  wire [12:5] PP6;
  wire [13:6] PP7;
  wire [14:7] PP8;
  wire [15:0] adder_1_out, adder_2_out, adder_3_out, adder_4_out, adder_5_out, adder_6_out;

  Multiplexer #(.width(8), .enable("false")) multiplexer_1 (.in0({8{1'b0}}), .in1(in_2), .out(PP1), .sel(in_1[0]));
  Adder #(.width(16)) adder_1 (.a({{8{1'b0}}, PP1}), .b({{7{1'b0}}, PP2, 1'b0}), .out(adder_1_out));  // open: cin, cout
  Adder #(.width(16)) adder_2 (
    .a({{6{1'b0}}, PP3, 2'b00}), .b({{5{1'b0}}, PP4, 3'b000}), .out(adder_2_out));  // open: cin, cout
  Adder #(.width(16)) adder_3 (
    .a({4'b0000, PP5, 4'b0000}), .b({3'b000, PP6, {5{1'b0}}}), .out(adder_3_out));  // open: cin, cout
  Adder #(.width(16)) adder_4 (
    .a({2'b00, PP7, {6{1'b0}}}), .b({1'b0, PP8, {7{1'b0}}}), .out(adder_4_out));  // open: cin, cout
  Multiplexer #(.width(8), .enable("false")) multiplexer_2 (.in0({8{1'b0}}), .in1(in_2), .out(PP2), .sel(in_1[1]));
  Adder #(.width(16)) adder_5 (.a(adder_1_out), .b(adder_2_out), .out(adder_5_out));  // open: cin, cout
  Adder #(.width(16)) adder_6 (.a(adder_3_out), .b(adder_4_out), .out(adder_6_out));  // open: cin, cout
  // Probe on out_3
  Adder #(.width(16)) adder_7 (.a(adder_5_out), .b(adder_6_out), .out(out_3));  // open: cin, cout
  Multiplexer #(.width(8), .enable("false")) multiplexer_3 (.in0({8{1'b0}}), .in1(in_2), .out(PP3), .sel(in_1[2]));
  Multiplexer #(.width(8), .enable("false")) multiplexer_4 (.in0({8{1'b0}}), .in1(in_2), .out(PP4), .sel(in_1[3]));
  Multiplexer #(.width(8), .enable("false")) multiplexer_5 (.in0({8{1'b0}}), .in1(in_2), .out(PP5), .sel(in_1[4]));
  Multiplexer #(.width(8), .enable("false")) multiplexer_6 (.in0({8{1'b0}}), .in1(in_2), .out(PP6), .sel(in_1[5]));
  Multiplexer #(.width(8), .enable("false")) multiplexer_7 (.in0({8{1'b0}}), .in1(in_2), .out(PP7), .sel(in_1[6]));
  Multiplexer #(.width(8), .enable("false")) multiplexer_8 (.in0({8{1'b0}}), .in1(in_2), .out(PP8), .sel(in_1[7]));

  // Other names for the same wires on the sheet: A[7:0] = in_1; B[7:0] = in_2; Result[15:0] = out_3
endmodule

module MUL16 (
  input  [15:0] in_1,
  input  [15:0] in_2,
  output [31:0] out_3
);

  wire [15:0] mul8_1_out_3, mul8_2_out_3, mul8_3_out_3, mul8_4_out_3;
  wire [31:0] adder_1_out, adder_2_out;

  // Probe on in_1
  MUL8 mul8_1 (.in_1(in_1[7:0]), .in_2(in_2[7:0]), .out_3(mul8_1_out_3));
  MUL8 mul8_2 (.in_1(in_1[7:0]), .in_2(in_2[15:8]), .out_3(mul8_2_out_3));
  MUL8 mul8_3 (.in_1(in_2[7:0]), .in_2(in_1[15:8]), .out_3(mul8_3_out_3));
  MUL8 mul8_4 (.in_1(in_1[15:8]), .in_2(in_2[15:8]), .out_3(mul8_4_out_3));
  // Probe on in_2
  Adder #(.width(32)) adder_1 (
    .a({{16{1'b0}}, mul8_1_out_3}), .b({{8{1'b0}}, mul8_2_out_3, {8{1'b0}}}), .out(adder_1_out));  // open: cin, cout
  Adder #(.width(32)) adder_2 (
    .a({{8{1'b0}}, mul8_3_out_3, {8{1'b0}}}), .b({mul8_4_out_3, {16{1'b0}}}), .out(adder_2_out));  // open: cin, cout
  // Probe on out_3
  Adder #(.width(32)) adder_3 (.a(adder_1_out), .b(adder_2_out), .out(out_3));  // open: cin, cout

  // Other names for the same wires on the sheet: A[15:0] = in_1; B[15:0] = in_2; Result[31:0] = out_3
endmodule
