// Logisim project 64位二进制快速加法器.circ as structural Verilog: 1 circuit, main circuit Adder64
// 加法器
module Adder64 (
  input  Cin,
  input  [31:0] X,
  input  [31:0] X_2,
  input  [31:0] Y,
  input  [31:0] Y_2,
  output CF,
  output OF,
  output Cout,
  output SF,
  output ZF,
  output [31:0] S,
  output [31:0] S_2
);

  wire and_1_out, and_2_out, and_3_out, and_4_out, clu4_1_c1, clu4_1_c2, clu4_1_c3, comparator_1_eq,
       comparator_2_eq, main_1_gg, main_1_pg, main_2_gg, main_2_pg, main_3_gg, main_3_pg, main_4_gg,
       main_4_pg, not_1_out, not_2_out, not_3_out;

  xor xor_1 (CF, Cout, Cin);
  not not_1 (not_1_out, X[31]);
  not not_2 (not_2_out, S[31]);
  lab4_2_main main_1 (
    .X(X[31:16]), .Y(Y[31:16]), .C0(clu4_1_c3), .S(S[31:16]), .C16(Cout), .Pg(main_1_pg), .Gg(main_1_gg));
  not not_3 (not_3_out, Y[31]);
  and and_1 (and_1_out, Y[31], X[31]);
  and and_2 (and_2_out, and_1_out, not_2_out);
  and and_3 (and_3_out, not_3_out, not_1_out);
  lab4_2_main main_2 (
    .X(X[15:0]), .Y(Y[15:0]), .C0(clu4_1_c2), .S(S[15:0]), .Pg(main_2_pg), .Gg(main_2_gg));  // open: C16
  or or_1 (OF, and_2_out, and_4_out);
  and and_4 (and_4_out, and_3_out, S[31]);
  Comparator #(.width(32), .mode("unsigned")) comparator_1 (
    .a(S), .b({32{1'b0}}), .eq(comparator_1_eq));  // open: gt, lt
  CLU4 clu4_1 (
    .P0(main_4_pg), .P1(main_3_pg), .P2(main_2_pg), .P3(main_1_pg), .C1(clu4_1_c1), .C3(clu4_1_c3),
    .G0(main_4_gg), .G1(main_3_gg), .G2(main_2_gg), .G3(main_1_gg), .C2(clu4_1_c2), .C0(Cin));  // open: C4, Pg, Gg
  // Probe on X
  // Probe on Y
  // Probe on S
  lab4_2_main main_3 (
    .X(X_2[31:16]), .Y(Y_2[31:16]), .C0(clu4_1_c1), .S(S_2[31:16]), .Pg(main_3_pg), .Gg(main_3_gg));  // open: C16
  // Probe on X_2
  // Probe on Y_2
  // Probe on S_2
  lab4_2_main main_4 (
    .X(X_2[15:0]), .Y(Y_2[15:0]), .C0(Cin), .S(S_2[15:0]), .Pg(main_4_pg), .Gg(main_4_gg));  // open: C16
  Comparator #(.width(32), .mode("unsigned")) comparator_2 (
    .a(S_2), .b({32{1'b0}}), .eq(comparator_2_eq));  // open: gt, lt
  and and_5 (ZF, comparator_1_eq, comparator_2_eq);

  assign SF = S[31];

  // Other names for the same wires on the sheet: S1[31:0] = S; S0[31:0] = S_2; X0[31:0] = X_2; X1[31:0] = X;
  //   Y0[31:0] = Y_2; Y1[31:0] = Y

  // Notes on the sheet:
  //   X_2: pull=down
  //   Y: pull=down
  //   Cin: pull=down
  //   Y_2: pull=down
  //   X: pull=down
  //   输入引脚区
  //   输出引脚区
  //   请勿修改引脚名称、电路名称及电路封装外观
  //   提示：使用16位并行加法器子电路实现32位快速加法器
  //   功能说明:32位Adder  S=X+Y，Cout为最高位进位位，Cin为进位输入， S为和，溢出OF、进位CF、零ZF、符号SF。
  //   +
  //   =
  //   无符号加法
endmodule
