// Logisim project lab4.3.circ as structural Verilog: 1 circuit, main circuit Adder32
// 加法器
module Adder32 (
  input  Cin,
  input  [31:0] X,
  input  [31:0] Y,
  output CF,
  output Cout,
  output OF,
  output SF,
  output [31:0] S,
  output ZF
);

  wire and_1_out, and_2_out, and_3_out, main_2_gg, main_2_pg, or_1_out;

  lab4_2_main main_1 (.X(X[31:16]), .Y(Y[31:16]), .C0(or_1_out), .S(S[31:16]), .C16(Cout));  // open: Pg, Gg
  and and_1 (and_1_out, ~Y[31], ~X[31], S[31]);  // AND_Gate
  and and_2 (and_2_out, Y[31], X[31], ~S[31]);  // AND_Gate
  and and_3 (and_3_out, Cin, main_2_pg);
  or or_1 (or_1_out, and_3_out, main_2_gg);
  or or_2 (OF, and_1_out, and_2_out);
  lab4_2_main main_2 (.X(X[15:0]), .Y(Y[15:0]), .C0(Cin), .S(S[15:0]), .Pg(main_2_pg), .Gg(main_2_gg));  // open: C16
  xor xor_1 (CF, Cout, Cin);
  // Probe on X
  // Probe on Y
  // Probe on S
  Comparator #(.width(32)) comparator_1 (.a({32{1'b0}}), .b(S), .eq(ZF));  // open: gt, lt

  assign SF = S[31];

  // Notes on the sheet:
  //   Cin: pull=down
  //   Y: pull=down
  //   X: pull=down
  //   输入引脚区
  //   输出引脚区
  //   请勿修改引脚名称、电路名称及电路封装外观
  //   提示：使用16位并行加法器子电路实现32位快速加法器
  //   功能说明:32位Adder  S=X+Y，Cout为最高位进位位，Cin为进位输入， S为和，溢出OF、进位CF、零ZF、符号SF。
  //   +
  //   =
  //   无符号加法
endmodule
