// Logisim project lab5.2.circ as structural Verilog: 2 circuits, main circuit DataRam
// DataRAM
module DataRam (
  input  CLK,
  input  CLR,
  input  WE,
  input  [2:0] MemOp,
  input  [17:0] Addr,
  input  [31:0] Din,
  output AlignErr,
  output [31:0] DataOut
);

  wire and_1_out, and_3_out, and_4_out, and_5_out, or_1_out, or_2_out, or_3_out, or_4_out;
  wire [3:0] SEL;
  wire [7:0] multiplexer_4_out, multiplexer_5_out, multiplexer_6_out;
  wire [31:0] bit_extender_1_out, bit_extender_2_out, bit_extender_3_out, bit_extender_4_out,
       bit_extender_5_out, bit_extender_6_out, Din_Aligened, multiplexer_1_out, multiplexer_2_out, RESULT,
       shifter_1_out, shifter_2_out, shifter_3_out, shifter_4_out;

  assign bit_extender_1_out = {{24{1'b0}}, Din[7:0]};  // Bit_Extender bit_extender_1
  assign bit_extender_2_out = {{16{1'b0}}, Din[15:0]};  // Bit_Extender bit_extender_2
  Shifter #(.width(32)) shifter_1 (.in(bit_extender_1_out), .\dist (5'b01000), .out(shifter_1_out));
  Shifter #(.width(32)) shifter_2 (.in(bit_extender_1_out), .\dist (5'b10000), .out(shifter_2_out));
  Shifter #(.width(32)) shifter_3 (.in(bit_extender_1_out), .\dist (5'b11000), .out(shifter_3_out));
  Shifter #(.width(32)) shifter_4 (.in(bit_extender_2_out), .\dist (5'b10000), .out(shifter_4_out));
  SEL sel_1 (
    .Mem2(MemOp[2]), .Mem1(MemOp[1]), .Mem0(MemOp[0]), .Addr1(Addr[1]), .Addr0(Addr[0]), .Sel3(SEL[3]),
    .Sel2(SEL[2]), .Sel1(SEL[1]), .Sel0(SEL[0]));
  and and_1 (and_1_out, SEL[3], WE);
  Multiplexer #(.select(2), .width(32), .enable("false")) multiplexer_1 (
    .in0(bit_extender_1_out), .in1(shifter_1_out), .in2(shifter_2_out), .in3(shifter_3_out),
    .out(multiplexer_1_out), .sel(Addr[1:0]));
  Multiplexer #(.select(2), .width(32), .enable("false")) multiplexer_2 (
    .in0(bit_extender_2_out), .in2(shifter_4_out), .out(multiplexer_2_out), .sel(Addr[1:0]));  // open: in1, in3
  or or_1 (or_1_out, SEL[3], WE);
  RAM #(.addrWidth(16), .bus("separate"), .Select("high"), .simpleMode("false")) ram_1 (
    .addr(Addr[17:2]), .din(Din_Aligened[31:24]), .data(RESULT[31:24]), .str(and_1_out), .sel(or_1_out),
    .clk(CLK), .clr(CLR));  // open: ld
  and and_2 (AlignErr, ~SEL[3], ~SEL[2], ~SEL[1], ~SEL[0]);  // AND_Gate
  Multiplexer #(.select(3), .width(32), .enable("false")) multiplexer_3 (
    .in0(Din), .in5(multiplexer_1_out), .in6(multiplexer_2_out), .out(Din_Aligened), .sel(MemOp));  // open: in1, in2, in3, in4, in7
  and and_3 (and_3_out, SEL[2], WE);
  RAM #(.addrWidth(16), .bus("separate"), .Select("high"), .simpleMode("false")) ram_2 (
    .addr(Addr[17:2]), .din(Din_Aligened[23:16]), .data(RESULT[23:16]), .str(and_3_out), .sel(or_2_out),
    .clk(CLK), .clr(CLR));  // open: ld
  or or_2 (or_2_out, SEL[2], WE);
  and and_4 (and_4_out, SEL[1], WE);
  RAM #(.addrWidth(16), .bus("separate"), .Select("high"), .simpleMode("false")) ram_3 (
    .addr(Addr[17:2]), .din(Din_Aligened[15:8]), .data(RESULT[15:8]), .str(and_4_out), .sel(or_3_out),
    .clk(CLK), .clr(CLR));  // open: ld
  or or_3 (or_3_out, SEL[1], WE);
  and and_5 (and_5_out, SEL[0], WE);
  RAM #(.addrWidth(16), .bus("separate"), .Select("high"), .simpleMode("false")) ram_4 (
    .addr(Addr[17:2]), .din(Din_Aligened[7:0]), .data(RESULT[7:0]), .str(and_5_out), .sel(or_4_out),
    .clk(CLK), .clr(CLR));  // open: ld
  or or_4 (or_4_out, SEL[0], WE);
  Multiplexer #(.select(4), .width(8), .enable("false")) multiplexer_4 (
    .in1(RESULT[7:0]), .in2(RESULT[15:8]), .in4(RESULT[23:16]), .in8(RESULT[31:24]), .out(multiplexer_4_out),
    .sel(SEL));  // open: in0, in3, in5, in6, in7, in9, in10, in11, in12, in13, in14, in15
  Multiplexer #(.select(4), .width(8), .enable("false")) multiplexer_5 (
    .in3(RESULT[7:0]), .in12(RESULT[23:16]), .out(multiplexer_5_out), .sel(SEL));  // open: in0, in1, in2, in4, in5, in6, in7, in8, in9, in10, in11, in13, in14, in15
  Multiplexer #(.select(4), .width(8), .enable("false")) multiplexer_6 (
    .in3(RESULT[15:8]), .in12(RESULT[31:24]), .out(multiplexer_6_out), .sel(SEL));  // open: in0, in1, in2, in4, in5, in6, in7, in8, in9, in10, in11, in13, in14, in15
  assign bit_extender_3_out = {{24{1'b0}}, multiplexer_4_out};  // Bit_Extender bit_extender_3
  assign bit_extender_4_out = {{24{multiplexer_4_out[7]}}, multiplexer_4_out};  // Bit_Extender bit_extender_4
  assign bit_extender_5_out = {{16{1'b0}}, {multiplexer_6_out, multiplexer_5_out}};  // Bit_Extender bit_extender_5
  assign bit_extender_6_out = {{16{multiplexer_6_out[7]}}, {multiplexer_6_out, multiplexer_5_out}};  // Bit_Extender bit_extender_6
  Multiplexer #(.select(3), .width(32), .enable("false")) multiplexer_7 (
    .in0(RESULT), .in1(bit_extender_3_out), .in2(bit_extender_5_out), .in5(bit_extender_4_out),
    .in6(bit_extender_6_out), .out(DataOut), .sel(MemOp));  // open: in3, in4, in7

  // Other names for the same wires on the sheet: AddrS[1:0] = Addr[1:0]; AddrR[15:0] = Addr[17:2];
  //   Dout[31:0] = DataOut

  // Notes on the sheet:
  //   输入引脚
  //   请勿修改引脚名称、电路名称及电路封装外观
  //   为了后续实验中的引用，不要修改MemOp的编码定义、引脚名称和在布局中的位置。
  //   32位数据存储器，按字节分4片存储，可按照字节、半字和字进行存储；读取字节或半字时，支持0扩展和符号位扩展。
  //   SEL3
  //   输出引脚
  //   SEL2
  //   SEL1
  //   SEL0
endmodule

module SEL (
  input  Mem2,
  input  Mem1,
  input  Mem0,
  input  Addr1,
  input  Addr0,
  output Sel3,
  output Sel2,
  output Sel1,
  output Sel0
);

  wire and_1_out, and_2_out, and_3_out, and_4_out, and_5_out, and_6_out, and_7_out, and_8_out, and_9_out,
       and_10_out, and_11_out, and_12_out, not_1_out, not_2_out, not_3_out, not_4_out, not_5_out, not_6_out,
       not_7_out, not_8_out, not_9_out, not_10_out, not_11_out, not_12_out, not_13_out, not_14_out,
       not_15_out, not_16_out, not_17_out, not_18_out, not_19_out, not_20_out, not_21_out, not_22_out,
       not_23_out, not_24_out, not_25_out, not_26_out, not_27_out, not_28_out, not_29_out, not_30_out,
       not_31_out, not_32_out, not_33_out, not_34_out, not_35_out, not_36_out;

  not not_1 (not_1_out, Mem2);
  not not_2 (not_2_out, Mem1);
  not not_3 (not_3_out, Mem0);
  not not_4 (not_4_out, Addr1);
  not not_5 (not_5_out, Addr0);
  not not_6 (not_6_out, Mem1);
  not not_7 (not_7_out, Mem0);
  not not_8 (not_8_out, Addr0);
  not not_9 (not_9_out, Mem2);
  not not_10 (not_10_out, Mem1);
  not not_11 (not_11_out, Mem0);
  not not_12 (not_12_out, Addr1);
  not not_13 (not_13_out, Addr0);
  not not_14 (not_14_out, Mem1);
  not not_15 (not_15_out, Addr0);
  not not_16 (not_16_out, Mem0);
  not not_17 (not_17_out, Addr0);
  not not_18 (not_18_out, Mem2);
  not not_19 (not_19_out, Mem0);
  not not_20 (not_20_out, Addr1);
  not not_21 (not_21_out, Addr0);
  not not_22 (not_22_out, Mem1);
  not not_23 (not_23_out, Addr1);
  not not_24 (not_24_out, Mem0);
  not not_25 (not_25_out, Addr1);
  not not_26 (not_26_out, Addr0);
  not not_27 (not_27_out, Mem2);
  not not_28 (not_28_out, Mem1);
  not not_29 (not_29_out, Addr1);
  not not_30 (not_30_out, Addr0);
  not not_31 (not_31_out, Mem1);
  not not_32 (not_32_out, Addr1);
  not not_33 (not_33_out, Addr0);
  not not_34 (not_34_out, Mem0);
  not not_35 (not_35_out, Addr1);
  not not_36 (not_36_out, Addr0);
  and and_1 (and_1_out, not_1_out, not_2_out, not_3_out, not_4_out, not_5_out);
  and and_2 (and_2_out, not_6_out, Mem0, Addr1, Addr0);
  and and_3 (and_3_out, Mem1, not_7_out, Addr1, not_8_out);
  and and_4 (and_4_out, not_9_out, not_10_out, not_11_out, not_12_out, not_13_out);
  and and_5 (and_5_out, not_14_out, Mem0, Addr1, not_15_out);
  and and_6 (and_6_out, Mem1, not_16_out, Addr1, not_17_out);
  and and_7 (and_7_out, not_18_out, not_19_out, not_20_out, not_21_out);
  and and_8 (and_8_out, not_22_out, Mem0, not_23_out, Addr0);
  and and_9 (and_9_out, Mem1, not_24_out, not_25_out, not_26_out);
  and and_10 (and_10_out, not_27_out, not_28_out, not_29_out, not_30_out);
  and and_11 (and_11_out, not_31_out, Mem0, not_32_out, not_33_out);
  and and_12 (and_12_out, Mem1, not_34_out, not_35_out, not_36_out);
  or or_1 (Sel3, and_1_out, and_2_out, and_3_out);
  or or_2 (Sel2, and_4_out, and_5_out, and_6_out);
  or or_3 (Sel1, and_7_out, and_8_out, and_9_out);
  or or_4 (Sel0, and_10_out, and_11_out, and_12_out);
endmodule
