// Logisim project lab5.4.circ as structural Verilog: 3 circuits, main circuit IDU
module IDU (
  input  [31:0] IR,
  input  [31:0] BusW,
  input  [31:0] PC,
  input  [2:0] ExtOp,
  input  RegWr,
  input  ALUASrc,
  input  [1:0] ALUBSrc,
  input  CLK,
  output [31:0] DataA,
  output [31:0] DataB,
  output [31:0] BusA,
  output [31:0] BusB,
  output [6:0] OpCode,
  output [31:0] Imm,
  output [2:0] Funct3,
  output [6:0] Funct7
);

  \立即数扩展器  \u_立即数扩展器_1  (.Instr(IR), .Extop(ExtOp), .imm(Imm));
  RegFile regfile_1 (
    .R1_num(IR[19:15]), .R2_num(IR[24:20]), .Write_Reg_num(IR[11:7]), .Din(BusW), .Reg1Out(BusA),
    .Reg2Out(BusB), .Write_Enable(RegWr), .Clock(CLK));
  Multiplexer #(.width(32), .enable("false")) multiplexer_1 (.in0(BusA), .in1(PC), .out(DataA), .sel(ALUASrc));
  Multiplexer #(.select(2), .width(32), .enable("false")) multiplexer_2 (
    .in0(BusB), .in1(32'h4), .in2(Imm), .out(DataB), .sel(ALUBSrc));  // open: in3

  assign Funct3 = IR[14:12];
  assign Funct7 = IR[31:25];
  assign OpCode = IR[6:0];

  // Other names for the same wires on the sheet: op[6:0] = IR[6:0]

  // Notes on the sheet:
  //   ALUBSrc: pull=down
  //   RegWr: pull=down
  //   PC: pull=down
  //   BusW: pull=down
  //   ALUASrc: pull=down
  //   ExtOp: pull=down
  //   输入信号
  //   为了后续实验中的引用，不要修改ALUASrc、ALUBSrc和EXtOP编码定义。
  //   请勿修改引脚名称、电路名称及电路封装外观
  //   输出信号
  //   修改寄存器堆电路设计，0号寄存器始终为0。
endmodule

module \立即数扩展器  (
  input  [31:0] Instr,
  input  [2:0] Extop,
  output [31:0] imm
);

  wire [11:0] bit_extender_2_out;
  wire [19:0] bit_extender_1_out;
  wire [20:0] bit_extender_4_out;
  wire [31:0] bit_extender_3_out;

  assign bit_extender_1_out = {{19{Instr[31]}}, Instr[31]};  // Bit_Extender bit_extender_1
  assign bit_extender_2_out = {{11{Instr[31]}}, Instr[31]};  // Bit_Extender bit_extender_2
  assign bit_extender_3_out = {{20{Instr[31]}}, Instr[31:20]};  // Bit_Extender bit_extender_3
  assign bit_extender_4_out = {{20{Instr[31]}}, Instr[31]};  // Bit_Extender bit_extender_4
  Multiplexer #(.select(3), .width(32), .enable("false")) multiplexer_1 (
    .in0(bit_extender_3_out), .in1({Instr[31:12], {12{1'b0}}}),
    .in2({bit_extender_4_out, Instr[30:25], Instr[11:7]}),
    .in3({bit_extender_1_out, Instr[7], Instr[30:25], Instr[11:8], 1'b0}),
    .in4({bit_extender_2_out, Instr[19:12], Instr[20], Instr[30:21], 1'b0}), .out(imm), .sel(Extop));  // open: in5, in6, in7

  // Notes on the sheet:
  //   Extop: pull=down
  //   Instr: pull=down
  //   输入引脚
  //   请勿修改引脚名称、电路名称及电路封装外观
  //   提示：使用分线器和多路选择器实现立即数扩展器
  //   输出引脚
endmodule

// 寄存器堆
module RegFile (
  input  [4:0] R1_num,
  input  [4:0] R2_num,
  input  [4:0] Write_Reg_num,
  input  [31:0] Din,
  input  Write_Enable,
  input  Clock,
  output [31:0] Reg1Out,
  output [31:0] Reg2Out
);

  wire and_1_out, and_2_out, and_3_out, and_4_out, and_5_out, and_6_out, and_7_out, and_8_out, and_9_out,
       and_10_out, and_11_out, and_12_out, and_13_out, and_14_out, and_15_out, and_16_out, and_17_out,
       and_18_out, and_19_out, and_20_out, and_21_out, and_22_out, and_23_out, and_24_out, and_25_out,
       and_26_out, and_27_out, and_28_out, and_29_out, and_30_out, and_31_out, and_32_out, decoder_1_out0,
       decoder_1_out1, decoder_1_out2, decoder_1_out3, decoder_1_out4, decoder_1_out5, decoder_1_out6,
       decoder_1_out7, decoder_1_out8, decoder_1_out9, decoder_1_out10, decoder_1_out11, decoder_1_out12,
       decoder_1_out13, decoder_1_out14, decoder_1_out15, decoder_1_out16, decoder_1_out17, decoder_1_out18,
       decoder_1_out19, decoder_1_out20, decoder_1_out21, decoder_1_out22, decoder_1_out23, decoder_1_out24,
       decoder_1_out25, decoder_1_out26, decoder_1_out27, decoder_1_out28, decoder_1_out29, decoder_1_out30,
       decoder_1_out31;
  wire [31:0] _0_q, _1_q, _2_q, _3_q, _4_q, _5_q, _6_q, _7_q, _8_q, _9_q, _10_q, _11_q, _12_q, _13_q, _14_q,
       _15_q, _16_q, _17_q, _18_q, _19_q, _20_q, _21_q, _22_q, _23_q, _24_q, _25_q, _26_q, _27_q, _28_q,
       _29_q, _30_q, _31_q;

  Decoder #(.select(5), .enable("false")) decoder_1 (
    .out0(decoder_1_out0), .out1(decoder_1_out1), .out2(decoder_1_out2), .out3(decoder_1_out3),
    .out4(decoder_1_out4), .out5(decoder_1_out5), .out6(decoder_1_out6), .out7(decoder_1_out7),
    .out8(decoder_1_out8), .out9(decoder_1_out9), .out10(decoder_1_out10), .out11(decoder_1_out11),
    .out12(decoder_1_out12), .out13(decoder_1_out13), .out14(decoder_1_out14), .out15(decoder_1_out15),
    .out16(decoder_1_out16), .out17(decoder_1_out17), .out18(decoder_1_out18), .out19(decoder_1_out19),
    .out20(decoder_1_out20), .out21(decoder_1_out21), .out22(decoder_1_out22), .out23(decoder_1_out23),
    .out24(decoder_1_out24), .out25(decoder_1_out25), .out26(decoder_1_out26), .out27(decoder_1_out27),
    .out28(decoder_1_out28), .out29(decoder_1_out29), .out30(decoder_1_out30), .out31(decoder_1_out31),
    .sel(Write_Reg_num));
  and and_1 (and_1_out, decoder_1_out0, Write_Enable);
  and and_2 (and_2_out, decoder_1_out1, Write_Enable);
  and and_3 (and_3_out, decoder_1_out2, Write_Enable);
  and and_4 (and_4_out, decoder_1_out3, Write_Enable);
  and and_5 (and_5_out, decoder_1_out4, Write_Enable);
  and and_6 (and_6_out, decoder_1_out5, Write_Enable);
  and and_7 (and_7_out, decoder_1_out6, Write_Enable);
  and and_8 (and_8_out, decoder_1_out7, Write_Enable);
  and and_9 (and_9_out, decoder_1_out8, Write_Enable);
  and and_10 (and_10_out, decoder_1_out9, Write_Enable);
  and and_11 (and_11_out, decoder_1_out10, Write_Enable);
  and and_12 (and_12_out, decoder_1_out11, Write_Enable);
  and and_13 (and_13_out, decoder_1_out12, Write_Enable);
  and and_14 (and_14_out, decoder_1_out13, Write_Enable);
  and and_15 (and_15_out, decoder_1_out14, Write_Enable);
  and and_16 (and_16_out, decoder_1_out15, Write_Enable);
  and and_17 (and_17_out, decoder_1_out16, Write_Enable);
  and and_18 (and_18_out, decoder_1_out17, Write_Enable);
  and and_19 (and_19_out, decoder_1_out18, Write_Enable);
  and and_20 (and_20_out, decoder_1_out19, Write_Enable);
  and and_21 (and_21_out, decoder_1_out20, Write_Enable);
  and and_22 (and_22_out, decoder_1_out21, Write_Enable);
  and and_23 (and_23_out, decoder_1_out22, Write_Enable);
  and and_24 (and_24_out, decoder_1_out23, Write_Enable);
  and and_25 (and_25_out, decoder_1_out24, Write_Enable);
  and and_26 (and_26_out, decoder_1_out25, Write_Enable);
  and and_27 (and_27_out, decoder_1_out26, Write_Enable);
  and and_28 (and_28_out, decoder_1_out27, Write_Enable);
  and and_29 (and_29_out, decoder_1_out28, Write_Enable);
  and and_30 (and_30_out, decoder_1_out29, Write_Enable);
  and and_31 (and_31_out, decoder_1_out30, Write_Enable);
  and and_32 (and_32_out, decoder_1_out31, Write_Enable);
  Register #(.width(32), .Select("high")) _0 (.D({32{1'b0}}), .en(and_1_out), .Q(_0_q), .clk(Clock));  // open: clr
  Register #(.width(32), .Select("high")) _1 (.D(Din), .en(and_2_out), .Q(_1_q), .clk(Clock));  // open: clr
  Register #(.width(32), .Select("high")) _2 (.D(Din), .en(and_3_out), .Q(_2_q), .clk(Clock));  // open: clr
  Register #(.width(32), .Select("high")) _3 (.D(Din), .en(and_4_out), .Q(_3_q), .clk(Clock));  // open: clr
  Register #(.width(32), .Select("high")) _4 (.D(Din), .en(and_5_out), .Q(_4_q), .clk(Clock));  // open: clr
  Register #(.width(32), .Select("high")) _5 (.D(Din), .en(and_6_out), .Q(_5_q), .clk(Clock));  // open: clr
  Register #(.width(32), .Select("high")) _6 (.D(Din), .en(and_7_out), .Q(_6_q), .clk(Clock));  // open: clr
  Register #(.width(32), .Select("high")) _7 (.D(Din), .en(and_8_out), .Q(_7_q), .clk(Clock));  // open: clr
  Register #(.width(32), .Select("high")) _8 (.D(Din), .en(and_9_out), .Q(_8_q), .clk(Clock));  // open: clr
  Register #(.width(32), .Select("high")) _9 (.D(Din), .en(and_10_out), .Q(_9_q), .clk(Clock));  // open: clr
  Register #(.width(32), .Select("high")) _10 (.D(Din), .en(and_11_out), .Q(_10_q), .clk(Clock));  // open: clr
  Register #(.width(32), .Select("high")) _11 (.D(Din), .en(and_12_out), .Q(_11_q), .clk(Clock));  // open: clr
  Register #(.width(32), .Select("high")) _12 (.D(Din), .en(and_13_out), .Q(_12_q), .clk(Clock));  // open: clr
  Register #(.width(32), .Select("high")) _13 (.D(Din), .en(and_14_out), .Q(_13_q), .clk(Clock));  // open: clr
  Register #(.width(32), .Select("high")) _14 (.D(Din), .en(and_15_out), .Q(_14_q), .clk(Clock));  // open: clr
  Register #(.width(32), .Select("high")) _15 (.D(Din), .en(and_16_out), .Q(_15_q), .clk(Clock));  // open: clr
  Register #(.width(32), .Select("high")) _16 (.D(Din), .en(and_17_out), .Q(_16_q), .clk(Clock));  // open: clr
  Register #(.width(32), .Select("high")) _17 (.D(Din), .en(and_18_out), .Q(_17_q), .clk(Clock));  // open: clr
  Register #(.width(32), .Select("high")) _18 (.D(Din), .en(and_19_out), .Q(_18_q), .clk(Clock));  // open: clr
  Register #(.width(32), .Select("high")) _19 (.D(Din), .en(and_20_out), .Q(_19_q), .clk(Clock));  // open: clr
  Register #(.width(32), .Select("high")) _20 (.D(Din), .en(and_21_out), .Q(_20_q), .clk(Clock));  // open: clr
  Register #(.width(32), .Select("high")) _21 (.D(Din), .en(and_22_out), .Q(_21_q), .clk(Clock));  // open: clr
  Register #(.width(32), .Select("high")) _22 (.D(Din), .en(and_23_out), .Q(_22_q), .clk(Clock));  // open: clr
  Register #(.width(32), .Select("high")) _23 (.D(Din), .en(and_24_out), .Q(_23_q), .clk(Clock));  // open: clr
  Register #(.width(32), .Select("high")) _24 (.D(Din), .en(and_25_out), .Q(_24_q), .clk(Clock));  // open: clr
  Register #(.width(32), .Select("high")) _25 (.D(Din), .en(and_26_out), .Q(_25_q), .clk(Clock));  // open: clr
  Register #(.width(32), .Select("high")) _26 (.D(Din), .en(and_27_out), .Q(_26_q), .clk(Clock));  // open: clr
  Register #(.width(32), .Select("high")) _27 (.D(Din), .en(and_28_out), .Q(_27_q), .clk(Clock));  // open: clr
  Register #(.width(32), .Select("high")) _28 (.D(Din), .en(and_29_out), .Q(_28_q), .clk(Clock));  // open: clr
  Register #(.width(32), .Select("high")) _29 (.D(Din), .en(and_30_out), .Q(_29_q), .clk(Clock));  // open: clr
  Register #(.width(32), .Select("high")) _30 (.D(Din), .en(and_31_out), .Q(_30_q), .clk(Clock));  // open: clr
  Register #(.width(32), .Select("high")) _31 (.D(Din), .en(and_32_out), .Q(_31_q), .clk(Clock));  // open: clr
  Multiplexer #(.select(5), .width(32), .enable("false")) multiplexer_1 (
    .in0(_0_q), .in1(_1_q), .in2(_2_q), .in3(_3_q), .in4(_4_q), .in5(_5_q), .in6(_6_q), .in7(_7_q),
    .in8(_8_q), .in9(_9_q), .in10(_10_q), .in11(_11_q), .in12(_12_q), .in13(_13_q), .in14(_14_q),
    .in15(_15_q), .in16(_16_q), .in17(_17_q), .in18(_18_q), .in19(_19_q), .in20(_20_q), .in21(_21_q),
    .in22(_22_q), .in23(_23_q), .in24(_24_q), .in25(_25_q), .in26(_26_q), .in27(_27_q), .in28(_28_q),
    .in29(_29_q), .in30(_30_q), .in31(_31_q), .out(Reg1Out), .sel(R1_num));
  Multiplexer #(.select(5), .width(32), .enable("false")) multiplexer_2 (
    .in0(_0_q), .in1(_1_q), .in2(_2_q), .in3(_3_q), .in4(_4_q), .in5(_5_q), .in6(_6_q), .in7(_7_q),
    .in8(_8_q), .in9(_9_q), .in10(_10_q), .in11(_11_q), .in12(_12_q), .in13(_13_q), .in14(_14_q),
    .in15(_15_q), .in16(_16_q), .in17(_17_q), .in18(_18_q), .in19(_19_q), .in20(_20_q), .in21(_21_q),
    .in22(_22_q), .in23(_23_q), .in24(_24_q), .in25(_25_q), .in26(_26_q), .in27(_27_q), .in28(_28_q),
    .in29(_29_q), .in30(_30_q), .in31(_31_q), .out(Reg2Out), .sel(R2_num));

  // Other names for the same wires on the sheet: CLK = Clock; RA[4:0] = R1_num; RB[4:0] = R2_num; RDA[31:0] = Reg1Out;
  //   RDB[31:0] = Reg2Out; RW[4:0] = Write_Reg_num; WE = Write_Enable

  // Notes on the sheet:
  //   输入引脚
  //   请勿修改引脚名称、电路名称及电路封装外观
  //   提示：使用译码器、多路选择器和32位寄存器及逻辑门实现寄存器堆，禁止直接使用存储器组件。
  //   输出引脚
endmodule
