// Logisim project lab6.5.circ as structural Verilog: 17 circuits, main circuit main
module main (
  input  ReSet,
  input  [31:0] Init_Addr,
  input  clk,
  output [31:0] PC,
  output [31:0] IR,
  output [31:0] BusW,
  output [31:0] Din,
  output [15:0] Cycles,
  output Halt
);

  wire alu_1_zero, bandj_1_npcasrc, bandj_1_npcbsrc, clk_out, clk_t, comparator_1_eq, comparator_2_eq,
       comparator_3_eq, not_2_out, \控制器_1_aluasrc , \控制器_1_memtoreg , \控制器_1_memwr , \控制器_1_regwr ;
  wire [1:0] \控制器_1_alubsrc ;
  wire [2:0] idu_1_funct3, \控制器_1_bandj , \控制器_1_extop , \控制器_1_memop ;
  wire [3:0] \控制器_1_aluctr ;
  wire [6:0] idu_1_funct7, idu_1_opcode;
  wire [31:0] alu_1_s, dataram_1_dataout, idu_1_busa, idu_1_dataa, idu_1_datab, idu_1_imm;

  Clock u_clk (.out(clk_out));
  not not_1 (clk_t, clk_out);
  IFU ifu_1 (
    .CLK(clk_t), .Reset(ReSet), .NPCASrc(bandj_1_npcasrc), .NPCBSrc(bandj_1_npcbsrc),
    .Initial_Address(Init_Addr), .Imm(idu_1_imm), .BusA(idu_1_busa), .PC(PC), .halt(Halt));
  \控制器  \u_控制器_1  (
    .opcode(idu_1_opcode), .ExtOp(\控制器_1_extop ), .RegWr(\控制器_1_regwr ), .BandJ(\控制器_1_bandj ),
    .funct3(idu_1_funct3), .ALUASrc(\控制器_1_aluasrc ), .ALUBSrc(\控制器_1_alubsrc ), .ALUctr(\控制器_1_aluctr ),
    .funct7(idu_1_funct7), .MemtoReg(\控制器_1_memtoreg ), .MemOp(\控制器_1_memop ), .MemWr(\控制器_1_memwr ));  // open: Halt
  ROM #(.addrWidth(16), .dataWidth(32), .Select("high")) rom_1 (.addr(PC[17:2]), .data(IR));
  IDU idu_1 (
    .OpCode(idu_1_opcode), .ExtOp(\控制器_1_extop ), .RegWr(\控制器_1_regwr ), .Imm(idu_1_imm),
    .Funct3(idu_1_funct3), .ALUASrc(\控制器_1_aluasrc ), .ALUBSrc(\控制器_1_alubsrc ), .Funct7(idu_1_funct7),
    .CLK(clk_t), .IR(IR), .BusW(BusW), .PC(PC), .DataA(idu_1_dataa), .DataB(idu_1_datab), .BusA(idu_1_busa),
    .BusB(Din));
  // Probe on Cycles
  Counter #(.width(16), .max('hffff), .behavior("old")) \u_计数器  (
    .count(not_2_out), .Q(Cycles), .clk(clk_t), .clr(ReSet));  // open: load, D, carry, preset
  not not_2 (not_2_out, Halt);
  BandJ bandj_1 (
    .BandJ(\控制器_1_bandj ), .NPCASrc(bandj_1_npcasrc), .Zero(alu_1_zero), .NPCBSrc(bandj_1_npcbsrc),
    .Result0(alu_1_s[0]));
  ALU alu_1 (.A(idu_1_dataa), .B(idu_1_datab), .ALUctr(\控制器_1_aluctr ), .S(alu_1_s), .Zero(alu_1_zero));
  DataRAM dataram_1 (
    .Addr(alu_1_s[17:0]), .Din(Din), .CLK(clk_t), .CLR(ReSet), .WE(\控制器_1_memwr ), .MemOp(\控制器_1_memop ),
    .DataOut(dataram_1_dataout));  // open: AlignErr
  Comparator #(.width(32), .mode("unsigned")) comparator_1 (.a(IR), .b(32'h73), .eq(comparator_1_eq));  // open: gt, lt
  Comparator #(.width(32), .mode("unsigned")) comparator_2 (.a(IR), .b(32'h6f), .eq(comparator_2_eq));  // open: gt, lt
  Comparator #(.width(32), .mode("unsigned")) comparator_3 (
    .a(IR), .b(32'hdead10cc), .eq(comparator_3_eq));  // open: gt, lt
  Multiplexer #(.width(32), .enable("false")) multiplexer_1 (
    .in0(alu_1_s), .in1(dataram_1_dataout), .out(BusW), .sel(\控制器_1_memtoreg ));
  or or_1 (Halt, comparator_1_eq, comparator_2_eq, comparator_3_eq);

  // Notes on the sheet:
  //   输入引脚
  //   请勿修改引脚名称、电路名称及电路封装外观
  //   指令存储器和数据存储器数据位都是32位，指令存储器编址以字为单位，数据存储器编址以字节为单位。
  //   引用取指令部件、取操作数部件、ALU部件、数据存储器、分支控制器、指令存储器等部件，完成单周期CPU设计。
  //   contents of rom_1 (hex, n*v repeats v):
  //   2297 28293 2a503 313 100393 2050863 100e13 3c50863 200e13 1c54c63 730eb3 700333 1d003b3 1e0e13
  //   fedff06f 7005b3 100006f 593 80006f 100593 2297 fb428293 b2a023 a00893 73 1948*0 a
  //   输出引脚
  //   状态元件的触发条件都设置成上升沿触发，时钟输入信号通过反相器输入。
  //   程序执行周期数
endmodule

module BandJ (
  input  [2:0] BandJ,
  input  Zero,
  input  Result0,
  output NPCASrc,
  output NPCBSrc
);

  wire not_1_out, or_1_out;

  Multiplexer #(.select(3), .enable("false")) multiplexer_1 (
    .in0(1'b0), .in1(1'b0), .in2(1'b1), .in4(1'b0), .in5(1'b0), .in6(1'b0), .in7(1'b0), .out(NPCASrc),
    .sel(BandJ));  // open: in3
  not not_1 (not_1_out, Zero);
  or or_1 (or_1_out, ~Result0, Zero);  // OR_Gate
  Multiplexer #(.select(3), .enable("false")) multiplexer_2 (
    .in0(1'b0), .in1(1'b1), .in2(1'b1), .in4(Zero), .in5(not_1_out), .in6(Result0), .in7(or_1_out),
    .out(NPCBSrc), .sel(BandJ));  // open: in3

  // Notes on the sheet:
  //   BandJ: pull=down
  //   Zero: pull=down
  //   输入信号
  //   请勿修改引脚名称、电路名称及电路封装外观
  //   不要修改控制信号的编码定义、引脚名称和在布局中的位置。
  //   输出信号
endmodule

module IFU (
  input  [31:0] Initial_Address,
  input  [31:0] Imm,
  input  [31:0] BusA,
  input  CLK,
  input  Reset,
  input  halt,
  input  NPCASrc,
  input  NPCBSrc,
  output [31:0] PC
);

  wire nand_1_out;
  wire [31:0] adder_1_out, IR, multiplexer_1_out, multiplexer_2_out, multiplexer_3_out;

  Multiplexer #(.width(32), .enable("false")) multiplexer_1 (
    .in0(PC), .in1(BusA), .out(multiplexer_1_out), .sel(NPCASrc));
  Multiplexer #(.width(32), .enable("false")) multiplexer_2 (
    .in0(32'h4), .in1(Imm), .out(multiplexer_2_out), .sel(NPCBSrc));
  Adder #(.width(32)) adder_1 (.a(multiplexer_1_out), .b(multiplexer_2_out), .out(adder_1_out));  // open: cin, cout
  Multiplexer #(.width(32), .enable("false")) multiplexer_3 (
    .in0(adder_1_out), .in1(Initial_Address), .out(multiplexer_3_out), .sel(Reset));
  nand nand_1 (nand_1_out, ~Reset, halt);  // NAND_Gate
  Register #(.width(32), .Select("low")) u_PC (.D(multiplexer_3_out), .en(nand_1_out), .Q(PC), .clk(CLK));  // open: clr
  ROM #(.addrWidth(16), .dataWidth(32), .Select("high")) Instruction (.addr(PC[17:2]), .data(IR));

  // Other names for the same wires on the sheet: Init_Addr[31:0] = Initial_Address

  // Notes on the sheet:
  //   NPCBSrc: pull=down
  //   NPCASrc: pull=down
  //   BusA: pull=down
  //   Imm: pull=down
  //   请勿修改引脚名称、电路名称及电路封装外观
  //   指令存储器256KB，数据位为32位，地址位为16位。PC寄存器数据宽度32位，片选信号高电平有效
  //   输入信号
  //   输出信号
  //   contents of Instruction (hex, n*v repeats v):
  //   256*0 2083 8133 106213 406293 fff06313 4410663 106193 406393 806413 21b5b3 2058063 3a483 42503
  //   a4b5b3 458c63 a3a023 942023 c0006f 610133 fc9ff06f 4181b3 5383b3 540433 fc9ff06f 6f 0 0 413 9117
  //   ffc10113 94000ef 50463 8067 ff010113 100513 112623 74000ef ff010113 812423 912223 15c00413 1212023
  //   112623 c400493 9840913 442783 42703 4a503 440413 e787b3 40f50533 153513 f42223 448493 fa5ff0ef
  //   fd241ce3 100513 f99ff0ef c12083 812403 412483 12903 513 1010113 8067 1ea02e23 6f ff010113 b800513
  //   112623 f7dff0ef 1ea02e23 6f 0 1 1 2 3 5 8 d 15 22 37 59 90 e9 179 262 3db 63d a18 1055 1a6d 2ac2
  //   452f 6ff1 b520 12511 1da31 2ff42 4d973 7d8b5 cb228 148add 213d05 35c7e2 5704e7 8cccc9 e3d1b0 1709e79
  //   2547029 3c50ea2 6197ecb 1 1 deadbeef 395*0 413 9117 ffc10113 ec000ef 50463 8067 ff010113 100513
  //   112623 cc000ef ff010113 19400813 112623 812423 912223 1212023 100793 f82223 f82023 880593 7c80313
  //   100713 19800513 100893 50493 50793 100693 80006f 7a703 d70633 c7a023 478793 70693 feb796e3 117a023
  //   478593 658663 482703 fc9ff06f 11400413 7c40913 100793 c0006f 4a783 448493 42503 440413 40f50533
  //   153513 f4dff0ef fe8912e3 100513 f41ff0ef c12083 812403 412483 12903 513 1010113 8067 18a02823 6f
  //   ff010113 11000513 112623 f25ff0ef 18a02823 6f 0 1 1e 1b3 fdc 6b0d 22caa 90f6f 1f1058 594efd da4f4e
  //   1ca7357 3418be4 527c829 72363ea 8aaf953 93ee7d0 8aaf953 72363ea 527c829 3418be4 1ca7357 da4f4e
  //   594efd 1f1058 90f6f 22caa 6b0d fdc 1b3 1e 1 2 3 4 5 6 7 8 9 a b c d e f 10 11 12 13 14 15 16 17 18
  //   19 1a 1b 1c 1d 1e 1f deadbeef deadbeef 444*0 413 9117 ffc10113 39c000ef 50463 8067 ff010113 100513
  //   112623 380000ef 259693 d506b3 50893 6a803 60513 6c5dc63 261793 f887b3 7a783 fff50613 261613 c88633
  //   140006f fff50513 472783 6b50863 70613 ffc60713 fef846e3 259693 d886b3 251313 f6a023 688633 4a5de63
  //   68713 c0006f 158593 2a58463 72783 70693 470713 fef856e3 f62023 f8a5cee3 58513 106a023 8067 6886b3
  //   6a783 f62023 106a023 8067 251693 d886b3 f6a023 fe9ff06f 58513 fe1ff06f 1ec5da63 fa010113 4812c23
  //   5612023 3812c23 4112e23 4912a23 5212823 5312623 5412423 5512223 3712e23 3912a23 3a12823 3b12623
  //   58c13 60b13 50413 b0613 c0593 40513 ee9ff0ef a12223 fff50c93 159c5663 c8613 c0593 40513 ecdff0ef
  //   a12423 fff50d13 13ac5263 d0613 c0593 40513 eb1ff0ef a12623 fff50d93 fbc5e63 d8613 c0593 40513
  //   e95ff0ef a12823 fff50993 d3c5a63 98613 c0593 40513 e79ff0ef fff50913 50493 b2c5863 90613 c0593 40513
  //   e5dff0ef fff50b93 50a13 97c5663 b8613 c0593 40513 e41ff0ef a12a23 fff50a93 75c5263 a8613 c0593 40513
  //   e25ff0ef fff50693 50713 4dc5063 68613 c0593 40513 e12e23 d12c23 e01ff0ef 50813 c0593 fff50613 40513
  //   180c13 eadff0ef 1812683 1c12703 fcdc44e3 170c13 fb5c42e3 1412783 178c13 f77c4ee3 1a0c13 f52c4ce3
  //   148c13 f33c4ae3 1012783 178c13 f1bc46e3 c12783 178c13 efac42e3 812783 178c13 eb9c4ee3 412783 178c13
  //   e96c4ae3 5c12083 5812403 5412483 5012903 4c12983 4812a03 4412a83 4012b03 3c12b83 3812c03 3412c83
  //   3012d03 2c12d83 6010113 8067 8067 fe010113 1412423 1300613 593 3c000513 812c23 912a23 1212823
  //   1312623 112e23 3c000493 dddff0ef 3c000913 413 1400993 92503 490913 40850533 153513 140413 cddff0ef
  //   ff3414e3 100513 cd1ff0ef 1300613 593 3c000513 d9dff0ef 413 1400913 4a503 448493 40850533 153513
  //   140413 ca1ff0ef ff2414e3 100513 c95ff0ef 1c12083 1812403 1412483 1012903 c12983 812a03 513 2010113
  //   8067 6f ff010113 3bc00513 112623 f31ff0ef 6f 0 2 c e 6 d f 10 a 0 12 b 13 9 1 7 5 4 3 8 11 deadbeef
  //   deadbeef 63658*0 413 9117 ffc10113 39c000ef 50463 8067 ff010113 100513 112623 380000ef 259693 d506b3
  //   50893 6a803 60513 6c5dc63 261793 f887b3 7a783 fff50613 261613 c88633 140006f fff50513 472783 6b50863
  //   70613 ffc60713 fef846e3 259693 d886b3 251313 f6a023 688633 4a5de63 68713 c0006f 158593 2a58463 72783
  //   70693 470713 fef856e3 f62023 f8a5cee3 58513 106a023 8067 6886b3 6a783 f62023 106a023 8067 251693
  //   d886b3 f6a023 fe9ff06f 58513 fe1ff06f 1ec5da63 fa010113 4812c23 5612023 3812c23 4112e23 4912a23
  //   5212823 5312623 5412423 5512223 3712e23 3912a23 3a12823 3b12623 58c13 60b13 50413 b0613 c0593 40513
  //   ee9ff0ef a12223 fff50c93 159c5663 c8613 c0593 40513 ecdff0ef a12423 fff50d13 13a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
endmodule

module \控制器  (
  input  [6:0] opcode,
  input  [2:0] funct3,
  input  [6:0] funct7,
  output [2:0] ExtOp,
  output RegWr,
  output [2:0] BandJ,
  output ALUASrc,
  output [1:0] ALUBSrc,
  output [3:0] ALUctr,
  output MemtoReg,
  output [2:0] MemOp,
  output MemWr,
  output Halt
);

  wire and_1_out, and_2_out, and_3_out, and_4_out, and_5_out, and_6_out, and_7_out, and_8_out, and_9_out,
       and_10_out, and_11_out, and_12_out, and_13_out, and_14_out, and_15_out, and_16_out, and_17_out,
       comparator_10_eq, comparator_11_eq, I_Arith, I_jalr, R_Arith, U_auipc, U_lui;

  Comparator #(.width(7), .mode("unsigned")) comparator_1 (.a(opcode), .b(7'b0110111), .eq(U_lui));  // open: gt, lt
  Comparator #(.width(7), .mode("unsigned")) comparator_2 (.a(opcode), .b(7'b1100111), .eq(I_jalr));  // open: gt, lt
  Comparator #(.width(7), .mode("unsigned")) comparator_3 (.a(opcode), .b(7'b0010111), .eq(U_auipc));  // open: gt, lt
  Comparator #(.width(7), .mode("unsigned")) comparator_4 (.a(opcode), .b(7'b1100011), .eq(BandJ[2]));  // open: gt, lt
  Comparator #(.width(7), .mode("unsigned")) comparator_5 (.a(opcode), .b(7'b0010011), .eq(I_Arith));  // open: gt, lt
  Comparator #(.width(7), .mode("unsigned")) comparator_6 (.a(opcode), .b(7'b0000011), .eq(MemtoReg));  // open: gt, lt
  Comparator #(.width(7), .mode("unsigned")) comparator_7 (.a(opcode), .b(7'b0110011), .eq(R_Arith));  // open: gt, lt
  Comparator #(.width(7), .mode("unsigned")) comparator_8 (.a(opcode), .b(7'b0100011), .eq(MemWr));  // open: gt, lt
  or or_1 (RegWr, U_lui, U_auipc, I_Arith, R_Arith, ExtOp[2], I_jalr, MemtoReg);
  or or_2 (ALUASrc, U_auipc, ExtOp[2], I_jalr);
  or or_3 (ALUBSrc[1], U_lui, U_auipc, I_Arith, MemtoReg, MemWr);
  or or_4 (ALUBSrc[0], ExtOp[2], I_jalr);
  or or_5 (ExtOp[0], U_lui, U_auipc, BandJ[2]);
  or or_6 (ExtOp[1], BandJ[2], MemWr);
  and and_1 (and_1_out, I_Arith, funct3[0]);
  or or_7 (ALUctr[0], U_lui, and_1_out, and_2_out, and_3_out);
  and and_2 (and_2_out, R_Arith, funct3[0]);
  and and_3 (and_3_out, BandJ[2], funct3[1], funct3[2]);
  and and_4 (and_4_out, I_Arith, funct3[1]);
  or or_8 (ALUctr[1], U_lui, and_4_out, and_5_out, BandJ[2]);
  and and_5 (and_5_out, R_Arith, funct3[1]);
  or or_9 (ALUctr[2], U_lui, and_6_out, and_7_out);
  and and_6 (and_6_out, I_Arith, funct3[2]);
  and and_7 (and_7_out, R_Arith, funct3[2]);
  or or_10 (ALUctr[3], U_lui, and_8_out, and_9_out);
  and and_8 (and_8_out, funct7[5], I_Arith, funct3[0], ~funct3[1], funct3[2]);  // AND_Gate
  and and_9 (and_9_out, R_Arith, funct7[5]);
  or or_11 (BandJ[0], ExtOp[2], and_10_out);
  and and_10 (and_10_out, BandJ[2], funct3[0]);
  or or_12 (BandJ[1], I_jalr, and_11_out);
  and and_11 (and_11_out, BandJ[2], funct3[2]);
  and and_12 (and_12_out, MemtoReg, ~funct3[0], ~funct3[1]);  // AND_Gate
  or or_13 (MemOp[0], and_12_out, and_13_out);
  and and_13 (and_13_out, MemWr, ~funct3[0], ~funct3[1]);  // AND_Gate
  and and_14 (and_14_out, MemtoReg, funct3[0], ~funct3[1]);  // AND_Gate
  or or_14 (MemOp[1], and_14_out, and_15_out);
  and and_15 (and_15_out, MemWr, funct3[0], ~funct3[1]);  // AND_Gate
  and and_16 (and_16_out, MemtoReg, ~funct3[1], ~funct3[2]);  // AND_Gate
  or or_15 (MemOp[2], and_16_out, and_17_out);
  and and_17 (and_17_out, MemWr, ~funct3[1], ~funct3[2]);  // AND_Gate
  Comparator #(.width(7), .mode("unsigned")) comparator_9 (.a(opcode), .b(7'b1101111), .eq(ExtOp[2]));  // open: gt, lt
  Comparator #(.width(7), .mode("unsigned")) comparator_10 (
    .a(opcode), .b(7'b1110011), .eq(comparator_10_eq));  // open: gt, lt
  Comparator #(.width(7), .mode("unsigned")) comparator_11 (
    .a(opcode), .b(7'b1001100), .eq(comparator_11_eq));  // open: gt, lt
  or or_16 (Halt, comparator_11_eq, comparator_10_eq);

  // Other names for the same wires on the sheet: B_Instr = BandJ[2]; J_jal = ExtOp[2]; I_load = MemtoReg;
  //   S_Instr = MemWr

  // Notes on the sheet:
  //   输入引脚
  //   请勿修改引脚名称、电路名称及电路封装外观
  //   提示：根据指令种类，把7位指令code用一位指令类型标志位来表示，再通过功能码来区分具体指令，生成控制信号。
  //   输出引脚
endmodule

module IDU (
  input  [31:0] IR,
  input  [31:0] BusW,
  input  [31:0] PC,
  input  [2:0] ExtOp,
  input  RegWr,
  input  ALUASrc,
  input  [1:0] ALUBSrc,
  input  CLK,
  output [31:0] DataA,
  output [31:0] DataB,
  output [31:0] BusA,
  output [31:0] BusB,
  output [6:0] OpCode,
  output [31:0] Imm,
  output [2:0] Funct3,
  output [6:0] Funct7
);

  \立即数扩展器  \u_立即数扩展器_1  (.Instr(IR), .Extop(ExtOp), .imm(Imm));
  RegFile regfile_1 (
    .R1_num(IR[19:15]), .R2_num(IR[24:20]), .Write_Reg_num(IR[11:7]), .Write_Enable(RegWr), .Clock(CLK),
    .Din(BusW), .Reg1Out(BusA), .Reg2Out(BusB));
  Multiplexer #(.width(32), .enable("false")) multiplexer_1 (.in0(BusA), .in1(PC), .out(DataA), .sel(ALUASrc));
  Multiplexer #(.select(2), .width(32), .enable("false")) multiplexer_2 (
    .in0(BusB), .in1(32'h4), .in2(Imm), .out(DataB), .sel(ALUBSrc));  // open: in3

  assign Funct3 = IR[14:12];
  assign Funct7 = IR[31:25];
  assign OpCode = IR[6:0];

  // Other names for the same wires on the sheet: op[6:0] = IR[6:0]

  // Notes on the sheet:
  //   PC: pull=down
  //   RegWr: pull=down
  //   ALUBSrc: pull=down
  //   ALUASrc: pull=down
  //   ExtOp: pull=down
  //   BusW: pull=down
  //   输入信号
  //   为了后续实验中的引用，不要修改ALUASrc、ALUBSrc和EXtOP编码定义。
  //   请勿修改引脚名称、电路名称及电路封装外观
  //   输出信号
  //   修改寄存器堆电路设计，0号寄存器始终为0。
endmodule

module RegFile (
  input  [4:0] R1_num,
  input  [4:0] R2_num,
  input  [4:0] Write_Reg_num,
  input  [31:0] Din,
  input  Write_Enable,
  input  Clock,
  output [31:0] Reg1Out,
  output [31:0] Reg2Out
);

  wire and_1_out, and_2_out, and_3_out, and_4_out, and_5_out, and_6_out, and_7_out, and_8_out, and_9_out,
       and_10_out, and_11_out, and_12_out, and_13_out, and_14_out, and_15_out, and_16_out, and_17_out,
       and_18_out, and_19_out, and_20_out, and_21_out, and_22_out, and_23_out, and_24_out, and_25_out,
       and_26_out, and_27_out, and_28_out, and_29_out, and_30_out, and_31_out, and_32_out, decoder_1_out0,
       decoder_1_out1, decoder_1_out2, decoder_1_out3, decoder_1_out4, decoder_1_out5, decoder_1_out6,
       decoder_1_out7, decoder_1_out8, decoder_1_out9, decoder_1_out10, decoder_1_out11, decoder_1_out12,
       decoder_1_out13, decoder_1_out14, decoder_1_out15, decoder_1_out16, decoder_1_out17, decoder_1_out18,
       decoder_1_out19, decoder_1_out20, decoder_1_out21, decoder_1_out22, decoder_1_out23, decoder_1_out24,
       decoder_1_out25, decoder_1_out26, decoder_1_out27, decoder_1_out28, decoder_1_out29, decoder_1_out30,
       decoder_1_out31;
  wire [31:0] _0_q, _1_q, _2_q, _3_q, _4_q, _5_q, _6_q, _7_q, _8_q, _9_q, _10_q, _11_q, _12_q, _13_q, _14_q,
       _15_q, _16_q, _17_q, _18_q, _19_q, _20_q, _21_q, _22_q, _23_q, _24_q, _25_q, _26_q, _27_q, _28_q,
       _29_q, _30_q, _31_q;

  Decoder #(.select(5), .enable("false")) decoder_1 (
    .out0(decoder_1_out0), .out1(decoder_1_out1), .out2(decoder_1_out2), .out3(decoder_1_out3),
    .out4(decoder_1_out4), .out5(decoder_1_out5), .out6(decoder_1_out6), .out7(decoder_1_out7),
    .out8(decoder_1_out8), .out9(decoder_1_out9), .out10(decoder_1_out10), .out11(decoder_1_out11),
    .out12(decoder_1_out12), .out13(decoder_1_out13), .out14(decoder_1_out14), .out15(decoder_1_out15),
    .out16(decoder_1_out16), .out17(decoder_1_out17), .out18(decoder_1_out18), .out19(decoder_1_out19),
    .out20(decoder_1_out20), .out21(decoder_1_out21), .out22(decoder_1_out22), .out23(decoder_1_out23),
    .out24(decoder_1_out24), .out25(decoder_1_out25), .out26(decoder_1_out26), .out27(decoder_1_out27),
    .out28(decoder_1_out28), .out29(decoder_1_out29), .out30(decoder_1_out30), .out31(decoder_1_out31),
    .sel(Write_Reg_num));
  and and_1 (and_1_out, decoder_1_out0, Write_Enable);
  and and_2 (and_2_out, decoder_1_out1, Write_Enable);
  and and_3 (and_3_out, decoder_1_out2, Write_Enable);
  and and_4 (and_4_out, decoder_1_out3, Write_Enable);
  and and_5 (and_5_out, decoder_1_out4, Write_Enable);
  and and_6 (and_6_out, decoder_1_out5, Write_Enable);
  and and_7 (and_7_out, decoder_1_out6, Write_Enable);
  and and_8 (and_8_out, decoder_1_out7, Write_Enable);
  and and_9 (and_9_out, decoder_1_out8, Write_Enable);
  and and_10 (and_10_out, decoder_1_out9, Write_Enable);
  and and_11 (and_11_out, decoder_1_out10, Write_Enable);
  and and_12 (and_12_out, decoder_1_out11, Write_Enable);
  and and_13 (and_13_out, decoder_1_out12, Write_Enable);
  and and_14 (and_14_out, decoder_1_out13, Write_Enable);
  and and_15 (and_15_out, decoder_1_out14, Write_Enable);
  and and_16 (and_16_out, decoder_1_out15, Write_Enable);
  and and_17 (and_17_out, decoder_1_out16, Write_Enable);
  and and_18 (and_18_out, decoder_1_out17, Write_Enable);
  and and_19 (and_19_out, decoder_1_out18, Write_Enable);
  and and_20 (and_20_out, decoder_1_out19, Write_Enable);
  and and_21 (and_21_out, decoder_1_out20, Write_Enable);
  and and_22 (and_22_out, decoder_1_out21, Write_Enable);
  and and_23 (and_23_out, decoder_1_out22, Write_Enable);
  and and_24 (and_24_out, decoder_1_out23, Write_Enable);
  and and_25 (and_25_out, decoder_1_out24, Write_Enable);
  and and_26 (and_26_out, decoder_1_out25, Write_Enable);
  and and_27 (and_27_out, decoder_1_out26, Write_Enable);
  and and_28 (and_28_out, decoder_1_out27, Write_Enable);
  and and_29 (and_29_out, decoder_1_out28, Write_Enable);
  and and_30 (and_30_out, decoder_1_out29, Write_Enable);
  and and_31 (and_31_out, decoder_1_out30, Write_Enable);
  and and_32 (and_32_out, decoder_1_out31, Write_Enable);
  Register #(.width(32), .Select("high")) _0 (.D({32{1'b0}}), .en(and_1_out), .Q(_0_q), .clk(Clock));  // open: clr
  Register #(.width(32), .Select("high")) _1 (.D(Din), .en(and_2_out), .Q(_1_q), .clk(Clock));  // open: clr
  Register #(.width(32), .Select("high")) _2 (.D(Din), .en(and_3_out), .Q(_2_q), .clk(Clock));  // open: clr
  Register #(.width(32), .Select("high")) _3 (.D(Din), .en(and_4_out), .Q(_3_q), .clk(Clock));  // open: clr
  Register #(.width(32), .Select("high")) _4 (.D(Din), .en(and_5_out), .Q(_4_q), .clk(Clock));  // open: clr
  Register #(.width(32), .Select("high")) _5 (.D(Din), .en(and_6_out), .Q(_5_q), .clk(Clock));  // open: clr
  Register #(.width(32), .Select("high")) _6 (.D(Din), .en(and_7_out), .Q(_6_q), .clk(Clock));  // open: clr
  Register #(.width(32), .Select("high")) _7 (.D(Din), .en(and_8_out), .Q(_7_q), .clk(Clock));  // open: clr
  Register #(.width(32), .Select("high")) _8 (.D(Din), .en(and_9_out), .Q(_8_q), .clk(Clock));  // open: clr
  Register #(.width(32), .Select("high")) _9 (.D(Din), .en(and_10_out), .Q(_9_q), .clk(Clock));  // open: clr
  Register #(.width(32), .Select("high")) _10 (.D(Din), .en(and_11_out), .Q(_10_q), .clk(Clock));  // open: clr
  Register #(.width(32), .Select("high")) _11 (.D(Din), .en(and_12_out), .Q(_11_q), .clk(Clock));  // open: clr
  Register #(.width(32), .Select("high")) _12 (.D(Din), .en(and_13_out), .Q(_12_q), .clk(Clock));  // open: clr
  Register #(.width(32), .Select("high")) _13 (.D(Din), .en(and_14_out), .Q(_13_q), .clk(Clock));  // open: clr
  Register #(.width(32), .Select("high")) _14 (.D(Din), .en(and_15_out), .Q(_14_q), .clk(Clock));  // open: clr
  Register #(.width(32), .Select("high")) _15 (.D(Din), .en(and_16_out), .Q(_15_q), .clk(Clock));  // open: clr
  Register #(.width(32), .Select("high")) _16 (.D(Din), .en(and_17_out), .Q(_16_q), .clk(Clock));  // open: clr
  Register #(.width(32), .Select("high")) _17 (.D(Din), .en(and_18_out), .Q(_17_q), .clk(Clock));  // open: clr
  Register #(.width(32), .Select("high")) _18 (.D(Din), .en(and_19_out), .Q(_18_q), .clk(Clock));  // open: clr
  Register #(.width(32), .Select("high")) _19 (.D(Din), .en(and_20_out), .Q(_19_q), .clk(Clock));  // open: clr
  Register #(.width(32), .Select("high")) _20 (.D(Din), .en(and_21_out), .Q(_20_q), .clk(Clock));  // open: clr
  Register #(.width(32), .Select("high")) _21 (.D(Din), .en(and_22_out), .Q(_21_q), .clk(Clock));  // open: clr
  Register #(.width(32), .Select("high")) _22 (.D(Din), .en(and_23_out), .Q(_22_q), .clk(Clock));  // open: clr
  Register #(.width(32), .Select("high")) _23 (.D(Din), .en(and_24_out), .Q(_23_q), .clk(Clock));  // open: clr
  Register #(.width(32), .Select("high")) _24 (.D(Din), .en(and_25_out), .Q(_24_q), .clk(Clock));  // open: clr
  Register #(.width(32), .Select("high")) _25 (.D(Din), .en(and_26_out), .Q(_25_q), .clk(Clock));  // open: clr
  Register #(.width(32), .Select("high")) _26 (.D(Din), .en(and_27_out), .Q(_26_q), .clk(Clock));  // open: clr
  Register #(.width(32), .Select("high")) _27 (.D(Din), .en(and_28_out), .Q(_27_q), .clk(Clock));  // open: clr
  Register #(.width(32), .Select("high")) _28 (.D(Din), .en(and_29_out), .Q(_28_q), .clk(Clock));  // open: clr
  Register #(.width(32), .Select("high")) _29 (.D(Din), .en(and_30_out), .Q(_29_q), .clk(Clock));  // open: clr
  Register #(.width(32), .Select("high")) _30 (.D(Din), .en(and_31_out), .Q(_30_q), .clk(Clock));  // open: clr
  Register #(.width(32), .Select("high")) _31 (.D(Din), .en(and_32_out), .Q(_31_q), .clk(Clock));  // open: clr
  Multiplexer #(.select(5), .width(32), .enable("false")) multiplexer_1 (
    .in0(_0_q), .in1(_1_q), .in2(_2_q), .in3(_3_q), .in4(_4_q), .in5(_5_q), .in6(_6_q), .in7(_7_q),
    .in8(_8_q), .in9(_9_q), .in10(_10_q), .in11(_11_q), .in12(_12_q), .in13(_13_q), .in14(_14_q),
    .in15(_15_q), .in16(_16_q), .in17(_17_q), .in18(_18_q), .in19(_19_q), .in20(_20_q), .in21(_21_q),
    .in22(_22_q), .in23(_23_q), .in24(_24_q), .in25(_25_q), .in26(_26_q), .in27(_27_q), .in28(_28_q),
    .in29(_29_q), .in30(_30_q), .in31(_31_q), .out(Reg1Out), .sel(R1_num));
  Multiplexer #(.select(5), .width(32), .enable("false")) multiplexer_2 (
    .in0(_0_q), .in1(_1_q), .in2(_2_q), .in3(_3_q), .in4(_4_q), .in5(_5_q), .in6(_6_q), .in7(_7_q),
    .in8(_8_q), .in9(_9_q), .in10(_10_q), .in11(_11_q), .in12(_12_q), .in13(_13_q), .in14(_14_q),
    .in15(_15_q), .in16(_16_q), .in17(_17_q), .in18(_18_q), .in19(_19_q), .in20(_20_q), .in21(_21_q),
    .in22(_22_q), .in23(_23_q), .in24(_24_q), .in25(_25_q), .in26(_26_q), .in27(_27_q), .in28(_28_q),
    .in29(_29_q), .in30(_30_q), .in31(_31_q), .out(Reg2Out), .sel(R2_num));

  // Other names for the same wires on the sheet: CLK = Clock; RA[4:0] = R1_num; RB[4:0] = R2_num; RDA[31:0] = Reg1Out;
  //   RDB[31:0] = Reg2Out; RW[4:0] = Write_Reg_num; WE = Write_Enable

  // Notes on the sheet:
  //   输入引脚
  //   请勿修改引脚名称、电路名称及电路封装外观
  //   提示：使用译码器、多路选择器和32位寄存器及逻辑门实现寄存器堆，禁止直接使用存储器组件。
  //   输出引脚
endmodule

module \立即数扩展器  (
  input  [31:0] Instr,
  input  [2:0] Extop,
  output [31:0] imm
);

  wire [11:0] bit_extender_2_out;
  wire [19:0] bit_extender_1_out;
  wire [20:0] bit_extender_4_out;
  wire [31:0] bit_extender_3_out;

  assign bit_extender_1_out = {{19{Instr[31]}}, Instr[31]};  // Bit_Extender bit_extender_1
  assign bit_extender_2_out = {{11{Instr[31]}}, Instr[31]};  // Bit_Extender bit_extender_2
  assign bit_extender_3_out = {{20{Instr[31]}}, Instr[31:20]};  // Bit_Extender bit_extender_3
  assign bit_extender_4_out = {{20{Instr[31]}}, Instr[31]};  // Bit_Extender bit_extender_4
  Multiplexer #(.select(3), .width(32), .enable("false")) multiplexer_1 (
    .in0(bit_extender_3_out), .in1({Instr[31:12], {12{1'b0}}}),
    .in2({bit_extender_4_out, Instr[30:25], Instr[11:7]}),
    .in3({bit_extender_1_out, Instr[7], Instr[30:25], Instr[11:8], 1'b0}),
    .in4({bit_extender_2_out, Instr[19:12], Instr[20], Instr[30:21], 1'b0}), .out(imm), .sel(Extop));  // open: in5, in6, in7

  // Notes on the sheet:
  //   Instr: pull=down
  //   Extop: pull=down
  //   输入引脚
  //   输出引脚
endmodule

module DataRAM (
  input  CLK,
  input  CLR,
  input  WE,
  input  [2:0] MemOp,
  input  [17:0] Addr,
  input  [31:0] Din,
  output AlignErr,
  output [31:0] DataOut
);

  wire and_1_out, and_3_out, and_4_out, and_5_out, or_1_out, or_2_out, or_3_out, or_4_out;
  wire [3:0] SEL;
  wire [7:0] multiplexer_4_out, multiplexer_5_out, multiplexer_6_out;
  wire [31:0] bit_extender_1_out, bit_extender_2_out, bit_extender_3_out, bit_extender_4_out,
       bit_extender_5_out, bit_extender_6_out, Din_Aligened, multiplexer_1_out, multiplexer_2_out, RESULT,
       shifter_1_out, shifter_2_out, shifter_3_out, shifter_4_out;

  assign bit_extender_1_out = {{24{1'b0}}, Din[7:0]};  // Bit_Extender bit_extender_1
  assign bit_extender_2_out = {{16{1'b0}}, Din[15:0]};  // Bit_Extender bit_extender_2
  Shifter #(.width(32)) shifter_1 (.in(bit_extender_1_out), .\dist (5'b01000), .out(shifter_1_out));
  Shifter #(.width(32)) shifter_2 (.in(bit_extender_1_out), .\dist (5'b10000), .out(shifter_2_out));
  Shifter #(.width(32)) shifter_3 (.in(bit_extender_1_out), .\dist (5'b11000), .out(shifter_3_out));
  Shifter #(.width(32)) shifter_4 (.in(bit_extender_2_out), .\dist (5'b10000), .out(shifter_4_out));
  SEL sel_1 (
    .Mem2(MemOp[2]), .Mem1(MemOp[1]), .Mem0(MemOp[0]), .Addr1(Addr[1]), .Addr0(Addr[0]), .Sel3(SEL[3]),
    .Sel2(SEL[2]), .Sel1(SEL[1]), .Sel0(SEL[0]));
  and and_1 (and_1_out, SEL[3], WE);
  Multiplexer #(.select(2), .width(32), .enable("false")) multiplexer_1 (
    .in0(bit_extender_1_out), .in1(shifter_1_out), .in2(shifter_2_out), .in3(shifter_3_out),
    .out(multiplexer_1_out), .sel(Addr[1:0]));
  Multiplexer #(.select(2), .width(32), .enable("false")) multiplexer_2 (
    .in0(bit_extender_2_out), .in2(shifter_4_out), .out(multiplexer_2_out), .sel(Addr[1:0]));  // open: in1, in3
  or or_1 (or_1_out, SEL[3], WE);
  RAM #(.addrWidth(16), .bus("separate"), .Select("high"), .simpleMode("false")) ram_1 (
    .addr(Addr[17:2]), .din(Din_Aligened[31:24]), .data(RESULT[31:24]), .str(and_1_out), .sel(or_1_out),
    .clk(CLK), .clr(CLR));  // open: ld
  and and_2 (AlignErr, ~SEL[3], ~SEL[2], ~SEL[1], ~SEL[0]);  // AND_Gate
  Multiplexer #(.select(3), .width(32), .enable("false")) multiplexer_3 (
    .in0(Din), .in5(multiplexer_1_out), .in6(multiplexer_2_out), .out(Din_Aligened), .sel(MemOp));  // open: in1, in2, in3, in4, in7
  and and_3 (and_3_out, SEL[2], WE);
  RAM #(.addrWidth(16), .bus("separate"), .Select("high"), .simpleMode("false")) ram_2 (
    .addr(Addr[17:2]), .din(Din_Aligened[23:16]), .data(RESULT[23:16]), .str(and_3_out), .sel(or_2_out),
    .clk(CLK), .clr(CLR));  // open: ld
  or or_2 (or_2_out, SEL[2], WE);
  and and_4 (and_4_out, SEL[1], WE);
  RAM #(.addrWidth(16), .bus("separate"), .Select("high"), .simpleMode("false")) ram_3 (
    .addr(Addr[17:2]), .din(Din_Aligened[15:8]), .data(RESULT[15:8]), .str(and_4_out), .sel(or_3_out),
    .clk(CLK), .clr(CLR));  // open: ld
  or or_3 (or_3_out, SEL[1], WE);
  and and_5 (and_5_out, SEL[0], WE);
  RAM #(.addrWidth(16), .bus("separate"), .Select("high"), .simpleMode("false")) ram_4 (
    .addr(Addr[17:2]), .din(Din_Aligened[7:0]), .data(RESULT[7:0]), .str(and_5_out), .sel(or_4_out),
    .clk(CLK), .clr(CLR));  // open: ld
  or or_4 (or_4_out, SEL[0], WE);
  Multiplexer #(.select(4), .width(8), .enable("false")) multiplexer_4 (
    .in1(RESULT[7:0]), .in2(RESULT[15:8]), .in4(RESULT[23:16]), .in8(RESULT[31:24]), .out(multiplexer_4_out),
    .sel(SEL));  // open: in0, in3, in5, in6, in7, in9, in10, in11, in12, in13, in14, in15
  Multiplexer #(.select(4), .width(8), .enable("false")) multiplexer_5 (
    .in3(RESULT[7:0]), .in12(RESULT[23:16]), .out(multiplexer_5_out), .sel(SEL));  // open: in0, in1, in2, in4, in5, in6, in7, in8, in9, in10, in11, in13, in14, in15
  Multiplexer #(.select(4), .width(8), .enable("false")) multiplexer_6 (
    .in3(RESULT[15:8]), .in12(RESULT[31:24]), .out(multiplexer_6_out), .sel(SEL));  // open: in0, in1, in2, in4, in5, in6, in7, in8, in9, in10, in11, in13, in14, in15
  assign bit_extender_3_out = {{24{1'b0}}, multiplexer_4_out};  // Bit_Extender bit_extender_3
  assign bit_extender_4_out = {{24{multiplexer_4_out[7]}}, multiplexer_4_out};  // Bit_Extender bit_extender_4
  assign bit_extender_5_out = {{16{1'b0}}, {multiplexer_6_out, multiplexer_5_out}};  // Bit_Extender bit_extender_5
  assign bit_extender_6_out = {{16{multiplexer_6_out[7]}}, {multiplexer_6_out, multiplexer_5_out}};  // Bit_Extender bit_extender_6
  Multiplexer #(.select(3), .width(32), .enable("false")) multiplexer_7 (
    .in0(RESULT), .in1(bit_extender_3_out), .in2(bit_extender_5_out), .in5(bit_extender_4_out),
    .in6(bit_extender_6_out), .out(DataOut), .sel(MemOp));  // open: in3, in4, in7

  // Other names for the same wires on the sheet: AddrS[1:0] = Addr[1:0]; AddrR[15:0] = Addr[17:2];
  //   Dout[31:0] = DataOut

  // Notes on the sheet:
  //   输入引脚
  //   请勿修改引脚名称、电路名称及电路封装外观
  //   为了后续实验中的引用，不要修改MemOp的编码定义、引脚名称和在布局中的位置。
  //   32位数据存储器，按字节分4片存储，可按照字节、半字和字进行存储；读取字节或半字时，支持0扩展和符号位扩展。
  //   SEL3
  //   输出引脚
  //   SEL2
  //   SEL1
  //   SEL0
endmodule

module SEL (
  input  Mem2,
  input  Mem1,
  input  Mem0,
  input  Addr1,
  input  Addr0,
  output Sel3,
  output Sel2,
  output Sel1,
  output Sel0
);

  wire and_1_out, and_2_out, and_3_out, and_4_out, and_5_out, and_6_out, and_7_out, and_8_out, and_9_out,
       and_10_out, and_11_out, and_12_out, not_1_out, not_2_out, not_3_out, not_4_out, not_5_out, not_6_out,
       not_7_out, not_8_out, not_9_out, not_10_out, not_11_out, not_12_out, not_13_out, not_14_out,
       not_15_out, not_16_out, not_17_out, not_18_out, not_19_out, not_20_out, not_21_out, not_22_out,
       not_23_out, not_24_out, not_25_out, not_26_out, not_27_out, not_28_out, not_29_out, not_30_out,
       not_31_out, not_32_out, not_33_out, not_34_out, not_35_out, not_36_out;

  not not_1 (not_1_out, Mem2);
  not not_2 (not_2_out, Mem1);
  not not_3 (not_3_out, Mem0);
  not not_4 (not_4_out, Addr1);
  not not_5 (not_5_out, Addr0);
  not not_6 (not_6_out, Mem1);
  not not_7 (not_7_out, Mem0);
  not not_8 (not_8_out, Addr0);
  not not_9 (not_9_out, Mem2);
  not not_10 (not_10_out, Mem1);
  not not_11 (not_11_out, Mem0);
  not not_12 (not_12_out, Addr1);
  not not_13 (not_13_out, Addr0);
  not not_14 (not_14_out, Mem1);
  not not_15 (not_15_out, Addr0);
  not not_16 (not_16_out, Mem0);
  not not_17 (not_17_out, Addr0);
  not not_18 (not_18_out, Mem2);
  not not_19 (not_19_out, Mem0);
  not not_20 (not_20_out, Addr1);
  not not_21 (not_21_out, Addr0);
  not not_22 (not_22_out, Mem1);
  not not_23 (not_23_out, Addr1);
  not not_24 (not_24_out, Mem0);
  not not_25 (not_25_out, Addr1);
  not not_26 (not_26_out, Addr0);
  not not_27 (not_27_out, Mem2);
  not not_28 (not_28_out, Mem1);
  not not_29 (not_29_out, Addr1);
  not not_30 (not_30_out, Addr0);
  not not_31 (not_31_out, Mem1);
  not not_32 (not_32_out, Addr1);
  not not_33 (not_33_out, Addr0);
  not not_34 (not_34_out, Mem0);
  not not_35 (not_35_out, Addr1);
  not not_36 (not_36_out, Addr0);
  and and_1 (and_1_out, not_1_out, not_2_out, not_3_out, not_4_out, not_5_out);
  and and_2 (and_2_out, not_6_out, Mem0, Addr1, Addr0);
  and and_3 (and_3_out, Mem1, not_7_out, Addr1, not_8_out);
  and and_4 (and_4_out, not_9_out, not_10_out, not_11_out, not_12_out, not_13_out);
  and and_5 (and_5_out, not_14_out, Mem0, Addr1, not_15_out);
  and and_6 (and_6_out, Mem1, not_16_out, Addr1, not_17_out);
  and and_7 (and_7_out, not_18_out, not_19_out, not_20_out, not_21_out);
  and and_8 (and_8_out, not_22_out, Mem0, not_23_out, Addr0);
  and and_9 (and_9_out, Mem1, not_24_out, not_25_out, not_26_out);
  and and_10 (and_10_out, not_27_out, not_28_out, not_29_out, not_30_out);
  and and_11 (and_11_out, not_31_out, Mem0, not_32_out, not_33_out);
  and and_12 (and_12_out, Mem1, not_34_out, not_35_out, not_36_out);
  or or_1 (Sel3, and_1_out, and_2_out, and_3_out);
  or or_2 (Sel2, and_4_out, and_5_out, and_6_out);
  or or_3 (Sel1, and_7_out, and_8_out, and_9_out);
  or or_4 (Sel0, and_10_out, and_11_out, and_12_out);
endmodule

module ALU (
  input  [3:0] ALUctr,
  input  [31:0] A,
  input  [31:0] B,
  output Zero,
  output [31:0] S
);

  wire adder32_1_cout, adder32_1_of, adder32_1_sf, aluctrl_1_alctr, aluctrl_1_sftctr, aluctrl_1_sigctr,
       aluctrl_1_subctr, multiplexer_1_out, xor_3_out, xor_4_out;
  wire [2:0] aluctrl_1_opctr;
  wire [31:0] adder32_1_s, and_1_out, bit_extender_1_out, bit_extender_2_out, or_1_out, shifter32_1_dataout,
       xor_1_out, xor_2_out;

  assign bit_extender_1_out = {{31{aluctrl_1_subctr}}, aluctrl_1_subctr};  // Bit_Extender bit_extender_1
  assign and_1_out = A & B;  // AND_Gate and_1, 32 bits wide
  assign or_1_out = A | B;  // OR_Gate or_1, 32 bits wide
  assign xor_1_out = A ^ B;  // XOR_Gate xor_1, 32 bits wide
  Shifter32 shifter32_1 (
    .DataIn(A), .shamt(B[4:0]), .L_R(aluctrl_1_sftctr), .A_L(aluctrl_1_alctr), .DataOut(shifter32_1_dataout));
  Adder32 adder32_1 (
    .OF(adder32_1_of), .SF(adder32_1_sf), .ZF(Zero), .X(A), .Y(xor_2_out), .Cin(aluctrl_1_subctr),
    .S(adder32_1_s), .Cout(adder32_1_cout));  // open: CF
  assign xor_2_out = B ^ bit_extender_1_out;  // XOR_Gate xor_2, 32 bits wide
  xor xor_3 (xor_3_out, aluctrl_1_subctr, adder32_1_cout);
  xor xor_4 (xor_4_out, adder32_1_of, adder32_1_sf);
  // Probe on A
  // Probe on B
  // Probe on S
  Multiplexer #(.enable("false")) multiplexer_1 (
    .in0(xor_3_out), .in1(xor_4_out), .out(multiplexer_1_out), .sel(aluctrl_1_sigctr));
  Multiplexer #(.select(3), .width(32), .enable("false")) multiplexer_2 (
    .in0(adder32_1_s), .in1(and_1_out), .in2(or_1_out), .in3(xor_1_out), .in4(shifter32_1_dataout), .in5(B),
    .in6(bit_extender_2_out), .out(S), .sel(aluctrl_1_opctr));  // open: in7
  ALUctrl aluctrl_1 (
    .SUBctr(aluctrl_1_subctr), .SFTctr(aluctrl_1_sftctr), .SIGctr(aluctrl_1_sigctr), .ALctr(aluctrl_1_alctr),
    .OPctr(aluctrl_1_opctr), .ALUctr(ALUctr));
  assign bit_extender_2_out = {{31{1'b0}}, multiplexer_1_out};  // Bit_Extender bit_extender_2

  // Other names for the same wires on the sheet: Result[31:0] = S

  // Notes on the sheet:
  //   ALUctr: pull=down
  //   B: pull=down
  //   A: pull=down
  //   输入引脚
  //   请勿修改引脚名称、电路名称及电路封装外观
  //   提示：使用32位并行加法器子电路、桶形移位器、ALU控制子电路实现32位ALU
  //   功能说明:32位ALU，输入32位操作数A、B，4位控制信号ALUctr，输出32位结果Reseult和1位Zero标志位
  //   输出引脚
  //   操作数和结果
endmodule

module ALUctrl (
  input  [3:0] ALUctr,
  output SUBctr,
  output SFTctr,
  output SIGctr,
  output ALctr,
  output [2:0] OPctr
);

  wire and_2_out, and_3_out;

  Multiplexer #(.select(4), .width(3), .enable("false")) multiplexer_1 (
    .in0(3'b000), .in1(3'b100), .in2(3'b110), .in3(3'b110), .in4(3'b011), .in5(3'b100), .in6(3'b010),
    .in7(3'b001), .in8(3'b000), .in13(3'b100), .in15(3'b101), .out(OPctr), .sel(ALUctr));  // open: in9, in10, in11, in12, in14
  and and_1 (SIGctr, ~ALUctr[3], ~ALUctr[2], ALUctr[1], ~ALUctr[0]);  // AND_Gate
  and and_2 (and_2_out, ~ALUctr[3], ~ALUctr[2], ALUctr[1], ALUctr[0]);  // AND_Gate
  and and_3 (and_3_out, ALUctr[3], ~ALUctr[2], ~ALUctr[1], ~ALUctr[0]);  // AND_Gate
  and and_4 (SFTctr, ~ALUctr[3], ~ALUctr[2], ~ALUctr[1], ALUctr[0]);  // AND_Gate
  and and_5 (ALctr, ALUctr[3], ALUctr[2], ~ALUctr[1], ALUctr[0]);  // AND_Gate
  or or_1 (SUBctr, SIGctr, and_2_out, and_3_out);

  // Other names for the same wires on the sheet: LRctr = SFTctr

  // Notes on the sheet:
  //   输入引脚
  //   ALU操作控制信号生成部件
  //   输出引脚
endmodule

module Adder32 (
  input  Cin,
  input  [31:0] X,
  input  [31:0] Y,
  output CF,
  output Cout,
  output OF,
  output SF,
  output [31:0] S,
  output ZF
);

  wire adder16_2_gg, adder16_2_pg, and_1_out, and_2_out, and_3_out, or_1_out;

  Adder16 adder16_1 (.X(X[31:16]), .Y(Y[31:16]), .C0(or_1_out), .S(S[31:16]), .C16(Cout));  // open: Pg, Gg
  and and_1 (and_1_out, ~Y[31], ~X[31], S[31]);  // AND_Gate
  and and_2 (and_2_out, Y[31], X[31], ~S[31]);  // AND_Gate
  and and_3 (and_3_out, Cin, adder16_2_pg);
  or or_1 (or_1_out, and_3_out, adder16_2_gg);
  or or_2 (OF, and_1_out, and_2_out);
  Adder16 adder16_2 (
    .X(X[15:0]), .Y(Y[15:0]), .C0(Cin), .S(S[15:0]), .Pg(adder16_2_pg), .Gg(adder16_2_gg));  // open: C16
  xor xor_1 (CF, Cout, Cin);
  // Probe on X
  // Probe on Y
  // Probe on S
  Comparator #(.width(32)) comparator_1 (.a({32{1'b0}}), .b(S), .eq(ZF));  // open: gt, lt

  assign SF = S[31];

  // Notes on the sheet:
  //   Y: pull=down
  //   X: pull=down
  //   Cin: pull=down
  //   输入引脚区
  //   输出引脚区
  //   请勿修改引脚名称、电路名称及电路封装外观
  //   提示：使用16位并行加法器子电路实现32位快速加法器
  //   功能说明:32位Adder  S=X+Y，Cout为最高位进位位，Cin为进位输入， S为和，溢出OF、进位CF、零ZF、符号SF。
  //   +
  //   =
  //   无符号加法
endmodule

// 移位器
module Shifter32 (
  input  [4:0] shamt,
  input  L_R,
  input  A_L,
  input  [31:0] DataIn,
  output [31:0] DataOut
);

  wire [0:0] multiplexer_2_out;
  wire [1:0] bit_extender_1_out, bit_extender_2_out, multiplexer_4_out;
  wire [3:0] bit_extender_3_out, bit_extender_4_out, multiplexer_6_out;
  wire [7:0] bit_extender_5_out, bit_extender_6_out, multiplexer_8_out;
  wire [15:0] bit_extender_8_out, multiplexer_10_out;
  wire [31:0] multiplexer_3_out, multiplexer_5_out, multiplexer_7_out, multiplexer_9_out;
  wire [31:16] multiplexer_9_out_2;
  wire [31:31] multiplexer_1_out;

  Multiplexer #(.enable("false")) multiplexer_1 (.in0(1'b0), .in1(DataIn[31]), .out(multiplexer_1_out[31]), .sel(A_L));
  Multiplexer #(.enable("false")) multiplexer_2 (.in0(1'b0), .in1(DataIn[31]), .out(multiplexer_2_out[0]), .sel(A_L));
  Multiplexer #(.select(2), .width(32), .enable("false")) multiplexer_3 (
    .in0(DataIn), .in1({multiplexer_1_out[31], DataIn[31:1]}), .in2(DataIn),
    .in3({DataIn[30:0], multiplexer_2_out[0]}), .out(multiplexer_3_out), .sel({L_R, shamt[0]}));
  assign bit_extender_1_out = {{1{multiplexer_1_out[31]}}, multiplexer_1_out[31]};  // Bit_Extender bit_extender_1
  assign bit_extender_2_out = {{1{1'b0}}, 1'b0};  // Bit_Extender bit_extender_2
  Multiplexer #(.width(2), .enable("false")) multiplexer_4 (
    .in0(bit_extender_2_out), .in1(multiplexer_3_out[31:30]), .out(multiplexer_4_out), .sel(A_L));
  assign bit_extender_3_out = {{2{bit_extender_1_out[1]}}, bit_extender_1_out};  // Bit_Extender bit_extender_3
  Multiplexer #(.select(2), .width(32), .enable("false")) multiplexer_5 (
    .in0(multiplexer_3_out), .in1({bit_extender_1_out, multiplexer_3_out[31:2]}), .in2(multiplexer_3_out),
    .in3({multiplexer_3_out[29:0], multiplexer_4_out}), .out(multiplexer_5_out), .sel({L_R, shamt[1]}));
  assign bit_extender_4_out = {{2{bit_extender_2_out[1]}}, bit_extender_2_out};  // Bit_Extender bit_extender_4
  Multiplexer #(.width(4), .enable("false")) multiplexer_6 (
    .in0(bit_extender_4_out), .in1(multiplexer_5_out[31:28]), .out(multiplexer_6_out), .sel(A_L));
  assign bit_extender_5_out = {{4{bit_extender_3_out[3]}}, bit_extender_3_out};  // Bit_Extender bit_extender_5
  Multiplexer #(.select(2), .width(32), .enable("false")) multiplexer_7 (
    .in0(multiplexer_5_out), .in1({bit_extender_3_out, multiplexer_5_out[31:4]}), .in2(multiplexer_5_out),
    .in3({multiplexer_5_out[27:0], multiplexer_6_out}), .out(multiplexer_7_out), .sel({L_R, shamt[2]}));
  assign bit_extender_6_out = {{4{bit_extender_4_out[3]}}, bit_extender_4_out};  // Bit_Extender bit_extender_6
  Multiplexer #(.width(8), .enable("false")) multiplexer_8 (
    .in0(bit_extender_6_out), .in1(multiplexer_7_out[31:24]), .out(multiplexer_8_out), .sel(A_L));
  Multiplexer #(.select(2), .width(32), .enable("false")) multiplexer_9 (
    .in0(multiplexer_7_out), .in1({bit_extender_5_out, multiplexer_7_out[31:8]}), .in2(multiplexer_7_out),
    .in3({multiplexer_7_out[23:0], multiplexer_8_out}), .out({multiplexer_9_out[15:0], multiplexer_9_out_2}),
    .sel({L_R, shamt[3]}));
  assign multiplexer_9_out[31:16] = {{8{bit_extender_5_out[7]}}, bit_extender_5_out};  // Bit_Extender bit_extender_7
  assign bit_extender_8_out = {{8{bit_extender_6_out[7]}}, bit_extender_6_out};  // Bit_Extender bit_extender_8
  Multiplexer #(.width(16), .enable("false")) multiplexer_10 (
    .in0(bit_extender_8_out), .in1(multiplexer_9_out[15:0]), .out(multiplexer_10_out), .sel(A_L));
  Multiplexer #(.select(2), .width(32), .enable("false")) multiplexer_11 (
    .in0({multiplexer_9_out[15:0], multiplexer_9_out_2}), .in1(multiplexer_9_out),
    .in2({multiplexer_9_out[15:0], multiplexer_9_out_2}), .in3({multiplexer_9_out_2, multiplexer_10_out}),
    .out(DataOut), .sel({L_R, shamt[4]}));

  // Other names for the same wires on the sheet: Din[31:0] = DataIn; Left_Right = L_R; Arth_Logic = A_L;
  //   Dout[31:0] = DataOut

  // Notes on the sheet:
  //   L/R,A/L: 00逻辑右移，01算术右移，10逻辑左移，11：循环左移
  //   输入引脚
  //   请勿修改引脚名称、电路名称及电路封装外观
  //   提示：使用多路选择器、逻辑门实现32位桶形移位器，禁止直接使用移位器组件。
  //   输出引脚
endmodule

module Adder16 (
  input  C0,
  input  [15:0] X,
  input  [15:0] Y,
  output C16,
  output Pg,
  output Gg,
  output [15:0] S
);

  wire cla4_1_gg, cla4_1_pg, cla4_2_gg, cla4_2_pg, cla4_3_gg, cla4_3_pg, cla4_4_gg, cla4_4_pg, clu4_1_c1,
       clu4_1_c2, clu4_1_c3;

  CLA4 cla4_1 (
    .X(X[15:12]), .F(S[15:12]), .Y(Y[15:12]), .Pg(cla4_1_pg), .Cin(clu4_1_c3), .Gg(cla4_1_gg));  // open: Cout
  CLA4 cla4_2 (.X(X[11:8]), .F(S[11:8]), .Y(Y[11:8]), .Pg(cla4_2_pg), .Cin(clu4_1_c2), .Gg(cla4_2_gg));  // open: Cout
  CLU4 clu4_1 (
    .P0(cla4_4_pg), .P1(cla4_3_pg), .P2(cla4_2_pg), .P3(cla4_1_pg), .C1(clu4_1_c1), .C3(clu4_1_c3),
    .G0(cla4_4_gg), .G1(cla4_3_gg), .G2(cla4_2_gg), .G3(cla4_1_gg), .C2(clu4_1_c2), .C4(C16), .C0(C0),
    .Pg(Pg), .Gg(Gg));
  CLA4 cla4_3 (.X(X[7:4]), .F(S[7:4]), .Y(Y[7:4]), .Pg(cla4_3_pg), .Cin(clu4_1_c1), .Gg(cla4_3_gg));  // open: Cout
  CLA4 cla4_4 (.X(X[3:0]), .F(S[3:0]), .Y(Y[3:0]), .Pg(cla4_4_pg), .Cin(C0), .Gg(cla4_4_gg));  // open: Cout
  // Probe on X
  // Probe on Y
  // Probe on S

  // Notes on the sheet:
  //   Y: pull=down
  //   X: pull=down
  //   C0: pull=down
  //   输入引脚区
  //   请勿修改引脚名称、电路名称及电路封装外观
  //   提示：使用4位先行进位加法器和CLU子电路实现16位并行加法器
  //   功能说明:16位Adder  S=X+Y，C16为最高位进位位，C0为进位输入， Pg、Gg为成组进位生成传递函数
  //   输出引脚区
  //   +
  //   =
  //   无符号加法
endmodule

module CLA4 (
  input  [3:0] X,
  input  [3:0] Y,
  input  Cin,
  output [3:0] F,
  output Cout,
  output Pg,
  output Gg
);

  wire clu4_1_c1, clu4_1_c2, clu4_1_c3, fa_1_g, fa_1_p, fa_2_g, fa_2_p, fa_3_g, fa_3_p, fa_4_g, fa_4_p;

  FA fa_1 (.A(X[3]), .F(F[3]), .B(Y[3]), .P(fa_1_p), .Cin(clu4_1_c3), .G(fa_1_g));
  Hex_Digit_Display hex_digit_display_1 (.value(X));  // open: dp
  FA fa_2 (.A(X[2]), .F(F[2]), .B(Y[2]), .P(fa_2_p), .Cin(clu4_1_c2), .G(fa_2_g));
  Hex_Digit_Display hex_digit_display_2 (.value(Y));  // open: dp
  CLU4 clu4_1 (
    .P0(fa_4_p), .P1(fa_3_p), .P2(fa_2_p), .P3(fa_1_p), .C1(clu4_1_c1), .C3(clu4_1_c3), .G0(fa_4_g),
    .G1(fa_3_g), .G2(fa_2_g), .G3(fa_1_g), .C2(clu4_1_c2), .C4(Cout), .C0(Cin), .Pg(Pg), .Gg(Gg));
  FA fa_3 (.A(X[1]), .F(F[1]), .B(Y[1]), .P(fa_3_p), .Cin(clu4_1_c1), .G(fa_3_g));
  Hex_Digit_Display hex_digit_display_3 (.value(F));  // open: dp
  FA fa_4 (.A(X[0]), .F(F[0]), .B(Y[0]), .P(fa_4_p), .Cin(Cin), .G(fa_4_g));

  // Other names for the same wires on the sheet: Z[3:0] = F

  // Notes on the sheet:
  //   +
  //   =
  //   输出
  //   输入
  //   请勿修改引脚名称、电路名称及电路封装外观
  //   提示：使用全加器和CLU子电路实现四位先行进位加法器CLA4
endmodule

module CLU4 (
  input  P0,
  input  P1,
  input  P2,
  input  P3,
  input  G0,
  input  G1,
  input  G2,
  input  G3,
  input  C0,
  output C1,
  output C3,
  output C2,
  output C4,
  output Pg,
  output Gg
);

  wire and_2_out, and_3_out, and_4_out, and_5_out, and_6_out, and_7_out, and_8_out, and_9_out, and_10_out,
       and_11_out;

  and and_1 (Pg, P3, P2, P1, P0);
  and and_2 (and_2_out, P3, G2);
  or or_1 (Gg, G3, and_2_out, and_3_out, and_5_out);
  and and_3 (and_3_out, P3, P2, G1);
  or or_2 (C4, Gg, and_4_out);
  and and_4 (and_4_out, P3, P2, P1, P0, C0);
  and and_5 (and_5_out, P3, P2, P1, G0);
  or or_3 (C3, G2, and_6_out, and_8_out, and_7_out);
  and and_6 (and_6_out, P2, G1);
  and and_7 (and_7_out, P2, P1, P0, C0);
  and and_8 (and_8_out, P2, P1, G0);
  or or_4 (C2, G1, and_9_out, and_10_out);
  and and_9 (and_9_out, P1, G0);
  and and_10 (and_10_out, P1, P0, C0);
  or or_5 (C1, G0, and_11_out);
  and and_11 (and_11_out, P0, C0);

  // Notes on the sheet:
  //   输入引脚
  //   请勿修改引脚名称、电路名称及电路封装外观
  //   提示：使用逻辑门电路实现4位四位先行进位部件CLU，Pg、Gg为成组进位生成传递函数
  //   输出引脚
endmodule

module FA (
  input  A,
  input  B,
  input  Cin,
  output F,
  output P,
  output G
);

  wire xor_1_out;

  xor xor_1 (xor_1_out, Cin, B);
  xor xor_2 (F, xor_1_out, A);
  or or_1 (P, A, B);
  and and_1 (G, A, B);

  // Notes on the sheet:
  //   输入引脚
  //   请勿修改引脚名称、电路名称及电路封装外观
  //   输出引脚
endmodule
