// Logisim project lab8.3.circ as structural Verilog: 22 circuits, main circuit main
module main (
  input  [31:0] Init_Addr,
  input  ReSet,
  input  [31:0] BP_PC,
  input  BPEn,
  input  clk,
  output [31:0] WB_PC,
  output [31:0] WB_BusW,
  output [15:0] Cycles,
  output halt
);

  wire clk_out, clk_t, comparator_1_eq, comparator_2_eq, comparator_3_eq, comparator_4_eq, comparator_5_eq,
       comparator_6_eq, comparator_7_eq, comparator_8_eq, eu_1_zero, nor_1_out, not_2_out, not_3_out,
       not_4_out, not_5_out, or_1_out, or_2_out, or_3_out, or_4_out, or_5_out, PCsrc, Stall, Stop,
       \控制器_1_aluasrc , \控制器_1_halt , \控制器_1_memtoreg , \控制器_1_memwr , \控制器_1_regwr , \流水段寄存器_2_aluasrco ,
       \流水段寄存器_2_halto , \流水段寄存器_2_memtorego , \流水段寄存器_2_memwro , \流水段寄存器_2_regwro , \流水段寄存器_3_halto ,
       \流水段寄存器_3_memtorego , \流水段寄存器_3_memwro , \流水段寄存器_3_regwro , \流水段寄存器_4_memtorego , \流水段寄存器_4_regwro ;
  wire [1:0] BusAFW, BusBFW, \控制器_1_alubsrc , \流水段寄存器_2_alubsrco ;
  wire [2:0] EX_BandJ, idu_1_funct3, \控制器_1_bandj , \控制器_1_extop , \控制器_1_memop , \流水段寄存器_2_memopo ,
       \流水段寄存器_3_memopo ;
  wire [3:0] \控制器_1_aluctr , \流水段寄存器_2_aluctro ;
  wire [4:0] idu_1_rd, idu_1_rs1, idu_1_rs2, \流水段寄存器_2_rdo , \流水段寄存器_2_rs1o , \流水段寄存器_2_rs2o ,
       \流水段寄存器_3_rdo , \流水段寄存器_4_rdo ;
  wire [6:0] idu_1_funct7, idu_1_opcode;
  wire [15:0] \RS1转发次数 , \RS2转发次数 , \冲刷次数 , \分支指令数 , \跳转指令数 , \阻塞次数 ;
  wire [31:0] dataram_1_dataout, eu_1_pctarget, eu_1_result, EX_PC, ID_PC, idu_1_busa, idu_1_busb, idu_1_imm,
       IF_PC, M_PC, multiplexer_1_out, multiplexer_2_out, rom_1_data, WB_IR, \流水段寄存器_1_iro ,
       \流水段寄存器_2_busao , \流水段寄存器_2_busbo , \流水段寄存器_2_immo , \流水段寄存器_2_iro , \流水段寄存器_3_busbo , \流水段寄存器_3_iro ,
       \流水段寄存器_3_resulto , \流水段寄存器_4_douto , \流水段寄存器_4_resulto ;

  Clock u_clk (.out(clk_out));
  not not_1 (clk_t, clk_out);
  or or_1 (or_1_out, Stop, halt);
  IFU ifu_1 (
    .CLK(clk_t), .Reset(ReSet), .PCSrc(or_3_out), .Initial_Address(Init_Addr), .PCTarget(eu_1_pctarget),
    .PC(IF_PC), .halt(or_1_out), .BPEn(BPEn), .BP_PC(BP_PC), .Stall(Stall));
  ROM #(.addrWidth(16), .dataWidth(32), .Select("low")) rom_1 (.addr(IF_PC[17:2]), .data(rom_1_data));
  \流水段寄存器  \u_流水段寄存器_1  (
    .CLR(or_3_out), .CLK(clk_t), .WE(or_2_out), .PC(IF_PC), .PCo(ID_PC), .IR(rom_1_data), .IRo(\流水段寄存器_1_iro ));  // open: ALUctr, ALUctro, ALUASrc, ALUASrco, ALUBSrc, ALUBSrco, Halt, Halto, BandJ, BandJo, MemOp, MemOpo, MemWr, MemWro, RegWr, RegWro, MemtoReg, MemtoRego, RD, RDo, BusA, BusAo, RS1, RS1o, RS2, RS2o, Zero, Zeroo, BusB, BusBo, Imm, Result, PCTarget, Dout, Immo, Resulto, PCTargeto, Douto
  or or_2 (or_2_out, or_3_out, nor_1_out);
  nor nor_1 (nor_1_out, Stall, \控制器_1_halt );
  \控制器  \u_控制器_1  (
    .opcode(idu_1_opcode), .ExtOp(\控制器_1_extop ), .RegWr(\控制器_1_regwr ), .BandJ(\控制器_1_bandj ),
    .funct3(idu_1_funct3), .ALUASrc(\控制器_1_aluasrc ), .ALUBSrc(\控制器_1_alubsrc ), .ALUctr(\控制器_1_aluctr ),
    .funct7(idu_1_funct7), .MemtoReg(\控制器_1_memtoreg ), .MemOp(\控制器_1_memop ), .MemWr(\控制器_1_memwr ),
    .Halt(\控制器_1_halt ), .Stall(Stall));
  IDU idu_1 (
    .OpCode(idu_1_opcode), .RegWr(\流水段寄存器_4_regwro ), .Imm(idu_1_imm), .Funct3(idu_1_funct3),
    .Funct7(idu_1_funct7), .CLK(clk_t), .IR(\流水段寄存器_1_iro ), .BusW(WB_BusW), .BusA(idu_1_busa),
    .BusB(idu_1_busb), .ExtOp(\控制器_1_extop ), .Rd(idu_1_rd), .Rs1(idu_1_rs1), .Rs2(idu_1_rs2),
    .WB_Rd(\流水段寄存器_4_rdo ));
  // Probe on IF_PC
  // Probe on ID_PC
  // Probe on EX_PC
  // Probe on M_PC
  // Probe on WB_PC
  \阻塞检测  \u_阻塞检测_1  (
    .EX_MemtoReg(\流水段寄存器_2_memtorego ), .EX_rd(\流水段寄存器_2_rdo ), .Stall(Stall), .IF_opcode(idu_1_opcode),
    .IF_rs1(idu_1_rs1), .IF_rs2(idu_1_rs2));
  // Probe on Cycles
  // Probe on \阻塞次数 
  // Probe on \冲刷次数 
  // Probe on \跳转指令数 
  // Probe on \分支指令数 
  // Probe on \RS1转发次数 
  // Probe on \RS2转发次数 
  or or_3 (or_3_out, PCsrc, ReSet);
  \流水段寄存器  \u_流水段寄存器_2  (
    .ALUctr(\控制器_1_aluctr ), .ALUctro(\流水段寄存器_2_aluctro ), .CLR(or_3_out), .ALUASrc(\控制器_1_aluasrc ),
    .ALUASrco(\流水段寄存器_2_aluasrco ), .CLK(clk_t), .ALUBSrc(\控制器_1_alubsrc ), .ALUBSrco(\流水段寄存器_2_alubsrco ),
    .WE(1'b1), .Halt(\控制器_1_halt ), .Halto(\流水段寄存器_2_halto ), .BandJ(\控制器_1_bandj ), .BandJo(EX_BandJ),
    .PC(ID_PC), .MemOp(\控制器_1_memop ), .PCo(EX_PC), .MemOpo(\流水段寄存器_2_memopo ), .MemWr(\控制器_1_memwr ),
    .MemWro(\流水段寄存器_2_memwro ), .RegWr(\控制器_1_regwr ), .RegWro(\流水段寄存器_2_regwro ), .IR(\流水段寄存器_1_iro ),
    .MemtoReg(\控制器_1_memtoreg ), .IRo(\流水段寄存器_2_iro ), .MemtoRego(\流水段寄存器_2_memtorego ), .RD(idu_1_rd),
    .RDo(\流水段寄存器_2_rdo ), .BusA(idu_1_busa), .BusAo(\流水段寄存器_2_busao ), .RS1(idu_1_rs1),
    .RS1o(\流水段寄存器_2_rs1o ), .RS2(idu_1_rs2), .RS2o(\流水段寄存器_2_rs2o ), .BusB(idu_1_busb),
    .BusBo(\流水段寄存器_2_busbo ), .Imm(idu_1_imm), .Immo(\流水段寄存器_2_immo ));  // open: Zero, Zeroo, Result, PCTarget, Dout, Resulto, PCTargeto, Douto
  Register #(.width(1), .trigger("falling"), .Select("low")) register_1 (
    .D(halt), .en(not_2_out), .Q(Stop), .clk(clk_t), .clr(ReSet));
  not not_2 (not_2_out, Stop);
  Multiplexer #(.select(2), .width(32), .enable("false")) multiplexer_1 (
    .in0(\流水段寄存器_2_busbo ), .in1(\流水段寄存器_3_resulto ), .in2(WB_BusW), .out(multiplexer_1_out), .sel(BusBFW));  // open: in3
  Multiplexer #(.select(2), .width(32), .enable("false")) multiplexer_2 (
    .in0(\流水段寄存器_2_busao ), .in1(\流水段寄存器_3_resulto ), .in2(WB_BusW), .out(multiplexer_2_out), .sel(BusAFW));  // open: in3
  \转发检测  \u_转发检测_1  (
    .EX_rs1(\流水段寄存器_2_rs1o ), .M_RegWr(\流水段寄存器_3_regwro ), .EX_rs2(\流水段寄存器_2_rs2o ), .M_rd(\流水段寄存器_3_rdo ),
    .WB_RegWr(\流水段寄存器_4_regwro ), .WB_rd(\流水段寄存器_4_rdo ), .BusAFW(BusAFW), .BusBFW(BusBFW));
  Hex_Digit_Display hex_digit_display_1 (.value(WB_IR[27:24]));  // open: dp
  Hex_Digit_Display hex_digit_display_2 (.value(WB_IR[31:28]));  // open: dp
  \跳转检测  \u_跳转检测_1  (.M_BandJ(EX_BandJ), .PCsrc(PCsrc), .M_Zero(eu_1_zero), .M_Result0(eu_1_result[0]));
  EU eu_1 (
    .ALUctr(\流水段寄存器_2_aluctro ), .ALUASrc(\流水段寄存器_2_aluasrco ), .ALUBSrc(\流水段寄存器_2_alubsrco ),
    .BandJ(EX_BandJ), .PC(EX_PC), .BusA(multiplexer_2_out), .BusB(multiplexer_1_out), .Imm(\流水段寄存器_2_immo ),
    .PCTarget(eu_1_pctarget), .Result(eu_1_result), .Zero(eu_1_zero));
  Hex_Digit_Display hex_digit_display_3 (.value(WB_IR[19:16]));  // open: dp
  Hex_Digit_Display hex_digit_display_4 (.value(WB_IR[23:20]));  // open: dp
  Hex_Digit_Display hex_digit_display_5 (.value(WB_IR[11:8]));  // open: dp
  Hex_Digit_Display hex_digit_display_6 (.value(WB_IR[15:12]));  // open: dp
  \流水段寄存器  \u_流水段寄存器_3  (
    .CLR(ReSet), .CLK(clk_t), .WE(1'b1), .Halt(\流水段寄存器_2_halto ), .Halto(\流水段寄存器_3_halto ), .PC(EX_PC),
    .MemOp(\流水段寄存器_2_memopo ), .PCo(M_PC), .MemOpo(\流水段寄存器_3_memopo ), .MemWr(\流水段寄存器_2_memwro ),
    .MemWro(\流水段寄存器_3_memwro ), .RegWr(\流水段寄存器_2_regwro ), .RegWro(\流水段寄存器_3_regwro ), .IR(\流水段寄存器_2_iro ),
    .MemtoReg(\流水段寄存器_2_memtorego ), .IRo(\流水段寄存器_3_iro ), .MemtoRego(\流水段寄存器_3_memtorego ),
    .RD(\流水段寄存器_2_rdo ), .RDo(\流水段寄存器_3_rdo ), .BusB(multiplexer_1_out), .BusBo(\流水段寄存器_3_busbo ),
    .Result(eu_1_result), .Resulto(\流水段寄存器_3_resulto ));  // open: ALUctr, ALUctro, ALUASrc, ALUASrco, ALUBSrc, ALUBSrco, BandJ, BandJo, BusA, BusAo, RS1, RS1o, RS2, RS2o, Zero, Zeroo, Imm, PCTarget, Dout, Immo, PCTargeto, Douto
  Hex_Digit_Display hex_digit_display_7 (.value(WB_IR[3:0]));  // open: dp
  Hex_Digit_Display hex_digit_display_8 (.value(WB_IR[7:4]));  // open: dp
  not not_3 (not_3_out, halt);
  Comparator #(.width(2), .mode("unsigned")) comparator_1 (
    .a(BusAFW), .b(2'b00), .eq(comparator_1_eq));  // open: gt, lt
  DataRAM dataram_1 (
    .Addr(\流水段寄存器_3_resulto [17:0]), .Din(\流水段寄存器_3_busbo ), .CLK(clk_t), .CLR(ReSet),
    .WE(\流水段寄存器_3_memwro ), .MemOp(\流水段寄存器_3_memopo ), .DataOut(dataram_1_dataout));  // open: AlignErr
  // Probe on Cycles
  Counter #(.width(16), .max('hffff), .trigger("falling"), .behavior("old")) \u_计数器  (
    .count(not_3_out), .Q(Cycles), .clk(clk_t), .clr(ReSet));  // open: load, D, carry, preset
  // Probe on \RS1转发次数 
  Counter #(.width(16), .max('hffff), .trigger("falling"), .behavior("old")) \u_计数器_2  (
    .count(not_4_out), .Q(\RS1转发次数 ), .clk(clk_t), .clr(ReSet));  // open: load, D, carry, preset
  not not_4 (not_4_out, comparator_1_eq);
  Comparator #(.width(3), .mode("unsigned")) comparator_2 (
    .a(EX_BandJ), .b(3'b001), .eq(comparator_2_eq));  // open: gt, lt
  Comparator #(.width(3), .mode("unsigned")) comparator_3 (
    .a(EX_BandJ), .b(3'b010), .eq(comparator_3_eq));  // open: gt, lt
  // Probe on \跳转指令数 
  Counter #(.width(16), .max('hffff), .trigger("falling"), .behavior("old")) \u_计数器_3  (
    .count(or_4_out), .Q(\跳转指令数 ), .clk(clk_t), .clr(ReSet));  // open: load, D, carry, preset
  or or_4 (or_4_out, comparator_2_eq, comparator_3_eq);
  \流水段寄存器  \u_流水段寄存器_4  (
    .CLR(ReSet), .CLK(clk_t), .WE(1'b1), .Halt(\流水段寄存器_3_halto ), .Halto(halt), .PC(M_PC), .PCo(WB_PC),
    .RegWr(\流水段寄存器_3_regwro ), .RegWro(\流水段寄存器_4_regwro ), .IR(\流水段寄存器_3_iro ),
    .MemtoReg(\流水段寄存器_3_memtorego ), .IRo(WB_IR), .MemtoRego(\流水段寄存器_4_memtorego ), .RD(\流水段寄存器_3_rdo ),
    .RDo(\流水段寄存器_4_rdo ), .Result(\流水段寄存器_3_resulto ), .Dout(dataram_1_dataout),
    .Resulto(\流水段寄存器_4_resulto ), .Douto(\流水段寄存器_4_douto ));  // open: ALUctr, ALUctro, ALUASrc, ALUASrco, ALUBSrc, ALUBSrco, BandJ, BandJo, MemOp, MemOpo, MemWr, MemWro, BusA, BusAo, RS1, RS1o, RS2, RS2o, Zero, Zeroo, BusB, BusBo, Imm, PCTarget, Immo, PCTargeto
  Counter #(.width(16), .max('hffff), .trigger("falling"), .behavior("old")) \u_计数器_4  (
    .count(Stall), .Q(\阻塞次数 ), .clk(clk_t), .clr(ReSet));  // open: load, D, carry, preset
  Multiplexer #(.width(32), .enable("false")) multiplexer_3 (
    .in0(\流水段寄存器_4_resulto ), .in1(\流水段寄存器_4_douto ), .out(WB_BusW), .sel(\流水段寄存器_4_memtorego ));
  // Probe on \阻塞次数 
  Comparator #(.width(2), .mode("unsigned")) comparator_4 (
    .a(BusBFW), .b(2'b00), .eq(comparator_4_eq));  // open: gt, lt
  Counter #(.width(16), .max('hffff), .trigger("falling"), .behavior("old")) \u_计数器_5  (
    .count(not_5_out), .Q(\RS2转发次数 ), .clk(clk_t), .clr(ReSet));  // open: load, D, carry, preset
  not not_5 (not_5_out, comparator_4_eq);
  Comparator #(.width(3), .mode("unsigned")) comparator_5 (
    .a(EX_BandJ), .b(3'b100), .eq(comparator_5_eq));  // open: gt, lt
  Comparator #(.width(3), .mode("unsigned")) comparator_6 (
    .a(EX_BandJ), .b(3'b101), .eq(comparator_6_eq));  // open: gt, lt
  Comparator #(.width(3), .mode("unsigned")) comparator_7 (
    .a(EX_BandJ), .b(3'b110), .eq(comparator_7_eq));  // open: gt, lt
  Comparator #(.width(3), .mode("unsigned")) comparator_8 (
    .a(EX_BandJ), .b(3'b111), .eq(comparator_8_eq));  // open: gt, lt
  // Probe on \冲刷次数 
  Counter #(.width(16), .max('hffff), .trigger("falling"), .behavior("old")) \u_计数器_6  (
    .count(PCsrc), .Q(\冲刷次数 ), .clk(clk_t), .clr(ReSet));  // open: load, D, carry, preset
  // Probe on \RS2转发次数 
  or or_5 (or_5_out, comparator_5_eq, comparator_6_eq, comparator_7_eq, comparator_8_eq);
  // Probe on \分支指令数 
  Counter #(.width(16), .max('hffff), .trigger("falling"), .behavior("old")) \u_计数器_7  (
    .count(or_5_out), .Q(\分支指令数 ), .clk(clk_t), .clr(ReSet));  // open: load, D, carry, preset

  // Other names for the same wires on the sheet: BP_En = BPEn; 总周期数[15:0] = Cycles

  // Notes on the sheet:
  //   断点调试
  //   输入引脚
  //   输出引脚
  //   contents of rom_1 (hex, n*v repeats v):
  //   93 113 193 213 293 313 393 413 493 513 593 613 693 713 793 813 893 913 993 a13 a93 b13 b93 c13 c93
  //   d13 d93 e13 e93 f13 f93 ff0100b7 f0008093 f0f1137 f0f10113 20f733 f0013b7 f0038393 200193 48771c63
  //   ff010b7 ff008093 f0f0f137 f010113 20f733 f003b7 f038393 300193 46771a63 ff00b7 ff08093 f0f1137
  //   f0f10113 20f733 f03b7 f38393 400193 44771863 f00ff0b7 f08093 f0f0f137 f010113 20f733 f000f3b7 500193
  //   42771863 ff0100b7 f0008093 f0f1137 f0f10113 20f0b3 f0013b7 f0038393 600193 40709663 ff010b7 ff008093
  //   f0f0f137 f010113 20f133 f003b7 f038393 700193 3e711463 ff0100b7 f0008093 10f0b3 ff0103b7 f0038393
  //   800193 3c709663 213 ff0100b7 f0008093 f0f1137 f0f10113 20f733 70313 120213 200293 fe5210e3 f0013b7
  //   f0038393 900193 38731a63 213 ff010b7 ff008093 f0f0f137 f010113 20f733 13 70313 120213 200293
  //   fc521ee3 f003b7 f038393 a00193 34731c63 213 ff00b7 ff08093 f0f1137 f0f10113 20f733 13 13 70313
  //   120213 200293 fc521ce3 f03b7 f38393 b00193 30731c63 213 ff0100b7 f0008093 f0f1137 f0f10113 20f733
  //   120213 200293 fe5212e3 f0013b7 f0038393 c00193 2e771263 213 ff010b7 ff008093 f0f0f137 f010113 13
  //   20f733 120213 200293 fe5210e3 f003b7 f038393 d00193 2a771663 213 ff00b7 ff08093 f0f1137 f0f10113 13
  //   13 20f733 120213 200293 fc521ee3 f03b7 f38393 e00193 26771863 213 ff0100b7 f0008093 13 f0f1137
  //   f0f10113 20f733 120213 200293 fe5210e3 f0013b7 f0038393 f00193 22771c63 213 ff010b7 ff008093 13
  //   f0f0f137 f010113 13 20f733 120213 200293 fc521ee3 f003b7 f038393 1000193 1e771e63 213 ff00b7 ff08093
  //   13 13 f0f1137 f0f10113 20f733 120213 200293 fc521ee3 f03b7 f38393 1100193 1c771063 213 f0f1137
  //   f0f10113 ff0100b7 f0008093 20f733 120213 200293 fe5212e3 f0013b7 f0038393 1200193 18771663 213
  //   f0f0f137 f010113 ff010b7 ff008093 13 20f733 120213 200293 fe5210e3 f003b7 f038393 1300193 14771a63
  //   213 f0f1137 f0f10113 ff00b7 ff08093 13 13 20f733 120213 200293 fc521ee3 f03b7 f38393 1400193
  //   10771c63 213 f0f1137 f0f10113 13 ff0100b7 f0008093 20f733 120213 200293 fe5210e3 f0013b7 f0038393
  //   1500193 e771063 213 f0f0f137 f010113 13 ff010b7 ff008093 13 20f733 120213 200293 fc521ee3 f003b7
  //   f038393 1600193 a771263 213 f0f1137 f0f10113 13 13 ff00b7 ff08093 20f733 120213 200293 fc521ee3
  //   f03b7 f38393 1700193 6771463 ff0100b7 f0008093 107133 393 1800193 4711863 ff00b7 ff08093 f133 393
  //   1900193 2711c63 70b3 393 1a00193 2709463 111110b7 11108093 22222137 22210113 20f033 393 1b00193
  //   701463 301863 deade537 ead50513 dead10cc c10537 fee50513 dead10cc c0001073
  //   请勿修改引脚名称、电路名称及电路封装外观
  //   为方便调试，需要输出流水线各段保存的PC值、时钟周期数、冒险处理次数、分支与跳转指令执行数等信息
  //   流水调试日志
  //   程序运行分析
  //   程序执行结束
  //   数码管输出
endmodule

module \跳转检测  (
  input  [2:0] M_BandJ,
  input  M_Zero,
  input  M_Result0,
  output PCsrc
);

  wire not_1_out, or_1_out;

  or or_1 (or_1_out, M_Zero, ~M_Result0);  // OR_Gate
  not not_1 (not_1_out, M_Zero);
  Multiplexer #(.select(3), .enable("false")) multiplexer_1 (
    .in0(1'b0), .in1(1'b1), .in2(1'b1), .in4(M_Zero), .in5(not_1_out), .in6(M_Result0), .in7(or_1_out),
    .out(PCsrc), .sel(M_BandJ));  // open: in3

  // Notes on the sheet:
  //   M_BandJ: pull=down
  //   M_Zero: pull=down
  //   输入信号
  //   请勿修改引脚名称、电路名称及电路封装外观
  //   不要修改控制信号的编码定义、引脚名称和在布局中的位置。
  //   输出信号
endmodule

module \控制器  (
  input  [6:0] opcode,
  input  [2:0] funct3,
  input  [6:0] funct7,
  input  Stall,
  output [2:0] ExtOp,
  output RegWr,
  output [2:0] BandJ,
  output ALUASrc,
  output [1:0] ALUBSrc,
  output [3:0] ALUctr,
  output MemtoReg,
  output [2:0] MemOp,
  output MemWr,
  output Halt
);

  wire and_1_out, and_2_out, and_3_out, and_4_out, and_5_out, and_6_out, and_7_out, and_8_out, and_9_out,
       and_10_out, and_11_out, and_12_out, and_13_out, and_14_out, and_15_out, and_16_out, and_17_out,
       B_Instr, I_Arith, I_jalr, I_load, J_jal, or_1_out, or_2_out, R_Arith, S_Instr, U_auipc, U_lui;
  wire [1:0] or_4_out, or_5_out, or_11_out;
  wire [2:0] or_13_out;
  wire [3:0] or_7_out;

  Comparator #(.width(7), .mode("unsigned")) comparator_1 (.a(opcode), .b(7'b0110111), .eq(U_lui));  // open: gt, lt
  Comparator #(.width(7), .mode("unsigned")) comparator_2 (.a(opcode), .b(7'b1100111), .eq(I_jalr));  // open: gt, lt
  Comparator #(.width(7), .mode("unsigned")) comparator_3 (.a(opcode), .b(7'b0010111), .eq(U_auipc));  // open: gt, lt
  Comparator #(.width(7), .mode("unsigned")) comparator_4 (.a(opcode), .b(7'b1100011), .eq(B_Instr));  // open: gt, lt
  Comparator #(.width(7), .mode("unsigned")) comparator_5 (.a(opcode), .b(7'b0010011), .eq(I_Arith));  // open: gt, lt
  Comparator #(.width(7), .mode("unsigned")) comparator_6 (.a(opcode), .b(7'b0000011), .eq(I_load));  // open: gt, lt
  Comparator #(.width(7), .mode("unsigned")) comparator_7 (.a(opcode), .b(7'b0110011), .eq(R_Arith));  // open: gt, lt
  Comparator #(.width(7), .mode("unsigned")) comparator_8 (.a(opcode), .b(7'b0100011), .eq(S_Instr));  // open: gt, lt
  or or_1 (or_1_out, U_lui, U_auipc, I_Arith, R_Arith, J_jal, I_jalr, I_load);
  or or_2 (or_2_out, U_auipc, J_jal, I_jalr);
  or or_3 (or_4_out[1], U_lui, U_auipc, I_Arith, I_load, S_Instr);
  or or_4 (or_4_out[0], J_jal, I_jalr);
  or or_5 (or_5_out[0], U_lui, U_auipc, B_Instr);
  or or_6 (or_5_out[1], B_Instr, S_Instr);
  and and_1 (and_1_out, I_Arith, funct3[0]);
  or or_7 (or_7_out[0], U_lui, and_1_out, and_2_out, and_3_out);
  and and_2 (and_2_out, R_Arith, funct3[0]);
  and and_3 (and_3_out, B_Instr, funct3[1], funct3[2]);
  and and_4 (and_4_out, I_Arith, funct3[1]);
  or or_8 (or_7_out[1], U_lui, and_4_out, and_5_out, B_Instr);
  and and_5 (and_5_out, R_Arith, funct3[1]);
  or or_9 (or_7_out[2], U_lui, and_6_out, and_7_out);
  and and_6 (and_6_out, I_Arith, funct3[2]);
  and and_7 (and_7_out, R_Arith, funct3[2]);
  or or_10 (or_7_out[3], U_lui, and_8_out, and_9_out);
  and and_8 (and_8_out, funct7[5], I_Arith, funct3[0], ~funct3[1], funct3[2]);  // AND_Gate
  and and_9 (and_9_out, R_Arith, funct7[5]);
  or or_11 (or_11_out[0], J_jal, and_10_out);
  and and_10 (and_10_out, B_Instr, funct3[0]);
  or or_12 (or_11_out[1], I_jalr, and_11_out);
  and and_11 (and_11_out, B_Instr, funct3[2]);
  and and_12 (and_12_out, I_load, ~funct3[0], ~funct3[1]);  // AND_Gate
  or or_13 (or_13_out[0], and_12_out, and_13_out);
  and and_13 (and_13_out, S_Instr, ~funct3[0], ~funct3[1]);  // AND_Gate
  and and_14 (and_14_out, I_load, funct3[0], ~funct3[1]);  // AND_Gate
  or or_14 (or_13_out[1], and_14_out, and_15_out);
  and and_15 (and_15_out, S_Instr, funct3[0], ~funct3[1]);  // AND_Gate
  and and_16 (and_16_out, I_load, ~funct3[1], ~funct3[2]);  // AND_Gate
  or or_15 (or_13_out[2], and_16_out, and_17_out);
  and and_17 (and_17_out, S_Instr, ~funct3[1], ~funct3[2]);  // AND_Gate
  Comparator #(.width(7), .mode("unsigned")) comparator_9 (.a(opcode), .b(7'b1101111), .eq(J_jal));  // open: gt, lt
  Comparator #(.width(7), .mode("unsigned")) comparator_10 (.a(opcode), .b(7'b1110011), .eq(Halt));  // open: gt, lt
  and and_18 (RegWr, or_1_out, ~Stall);  // AND_Gate
  and and_19 (ALUASrc, or_2_out, ~Stall);  // AND_Gate
  Multiplexer #(.width(2), .enable("false")) multiplexer_1 (.in0(or_4_out), .in1(2'b00), .out(ALUBSrc), .sel(Stall));
  and and_20 (MemWr, S_Instr, ~Stall);  // AND_Gate
  Multiplexer #(.width(3), .enable("false")) multiplexer_2 (
    .in0({J_jal, or_5_out}), .in1(3'b000), .out(ExtOp), .sel(Stall));
  Multiplexer #(.width(4), .enable("false")) multiplexer_3 (.in0(or_7_out), .in1(4'b0000), .out(ALUctr), .sel(Stall));
  Multiplexer #(.width(3), .enable("false")) multiplexer_4 (
    .in0({B_Instr, or_11_out}), .in1(3'b000), .out(BandJ), .sel(Stall));
  and and_21 (MemtoReg, I_load, ~Stall);  // AND_Gate
  Multiplexer #(.width(3), .enable("false")) multiplexer_5 (.in0(or_13_out), .in1(3'b000), .out(MemOp), .sel(Stall));

  // Notes on the sheet:
  //   输入引脚
  //   请勿修改引脚名称、电路名称及电路封装外观
  //   提示：根据指令种类，把7位指令code用一位指令类型标志位来表示，再通过功能码来区分具体指令，生成控制信号。
  //   输出引脚
endmodule

module IFU (
  input  Reset,
  input  BPEn,
  input  PCSrc,
  input  Stall,
  input  [31:0] Initial_Address,
  input  [31:0] BP_PC,
  input  [31:0] PCTarget,
  input  CLK,
  input  halt,
  output [31:0] PC
);

  wire and_1_out, BP_trigger, comparator_1_eq, nand_1_out, or_1_out;
  wire [31:0] adder_1_out, multiplexer_1_out, multiplexer_2_out;

  Adder #(.width(32)) adder_1 (.a(PC), .b(32'h4), .out(adder_1_out));  // open: cin, cout
  Multiplexer #(.width(32), .enable("false")) multiplexer_1 (
    .in0(adder_1_out), .in1(PCTarget), .out(multiplexer_1_out), .sel(PCSrc));
  Multiplexer #(.width(32), .enable("false")) multiplexer_2 (
    .in0(multiplexer_1_out), .in1(Initial_Address), .out(multiplexer_2_out), .sel(Reset));
  nand nand_1 (nand_1_out, ~Reset, and_1_out);  // NAND_Gate
  Register #(.width(32), .Select("low")) u_PC (.D(multiplexer_2_out), .en(nand_1_out), .Q(PC), .clk(CLK));  // open: clr
  and and_1 (and_1_out, or_1_out, ~PCSrc);  // AND_Gate
  Comparator #(.width(32), .mode("unsigned")) comparator_1 (.a(BP_PC), .b(PC), .eq(comparator_1_eq));  // open: gt, lt
  or or_1 (or_1_out, halt, BP_trigger, Stall);
  and and_2 (BP_trigger, BPEn, comparator_1_eq);

  // Other names for the same wires on the sheet: BP_En = BPEn; Init_Addr[31:0] = Initial_Address

  // Notes on the sheet:
  //   PCSrc: pull=down
  //   PCTarget: pull=down
  //   Stall: pull=down
  //   断点调试
  //   输入信号
  //   请勿修改引脚名称、电路名称及电路封装外观
  //   指令存储器256KB，数据位为32位，地址位为16位。PC寄存器数据宽度32位，片选信号高电平有效
  //   输出信号
endmodule

module IDU (
  input  [2:0] ExtOp,
  input  RegWr,
  input  [4:0] WB_Rd,
  input  [31:0] IR,
  input  [31:0] BusW,
  input  CLK,
  output [6:0] OpCode,
  output [2:0] Funct3,
  output [6:0] Funct7,
  output [31:0] Imm,
  output [31:0] BusA,
  output [31:0] BusB,
  output [4:0] Rd,
  output [4:0] Rs1,
  output [4:0] Rs2
);

  \立即数扩展器  \u_立即数扩展器_1  (.Instr(IR), .Extop(ExtOp), .imm(Imm));
  RegFile regfile_1 (
    .R1_num(IR[19:15]), .R2_num(IR[24:20]), .Write_Reg_num(WB_Rd), .Write_Enable(RegWr), .Clock(CLK),
    .Din(BusW), .Reg1Out(BusA), .Reg2Out(BusB));

  assign Funct3 = IR[14:12];
  assign Funct7 = IR[31:25];
  assign OpCode = IR[6:0];
  assign Rd = IR[11:7];
  assign Rs1 = IR[19:15];
  assign Rs2 = IR[24:20];

  // Other names for the same wires on the sheet: op[6:0] = IR[6:0]

  // Notes on the sheet:
  //   BusW: pull=down
  //   ExtOp: pull=down
  //   RegWr: pull=down
  //   WB_Rd: pull=down
  //   输入信号
  //   为了后续实验中的引用，不要修改ExtOP编码定义。
  //   请勿修改引脚名称、电路名称及电路封装外观
  //   修改寄存器堆电路设计，0号寄存器始终为0。
  //   输出信号
endmodule

module RegFile (
  input  [4:0] R1_num,
  input  [4:0] R2_num,
  input  [4:0] Write_Reg_num,
  input  [31:0] Din,
  input  Write_Enable,
  input  Clock,
  output [31:0] Reg1Out,
  output [31:0] Reg2Out
);

  wire and_1_out, and_2_out, and_3_out, and_4_out, and_5_out, and_6_out, and_7_out, and_8_out, and_9_out,
       and_10_out, and_11_out, and_12_out, and_13_out, and_14_out, and_15_out, and_16_out, and_17_out,
       and_18_out, and_19_out, and_20_out, and_21_out, and_22_out, and_23_out, and_24_out, and_25_out,
       and_26_out, and_27_out, and_28_out, and_29_out, and_30_out, and_31_out, and_32_out, decoder_1_out0,
       decoder_1_out1, decoder_1_out2, decoder_1_out3, decoder_1_out4, decoder_1_out5, decoder_1_out6,
       decoder_1_out7, decoder_1_out8, decoder_1_out9, decoder_1_out10, decoder_1_out11, decoder_1_out12,
       decoder_1_out13, decoder_1_out14, decoder_1_out15, decoder_1_out16, decoder_1_out17, decoder_1_out18,
       decoder_1_out19, decoder_1_out20, decoder_1_out21, decoder_1_out22, decoder_1_out23, decoder_1_out24,
       decoder_1_out25, decoder_1_out26, decoder_1_out27, decoder_1_out28, decoder_1_out29, decoder_1_out30,
       decoder_1_out31, not_1_out;
  wire [31:0] _0_q, _1_q, _2_q, _3_q, _4_q, _5_q, _6_q, _7_q, _8_q, _9_q, _10_q, _11_q, _12_q, _13_q, _14_q,
       _15_q, _16_q, _17_q, _18_q, _19_q, _20_q, _21_q, _22_q, _23_q, _24_q, _25_q, _26_q, _27_q, _28_q,
       _29_q, _30_q, _31_q;

  Decoder #(.select(5), .enable("false")) decoder_1 (
    .out0(decoder_1_out0), .out1(decoder_1_out1), .out2(decoder_1_out2), .out3(decoder_1_out3),
    .out4(decoder_1_out4), .out5(decoder_1_out5), .out6(decoder_1_out6), .out7(decoder_1_out7),
    .out8(decoder_1_out8), .out9(decoder_1_out9), .out10(decoder_1_out10), .out11(decoder_1_out11),
    .out12(decoder_1_out12), .out13(decoder_1_out13), .out14(decoder_1_out14), .out15(decoder_1_out15),
    .out16(decoder_1_out16), .out17(decoder_1_out17), .out18(decoder_1_out18), .out19(decoder_1_out19),
    .out20(decoder_1_out20), .out21(decoder_1_out21), .out22(decoder_1_out22), .out23(decoder_1_out23),
    .out24(decoder_1_out24), .out25(decoder_1_out25), .out26(decoder_1_out26), .out27(decoder_1_out27),
    .out28(decoder_1_out28), .out29(decoder_1_out29), .out30(decoder_1_out30), .out31(decoder_1_out31),
    .sel(Write_Reg_num));
  and and_1 (and_1_out, decoder_1_out0, Write_Enable);
  and and_2 (and_2_out, decoder_1_out1, Write_Enable);
  and and_3 (and_3_out, decoder_1_out2, Write_Enable);
  and and_4 (and_4_out, decoder_1_out3, Write_Enable);
  and and_5 (and_5_out, decoder_1_out4, Write_Enable);
  and and_6 (and_6_out, decoder_1_out5, Write_Enable);
  and and_7 (and_7_out, decoder_1_out6, Write_Enable);
  and and_8 (and_8_out, decoder_1_out7, Write_Enable);
  and and_9 (and_9_out, decoder_1_out8, Write_Enable);
  and and_10 (and_10_out, decoder_1_out9, Write_Enable);
  and and_11 (and_11_out, decoder_1_out10, Write_Enable);
  and and_12 (and_12_out, decoder_1_out11, Write_Enable);
  and and_13 (and_13_out, decoder_1_out12, Write_Enable);
  and and_14 (and_14_out, decoder_1_out13, Write_Enable);
  and and_15 (and_15_out, decoder_1_out14, Write_Enable);
  and and_16 (and_16_out, decoder_1_out15, Write_Enable);
  and and_17 (and_17_out, decoder_1_out16, Write_Enable);
  and and_18 (and_18_out, decoder_1_out17, Write_Enable);
  and and_19 (and_19_out, decoder_1_out18, Write_Enable);
  and and_20 (and_20_out, decoder_1_out19, Write_Enable);
  and and_21 (and_21_out, decoder_1_out20, Write_Enable);
  and and_22 (and_22_out, decoder_1_out21, Write_Enable);
  and and_23 (and_23_out, decoder_1_out22, Write_Enable);
  and and_24 (and_24_out, decoder_1_out23, Write_Enable);
  and and_25 (and_25_out, decoder_1_out24, Write_Enable);
  and and_26 (and_26_out, decoder_1_out25, Write_Enable);
  and and_27 (and_27_out, decoder_1_out26, Write_Enable);
  and and_28 (and_28_out, decoder_1_out27, Write_Enable);
  and and_29 (and_29_out, decoder_1_out28, Write_Enable);
  and and_30 (and_30_out, decoder_1_out29, Write_Enable);
  and and_31 (and_31_out, decoder_1_out30, Write_Enable);
  and and_32 (and_32_out, decoder_1_out31, Write_Enable);
  not not_1 (not_1_out, Clock);
  Register #(.width(32), .Select("high")) _0 (.D({32{1'b0}}), .en(and_1_out), .Q(_0_q), .clk(not_1_out));  // open: clr
  Register #(.width(32), .Select("high")) _1 (.D(Din), .en(and_2_out), .Q(_1_q), .clk(not_1_out));  // open: clr
  Register #(.width(32), .Select("high")) _2 (.D(Din), .en(and_3_out), .Q(_2_q), .clk(not_1_out));  // open: clr
  Register #(.width(32), .Select("high")) _3 (.D(Din), .en(and_4_out), .Q(_3_q), .clk(not_1_out));  // open: clr
  Register #(.width(32), .Select("high")) _4 (.D(Din), .en(and_5_out), .Q(_4_q), .clk(not_1_out));  // open: clr
  Register #(.width(32), .Select("high")) _5 (.D(Din), .en(and_6_out), .Q(_5_q), .clk(not_1_out));  // open: clr
  Register #(.width(32), .Select("high")) _6 (.D(Din), .en(and_7_out), .Q(_6_q), .clk(not_1_out));  // open: clr
  Register #(.width(32), .Select("high")) _7 (.D(Din), .en(and_8_out), .Q(_7_q), .clk(not_1_out));  // open: clr
  Register #(.width(32), .Select("high")) _8 (.D(Din), .en(and_9_out), .Q(_8_q), .clk(not_1_out));  // open: clr
  Register #(.width(32), .Select("high")) _9 (.D(Din), .en(and_10_out), .Q(_9_q), .clk(not_1_out));  // open: clr
  Register #(.width(32), .Select("high")) _10 (.D(Din), .en(and_11_out), .Q(_10_q), .clk(not_1_out));  // open: clr
  Register #(.width(32), .Select("high")) _11 (.D(Din), .en(and_12_out), .Q(_11_q), .clk(not_1_out));  // open: clr
  Register #(.width(32), .Select("high")) _12 (.D(Din), .en(and_13_out), .Q(_12_q), .clk(not_1_out));  // open: clr
  Register #(.width(32), .Select("high")) _13 (.D(Din), .en(and_14_out), .Q(_13_q), .clk(not_1_out));  // open: clr
  Register #(.width(32), .Select("high")) _14 (.D(Din), .en(and_15_out), .Q(_14_q), .clk(not_1_out));  // open: clr
  Register #(.width(32), .Select("high")) _15 (.D(Din), .en(and_16_out), .Q(_15_q), .clk(not_1_out));  // open: clr
  Register #(.width(32), .Select("high")) _16 (.D(Din), .en(and_17_out), .Q(_16_q), .clk(not_1_out));  // open: clr
  Register #(.width(32), .Select("high")) _17 (.D(Din), .en(and_18_out), .Q(_17_q), .clk(not_1_out));  // open: clr
  Register #(.width(32), .Select("high")) _18 (.D(Din), .en(and_19_out), .Q(_18_q), .clk(not_1_out));  // open: clr
  Register #(.width(32), .Select("high")) _19 (.D(Din), .en(and_20_out), .Q(_19_q), .clk(not_1_out));  // open: clr
  Register #(.width(32), .Select("high")) _20 (.D(Din), .en(and_21_out), .Q(_20_q), .clk(not_1_out));  // open: clr
  Register #(.width(32), .Select("high")) _21 (.D(Din), .en(and_22_out), .Q(_21_q), .clk(not_1_out));  // open: clr
  Register #(.width(32), .Select("high")) _22 (.D(Din), .en(and_23_out), .Q(_22_q), .clk(not_1_out));  // open: clr
  Register #(.width(32), .Select("high")) _23 (.D(Din), .en(and_24_out), .Q(_23_q), .clk(not_1_out));  // open: clr
  Register #(.width(32), .Select("high")) _24 (.D(Din), .en(and_25_out), .Q(_24_q), .clk(not_1_out));  // open: clr
  Register #(.width(32), .Select("high")) _25 (.D(Din), .en(and_26_out), .Q(_25_q), .clk(not_1_out));  // open: clr
  Register #(.width(32), .Select("high")) _26 (.D(Din), .en(and_27_out), .Q(_26_q), .clk(not_1_out));  // open: clr
  Register #(.width(32), .Select("high")) _27 (.D(Din), .en(and_28_out), .Q(_27_q), .clk(not_1_out));  // open: clr
  Register #(.width(32), .Select("high")) _28 (.D(Din), .en(and_29_out), .Q(_28_q), .clk(not_1_out));  // open: clr
  Register #(.width(32), .Select("high")) _29 (.D(Din), .en(and_30_out), .Q(_29_q), .clk(not_1_out));  // open: clr
  Register #(.width(32), .Select("high")) _30 (.D(Din), .en(and_31_out), .Q(_30_q), .clk(not_1_out));  // open: clr
  Register #(.width(32), .Select("high")) _31 (.D(Din), .en(and_32_out), .Q(_31_q), .clk(not_1_out));  // open: clr
  Multiplexer #(.select(5), .width(32), .enable("false")) multiplexer_1 (
    .in0(_0_q), .in1(_1_q), .in2(_2_q), .in3(_3_q), .in4(_4_q), .in5(_5_q), .in6(_6_q), .in7(_7_q),
    .in8(_8_q), .in9(_9_q), .in10(_10_q), .in11(_11_q), .in12(_12_q), .in13(_13_q), .in14(_14_q),
    .in15(_15_q), .in16(_16_q), .in17(_17_q), .in18(_18_q), .in19(_19_q), .in20(_20_q), .in21(_21_q),
    .in22(_22_q), .in23(_23_q), .in24(_24_q), .in25(_25_q), .in26(_26_q), .in27(_27_q), .in28(_28_q),
    .in29(_29_q), .in30(_30_q), .in31(_31_q), .out(Reg1Out), .sel(R1_num));
  Multiplexer #(.select(5), .width(32), .enable("false")) multiplexer_2 (
    .in0(_0_q), .in1(_1_q), .in2(_2_q), .in3(_3_q), .in4(_4_q), .in5(_5_q), .in6(_6_q), .in7(_7_q),
    .in8(_8_q), .in9(_9_q), .in10(_10_q), .in11(_11_q), .in12(_12_q), .in13(_13_q), .in14(_14_q),
    .in15(_15_q), .in16(_16_q), .in17(_17_q), .in18(_18_q), .in19(_19_q), .in20(_20_q), .in21(_21_q),
    .in22(_22_q), .in23(_23_q), .in24(_24_q), .in25(_25_q), .in26(_26_q), .in27(_27_q), .in28(_28_q),
    .in29(_29_q), .in30(_30_q), .in31(_31_q), .out(Reg2Out), .sel(R2_num));

  // Other names for the same wires on the sheet: CLK = Clock; RA[4:0] = R1_num; RB[4:0] = R2_num; RDA[31:0] = Reg1Out;
  //   RDB[31:0] = Reg2Out; RW[4:0] = Write_Reg_num; WE = Write_Enable

  // Notes on the sheet:
  //   输入引脚
  //   请勿修改引脚名称、电路名称及电路封装外观
  //   提示：使用译码器、多路选择器和32位寄存器及逻辑门实现寄存器堆，禁止直接使用存储器组件。
  //   输出引脚
endmodule

module \立即数扩展器  (
  input  [31:0] Instr,
  input  [2:0] Extop,
  output [31:0] imm
);

  wire [11:0] bit_extender_2_out;
  wire [19:0] bit_extender_1_out;
  wire [20:0] bit_extender_4_out;
  wire [31:0] bit_extender_3_out;

  assign bit_extender_1_out = {{19{Instr[31]}}, Instr[31]};  // Bit_Extender bit_extender_1
  assign bit_extender_2_out = {{11{Instr[31]}}, Instr[31]};  // Bit_Extender bit_extender_2
  assign bit_extender_3_out = {{20{Instr[31]}}, Instr[31:20]};  // Bit_Extender bit_extender_3
  assign bit_extender_4_out = {{20{Instr[31]}}, Instr[31]};  // Bit_Extender bit_extender_4
  Multiplexer #(.select(3), .width(32), .enable("false")) multiplexer_1 (
    .in0(bit_extender_3_out), .in1({Instr[31:12], {12{1'b0}}}),
    .in2({bit_extender_4_out, Instr[30:25], Instr[11:7]}),
    .in3({bit_extender_1_out, Instr[7], Instr[30:25], Instr[11:8], 1'b0}),
    .in4({bit_extender_2_out, Instr[19:12], Instr[20], Instr[30:21], 1'b0}), .out(imm), .sel(Extop));  // open: in5, in6, in7

  // Notes on the sheet:
  //   Extop: pull=down
  //   Instr: pull=down
  //   输入引脚
  //   输出引脚
endmodule

module SEL (
  input  Mem2,
  input  Mem1,
  input  Mem0,
  input  Addr1,
  input  Addr0,
  output Sel3,
  output Sel2,
  output Sel1,
  output Sel0
);

  wire and_1_out, and_2_out, and_3_out, and_4_out, and_5_out, and_6_out, and_7_out, and_8_out, and_9_out,
       and_10_out, and_11_out, and_12_out, not_1_out, not_2_out, not_3_out, not_4_out, not_5_out, not_6_out,
       not_7_out, not_8_out, not_9_out, not_10_out, not_11_out, not_12_out, not_13_out, not_14_out,
       not_15_out, not_16_out, not_17_out, not_18_out, not_19_out, not_20_out, not_21_out, not_22_out,
       not_23_out, not_24_out, not_25_out, not_26_out, not_27_out, not_28_out, not_29_out, not_30_out,
       not_31_out, not_32_out, not_33_out, not_34_out, not_35_out, not_36_out;

  not not_1 (not_1_out, Mem2);
  not not_2 (not_2_out, Mem1);
  not not_3 (not_3_out, Mem0);
  not not_4 (not_4_out, Addr1);
  not not_5 (not_5_out, Addr0);
  not not_6 (not_6_out, Mem1);
  not not_7 (not_7_out, Mem0);
  not not_8 (not_8_out, Addr0);
  not not_9 (not_9_out, Mem2);
  not not_10 (not_10_out, Mem1);
  not not_11 (not_11_out, Mem0);
  not not_12 (not_12_out, Addr1);
  not not_13 (not_13_out, Addr0);
  not not_14 (not_14_out, Mem1);
  not not_15 (not_15_out, Addr0);
  not not_16 (not_16_out, Mem0);
  not not_17 (not_17_out, Addr0);
  not not_18 (not_18_out, Mem2);
  not not_19 (not_19_out, Mem0);
  not not_20 (not_20_out, Addr1);
  not not_21 (not_21_out, Addr0);
  not not_22 (not_22_out, Mem1);
  not not_23 (not_23_out, Addr1);
  not not_24 (not_24_out, Mem0);
  not not_25 (not_25_out, Addr1);
  not not_26 (not_26_out, Addr0);
  not not_27 (not_27_out, Mem2);
  not not_28 (not_28_out, Mem1);
  not not_29 (not_29_out, Addr1);
  not not_30 (not_30_out, Addr0);
  not not_31 (not_31_out, Mem1);
  not not_32 (not_32_out, Addr1);
  not not_33 (not_33_out, Addr0);
  not not_34 (not_34_out, Mem0);
  not not_35 (not_35_out, Addr1);
  not not_36 (not_36_out, Addr0);
  and and_1 (and_1_out, not_1_out, not_2_out, not_3_out, not_4_out, not_5_out);
  and and_2 (and_2_out, not_6_out, Mem0, Addr1, Addr0);
  and and_3 (and_3_out, Mem1, not_7_out, Addr1, not_8_out);
  and and_4 (and_4_out, not_9_out, not_10_out, not_11_out, not_12_out, not_13_out);
  and and_5 (and_5_out, not_14_out, Mem0, Addr1, not_15_out);
  and and_6 (and_6_out, Mem1, not_16_out, Addr1, not_17_out);
  and and_7 (and_7_out, not_18_out, not_19_out, not_20_out, not_21_out);
  and and_8 (and_8_out, not_22_out, Mem0, not_23_out, Addr0);
  and and_9 (and_9_out, Mem1, not_24_out, not_25_out, not_26_out);
  and and_10 (and_10_out, not_27_out, not_28_out, not_29_out, not_30_out);
  and and_11 (and_11_out, not_31_out, Mem0, not_32_out, not_33_out);
  and and_12 (and_12_out, Mem1, not_34_out, not_35_out, not_36_out);
  or or_1 (Sel3, and_1_out, and_2_out, and_3_out);
  or or_2 (Sel2, and_4_out, and_5_out, and_6_out);
  or or_3 (Sel1, and_7_out, and_8_out, and_9_out);
  or or_4 (Sel0, and_10_out, and_11_out, and_12_out);
endmodule

module DataRAM (
  input  CLK,
  input  CLR,
  input  WE,
  input  [2:0] MemOp,
  input  [17:0] Addr,
  input  [31:0] Din,
  output AlignErr,
  output [31:0] DataOut
);

  wire and_1_out, and_3_out, and_4_out, and_5_out, or_1_out, or_2_out, or_3_out, or_4_out;
  wire [3:0] SEL;
  wire [7:0] multiplexer_4_out, multiplexer_5_out, multiplexer_6_out;
  wire [31:0] bit_extender_1_out, bit_extender_2_out, bit_extender_3_out, bit_extender_4_out,
       bit_extender_5_out, bit_extender_6_out, Din_Aligened, multiplexer_1_out, multiplexer_2_out, RESULT,
       shifter_1_out, shifter_2_out, shifter_3_out, shifter_4_out;

  assign bit_extender_1_out = {{24{1'b0}}, Din[7:0]};  // Bit_Extender bit_extender_1
  assign bit_extender_2_out = {{16{1'b0}}, Din[15:0]};  // Bit_Extender bit_extender_2
  Shifter #(.width(32)) shifter_1 (.in(bit_extender_1_out), .\dist (5'b01000), .out(shifter_1_out));
  Shifter #(.width(32)) shifter_2 (.in(bit_extender_1_out), .\dist (5'b10000), .out(shifter_2_out));
  Shifter #(.width(32)) shifter_3 (.in(bit_extender_1_out), .\dist (5'b11000), .out(shifter_3_out));
  Shifter #(.width(32)) shifter_4 (.in(bit_extender_2_out), .\dist (5'b10000), .out(shifter_4_out));
  SEL sel_1 (
    .Mem2(MemOp[2]), .Mem1(MemOp[1]), .Mem0(MemOp[0]), .Addr1(Addr[1]), .Addr0(Addr[0]), .Sel3(SEL[3]),
    .Sel2(SEL[2]), .Sel1(SEL[1]), .Sel0(SEL[0]));
  and and_1 (and_1_out, SEL[3], WE);
  Multiplexer #(.select(2), .width(32), .enable("false")) multiplexer_1 (
    .in0(bit_extender_1_out), .in1(shifter_1_out), .in2(shifter_2_out), .in3(shifter_3_out),
    .out(multiplexer_1_out), .sel(Addr[1:0]));
  Multiplexer #(.select(2), .width(32), .enable("false")) multiplexer_2 (
    .in0(bit_extender_2_out), .in2(shifter_4_out), .out(multiplexer_2_out), .sel(Addr[1:0]));  // open: in1, in3
  or or_1 (or_1_out, SEL[3], WE);
  RAM #(.addrWidth(16), .bus("separate"), .Select("high"), .simpleMode("false")) ram_1 (
    .addr(Addr[17:2]), .din(Din_Aligened[31:24]), .data(RESULT[31:24]), .str(and_1_out), .sel(or_1_out),
    .clk(CLK), .clr(CLR));  // open: ld
  and and_2 (AlignErr, ~SEL[3], ~SEL[2], ~SEL[1], ~SEL[0]);  // AND_Gate
  Multiplexer #(.select(3), .width(32), .enable("false")) multiplexer_3 (
    .in0(Din), .in5(multiplexer_1_out), .in6(multiplexer_2_out), .out(Din_Aligened), .sel(MemOp));  // open: in1, in2, in3, in4, in7
  and and_3 (and_3_out, SEL[2], WE);
  RAM #(.addrWidth(16), .bus("separate"), .Select("high"), .simpleMode("false")) ram_2 (
    .addr(Addr[17:2]), .din(Din_Aligened[23:16]), .data(RESULT[23:16]), .str(and_3_out), .sel(or_2_out),
    .clk(CLK), .clr(CLR));  // open: ld
  or or_2 (or_2_out, SEL[2], WE);
  and and_4 (and_4_out, SEL[1], WE);
  RAM #(.addrWidth(16), .bus("separate"), .Select("high"), .simpleMode("false")) ram_3 (
    .addr(Addr[17:2]), .din(Din_Aligened[15:8]), .data(RESULT[15:8]), .str(and_4_out), .sel(or_3_out),
    .clk(CLK), .clr(CLR));  // open: ld
  or or_3 (or_3_out, SEL[1], WE);
  and and_5 (and_5_out, SEL[0], WE);
  RAM #(.addrWidth(16), .bus("separate"), .Select("high"), .simpleMode("false")) ram_4 (
    .addr(Addr[17:2]), .din(Din_Aligened[7:0]), .data(RESULT[7:0]), .str(and_5_out), .sel(or_4_out),
    .clk(CLK), .clr(CLR));  // open: ld
  or or_4 (or_4_out, SEL[0], WE);
  Multiplexer #(.select(4), .width(8), .enable("false")) multiplexer_4 (
    .in1(RESULT[7:0]), .in2(RESULT[15:8]), .in4(RESULT[23:16]), .in8(RESULT[31:24]), .out(multiplexer_4_out),
    .sel(SEL));  // open: in0, in3, in5, in6, in7, in9, in10, in11, in12, in13, in14, in15
  Multiplexer #(.select(4), .width(8), .enable("false")) multiplexer_5 (
    .in3(RESULT[7:0]), .in12(RESULT[23:16]), .out(multiplexer_5_out), .sel(SEL));  // open: in0, in1, in2, in4, in5, in6, in7, in8, in9, in10, in11, in13, in14, in15
  Multiplexer #(.select(4), .width(8), .enable("false")) multiplexer_6 (
    .in3(RESULT[15:8]), .in12(RESULT[31:24]), .out(multiplexer_6_out), .sel(SEL));  // open: in0, in1, in2, in4, in5, in6, in7, in8, in9, in10, in11, in13, in14, in15
  assign bit_extender_3_out = {{24{1'b0}}, multiplexer_4_out};  // Bit_Extender bit_extender_3
  assign bit_extender_4_out = {{24{multiplexer_4_out[7]}}, multiplexer_4_out};  // Bit_Extender bit_extender_4
  assign bit_extender_5_out = {{16{1'b0}}, {multiplexer_6_out, multiplexer_5_out}};  // Bit_Extender bit_extender_5
  assign bit_extender_6_out = {{16{multiplexer_6_out[7]}}, {multiplexer_6_out, multiplexer_5_out}};  // Bit_Extender bit_extender_6
  Multiplexer #(.select(3), .width(32), .enable("false")) multiplexer_7 (
    .in0(RESULT), .in1(bit_extender_3_out), .in2(bit_extender_5_out), .in5(bit_extender_4_out),
    .in6(bit_extender_6_out), .out(DataOut), .sel(MemOp));  // open: in3, in4, in7

  // Other names for the same wires on the sheet: AddrS[1:0] = Addr[1:0]; AddrR[15:0] = Addr[17:2];
  //   Dout[31:0] = DataOut

  // Notes on the sheet:
  //   输入引脚
  //   请勿修改引脚名称、电路名称及电路封装外观
  //   为了后续实验中的引用，不要修改MemOp的编码定义、引脚名称和在布局中的位置。
  //   32位数据存储器，按字节分4片存储，可按照字节、半字和字进行存储；读取字节或半字时，支持0扩展和符号位扩展。
  //   SEL3
  //   输出引脚
  //   SEL2
  //   SEL1
  //   SEL0
endmodule

module ALU (
  input  [3:0] ALUctr,
  input  [31:0] A,
  input  [31:0] B,
  output Zero,
  output [31:0] S
);

  wire adder32_1_cout, adder32_1_of, adder32_1_sf, aluctrl_1_alctr, aluctrl_1_sftctr, aluctrl_1_sigctr,
       aluctrl_1_subctr, multiplexer_1_out, xor_3_out, xor_4_out;
  wire [2:0] aluctrl_1_opctr;
  wire [31:0] adder32_1_s, and_1_out, bit_extender_1_out, bit_extender_2_out, or_1_out, shifter32_1_dataout,
       xor_1_out, xor_2_out;

  assign bit_extender_1_out = {{31{aluctrl_1_subctr}}, aluctrl_1_subctr};  // Bit_Extender bit_extender_1
  assign and_1_out = A & B;  // AND_Gate and_1, 32 bits wide
  assign or_1_out = A | B;  // OR_Gate or_1, 32 bits wide
  assign xor_1_out = A ^ B;  // XOR_Gate xor_1, 32 bits wide
  Shifter32 shifter32_1 (
    .DataIn(A), .shamt(B[4:0]), .L_R(aluctrl_1_sftctr), .A_L(aluctrl_1_alctr), .DataOut(shifter32_1_dataout));
  Adder32 adder32_1 (
    .OF(adder32_1_of), .SF(adder32_1_sf), .ZF(Zero), .X(A), .Y(xor_2_out), .Cin(aluctrl_1_subctr),
    .S(adder32_1_s), .Cout(adder32_1_cout));  // open: CF
  assign xor_2_out = B ^ bit_extender_1_out;  // XOR_Gate xor_2, 32 bits wide
  xor xor_3 (xor_3_out, aluctrl_1_subctr, adder32_1_cout);
  xor xor_4 (xor_4_out, adder32_1_of, adder32_1_sf);
  // Probe on A
  // Probe on B
  // Probe on S
  Multiplexer #(.enable("false")) multiplexer_1 (
    .in0(xor_3_out), .in1(xor_4_out), .out(multiplexer_1_out), .sel(aluctrl_1_sigctr));
  Multiplexer #(.select(3), .width(32), .enable("false")) multiplexer_2 (
    .in0(adder32_1_s), .in1(and_1_out), .in2(or_1_out), .in3(xor_1_out), .in4(shifter32_1_dataout), .in5(B),
    .in6(bit_extender_2_out), .out(S), .sel(aluctrl_1_opctr));  // open: in7
  ALUctrl aluctrl_1 (
    .SUBctr(aluctrl_1_subctr), .SFTctr(aluctrl_1_sftctr), .SIGctr(aluctrl_1_sigctr), .ALctr(aluctrl_1_alctr),
    .OPctr(aluctrl_1_opctr), .ALUctr(ALUctr));
  assign bit_extender_2_out = {{31{1'b0}}, multiplexer_1_out};  // Bit_Extender bit_extender_2

  // Other names for the same wires on the sheet: Result[31:0] = S

  // Notes on the sheet:
  //   A: pull=down
  //   B: pull=down
  //   ALUctr: pull=down
  //   输入引脚
  //   请勿修改引脚名称、电路名称及电路封装外观
  //   提示：使用32位并行加法器子电路、桶形移位器、ALU控制子电路实现32位ALU
  //   功能说明:32位ALU，输入32位操作数A、B，4位控制信号ALUctr，输出32位结果Reseult和1位Zero标志位
  //   输出引脚
  //   操作数和结果
endmodule

module ALUctrl (
  input  [3:0] ALUctr,
  output SUBctr,
  output SFTctr,
  output SIGctr,
  output ALctr,
  output [2:0] OPctr
);

  wire and_2_out, and_3_out;

  Multiplexer #(.select(4), .width(3), .enable("false")) multiplexer_1 (
    .in0(3'b000), .in1(3'b100), .in2(3'b110), .in3(3'b110), .in4(3'b011), .in5(3'b100), .in6(3'b010),
    .in7(3'b001), .in8(3'b000), .in13(3'b100), .in15(3'b101), .out(OPctr), .sel(ALUctr));  // open: in9, in10, in11, in12, in14
  and and_1 (SIGctr, ~ALUctr[3], ~ALUctr[2], ALUctr[1], ~ALUctr[0]);  // AND_Gate
  and and_2 (and_2_out, ~ALUctr[3], ~ALUctr[2], ALUctr[1], ALUctr[0]);  // AND_Gate
  and and_3 (and_3_out, ALUctr[3], ~ALUctr[2], ~ALUctr[1], ~ALUctr[0]);  // AND_Gate
  and and_4 (SFTctr, ~ALUctr[3], ~ALUctr[2], ~ALUctr[1], ALUctr[0]);  // AND_Gate
  and and_5 (ALctr, ALUctr[3], ALUctr[2], ~ALUctr[1], ALUctr[0]);  // AND_Gate
  or or_1 (SUBctr, SIGctr, and_2_out, and_3_out);

  // Other names for the same wires on the sheet: LRctr = SFTctr

  // Notes on the sheet:
  //   输入引脚
  //   ALU操作控制信号生成部件
  //   输出引脚
endmodule

module Adder32 (
  input  Cin,
  input  [31:0] X,
  input  [31:0] Y,
  output CF,
  output Cout,
  output OF,
  output SF,
  output [31:0] S,
  output ZF
);

  wire adder16_2_gg, adder16_2_pg, and_1_out, and_2_out, and_3_out, or_1_out;

  Adder16 adder16_1 (.X(X[31:16]), .Y(Y[31:16]), .C0(or_1_out), .S(S[31:16]), .C16(Cout));  // open: Pg, Gg
  and and_1 (and_1_out, ~Y[31], ~X[31], S[31]);  // AND_Gate
  and and_2 (and_2_out, Y[31], X[31], ~S[31]);  // AND_Gate
  and and_3 (and_3_out, Cin, adder16_2_pg);
  or or_1 (or_1_out, and_3_out, adder16_2_gg);
  or or_2 (OF, and_1_out, and_2_out);
  Adder16 adder16_2 (
    .X(X[15:0]), .Y(Y[15:0]), .C0(Cin), .S(S[15:0]), .Pg(adder16_2_pg), .Gg(adder16_2_gg));  // open: C16
  xor xor_1 (CF, Cout, Cin);
  // Probe on X
  // Probe on Y
  // Probe on S
  Comparator #(.width(32)) comparator_1 (.a({32{1'b0}}), .b(S), .eq(ZF));  // open: gt, lt

  assign SF = S[31];

  // Notes on the sheet:
  //   Cin: pull=down
  //   X: pull=down
  //   Y: pull=down
  //   输入引脚区
  //   输出引脚区
  //   请勿修改引脚名称、电路名称及电路封装外观
  //   提示：使用16位并行加法器子电路实现32位快速加法器
  //   功能说明:32位Adder  S=X+Y，Cout为最高位进位位，Cin为进位输入， S为和，溢出OF、进位CF、零ZF、符号SF。
  //   +
  //   =
  //   无符号加法
endmodule

// 移位器
module Shifter32 (
  input  [4:0] shamt,
  input  L_R,
  input  A_L,
  input  [31:0] DataIn,
  output [31:0] DataOut
);

  wire [0:0] multiplexer_2_out;
  wire [1:0] bit_extender_1_out, bit_extender_2_out, multiplexer_4_out;
  wire [3:0] bit_extender_3_out, bit_extender_4_out, multiplexer_6_out;
  wire [7:0] bit_extender_5_out, bit_extender_6_out, multiplexer_8_out;
  wire [15:0] bit_extender_8_out, multiplexer_10_out;
  wire [31:0] multiplexer_3_out, multiplexer_5_out, multiplexer_7_out, multiplexer_9_out;
  wire [31:16] multiplexer_9_out_2;
  wire [31:31] multiplexer_1_out;

  Multiplexer #(.enable("false")) multiplexer_1 (.in0(1'b0), .in1(DataIn[31]), .out(multiplexer_1_out[31]), .sel(A_L));
  Multiplexer #(.enable("false")) multiplexer_2 (.in0(1'b0), .in1(DataIn[31]), .out(multiplexer_2_out[0]), .sel(A_L));
  Multiplexer #(.select(2), .width(32), .enable("false")) multiplexer_3 (
    .in0(DataIn), .in1({multiplexer_1_out[31], DataIn[31:1]}), .in2(DataIn),
    .in3({DataIn[30:0], multiplexer_2_out[0]}), .out(multiplexer_3_out), .sel({L_R, shamt[0]}));
  assign bit_extender_1_out = {{1{multiplexer_1_out[31]}}, multiplexer_1_out[31]};  // Bit_Extender bit_extender_1
  assign bit_extender_2_out = {{1{1'b0}}, 1'b0};  // Bit_Extender bit_extender_2
  Multiplexer #(.width(2), .enable("false")) multiplexer_4 (
    .in0(bit_extender_2_out), .in1(multiplexer_3_out[31:30]), .out(multiplexer_4_out), .sel(A_L));
  assign bit_extender_3_out = {{2{bit_extender_1_out[1]}}, bit_extender_1_out};  // Bit_Extender bit_extender_3
  Multiplexer #(.select(2), .width(32), .enable("false")) multiplexer_5 (
    .in0(multiplexer_3_out), .in1({bit_extender_1_out, multiplexer_3_out[31:2]}), .in2(multiplexer_3_out),
    .in3({multiplexer_3_out[29:0], multiplexer_4_out}), .out(multiplexer_5_out), .sel({L_R, shamt[1]}));
  assign bit_extender_4_out = {{2{bit_extender_2_out[1]}}, bit_extender_2_out};  // Bit_Extender bit_extender_4
  Multiplexer #(.width(4), .enable("false")) multiplexer_6 (
    .in0(bit_extender_4_out), .in1(multiplexer_5_out[31:28]), .out(multiplexer_6_out), .sel(A_L));
  assign bit_extender_5_out = {{4{bit_extender_3_out[3]}}, bit_extender_3_out};  // Bit_Extender bit_extender_5
  Multiplexer #(.select(2), .width(32), .enable("false")) multiplexer_7 (
    .in0(multiplexer_5_out), .in1({bit_extender_3_out, multiplexer_5_out[31:4]}), .in2(multiplexer_5_out),
    .in3({multiplexer_5_out[27:0], multiplexer_6_out}), .out(multiplexer_7_out), .sel({L_R, shamt[2]}));
  assign bit_extender_6_out = {{4{bit_extender_4_out[3]}}, bit_extender_4_out};  // Bit_Extender bit_extender_6
  Multiplexer #(.width(8), .enable("false")) multiplexer_8 (
    .in0(bit_extender_6_out), .in1(multiplexer_7_out[31:24]), .out(multiplexer_8_out), .sel(A_L));
  Multiplexer #(.select(2), .width(32), .enable("false")) multiplexer_9 (
    .in0(multiplexer_7_out), .in1({bit_extender_5_out, multiplexer_7_out[31:8]}), .in2(multiplexer_7_out),
    .in3({multiplexer_7_out[23:0], multiplexer_8_out}), .out({multiplexer_9_out[15:0], multiplexer_9_out_2}),
    .sel({L_R, shamt[3]}));
  assign multiplexer_9_out[31:16] = {{8{bit_extender_5_out[7]}}, bit_extender_5_out};  // Bit_Extender bit_extender_7
  assign bit_extender_8_out = {{8{bit_extender_6_out[7]}}, bit_extender_6_out};  // Bit_Extender bit_extender_8
  Multiplexer #(.width(16), .enable("false")) multiplexer_10 (
    .in0(bit_extender_8_out), .in1(multiplexer_9_out[15:0]), .out(multiplexer_10_out), .sel(A_L));
  Multiplexer #(.select(2), .width(32), .enable("false")) multiplexer_11 (
    .in0({multiplexer_9_out[15:0], multiplexer_9_out_2}), .in1(multiplexer_9_out),
    .in2({multiplexer_9_out[15:0], multiplexer_9_out_2}), .in3({multiplexer_9_out_2, multiplexer_10_out}),
    .out(DataOut), .sel({L_R, shamt[4]}));

  // Other names for the same wires on the sheet: Din[31:0] = DataIn; Left_Right = L_R; Arth_Logic = A_L;
  //   Dout[31:0] = DataOut

  // Notes on the sheet:
  //   L/R,A/L: 00逻辑右移，01算术右移，10逻辑左移，11：循环左移
  //   输入引脚
  //   请勿修改引脚名称、电路名称及电路封装外观
  //   提示：使用多路选择器、逻辑门实现32位桶形移位器，禁止直接使用移位器组件。
  //   输出引脚
endmodule

module Adder16 (
  input  C0,
  input  [15:0] X,
  input  [15:0] Y,
  output C16,
  output Pg,
  output Gg,
  output [15:0] S
);

  wire cla4_1_gg, cla4_1_pg, cla4_2_gg, cla4_2_pg, cla4_3_gg, cla4_3_pg, cla4_4_gg, cla4_4_pg, clu4_1_c1,
       clu4_1_c2, clu4_1_c3;

  CLA4 cla4_1 (
    .X(X[15:12]), .F(S[15:12]), .Y(Y[15:12]), .Pg(cla4_1_pg), .Cin(clu4_1_c3), .Gg(cla4_1_gg));  // open: Cout
  CLA4 cla4_2 (.X(X[11:8]), .F(S[11:8]), .Y(Y[11:8]), .Pg(cla4_2_pg), .Cin(clu4_1_c2), .Gg(cla4_2_gg));  // open: Cout
  CLU4 clu4_1 (
    .P0(cla4_4_pg), .P1(cla4_3_pg), .P2(cla4_2_pg), .P3(cla4_1_pg), .C1(clu4_1_c1), .C3(clu4_1_c3),
    .G0(cla4_4_gg), .G1(cla4_3_gg), .G2(cla4_2_gg), .G3(cla4_1_gg), .C2(clu4_1_c2), .C4(C16), .C0(C0),
    .Pg(Pg), .Gg(Gg));
  CLA4 cla4_3 (.X(X[7:4]), .F(S[7:4]), .Y(Y[7:4]), .Pg(cla4_3_pg), .Cin(clu4_1_c1), .Gg(cla4_3_gg));  // open: Cout
  CLA4 cla4_4 (.X(X[3:0]), .F(S[3:0]), .Y(Y[3:0]), .Pg(cla4_4_pg), .Cin(C0), .Gg(cla4_4_gg));  // open: Cout
  // Probe on X
  // Probe on Y
  // Probe on S

  // Notes on the sheet:
  //   Y: pull=down
  //   C0: pull=down
  //   X: pull=down
  //   输入引脚区
  //   请勿修改引脚名称、电路名称及电路封装外观
  //   提示：使用4位先行进位加法器和CLU子电路实现16位并行加法器
  //   功能说明:16位Adder  S=X+Y，C16为最高位进位位，C0为进位输入， Pg、Gg为成组进位生成传递函数
  //   输出引脚区
  //   +
  //   =
  //   无符号加法
endmodule

module CLA4 (
  input  [3:0] X,
  input  [3:0] Y,
  input  Cin,
  output [3:0] F,
  output Cout,
  output Pg,
  output Gg
);

  wire clu4_1_c1, clu4_1_c2, clu4_1_c3, fa_1_g, fa_1_p, fa_2_g, fa_2_p, fa_3_g, fa_3_p, fa_4_g, fa_4_p;

  FA fa_1 (.A(X[3]), .F(F[3]), .B(Y[3]), .P(fa_1_p), .Cin(clu4_1_c3), .G(fa_1_g));
  Hex_Digit_Display hex_digit_display_1 (.value(X));  // open: dp
  FA fa_2 (.A(X[2]), .F(F[2]), .B(Y[2]), .P(fa_2_p), .Cin(clu4_1_c2), .G(fa_2_g));
  Hex_Digit_Display hex_digit_display_2 (.value(Y));  // open: dp
  CLU4 clu4_1 (
    .P0(fa_4_p), .P1(fa_3_p), .P2(fa_2_p), .P3(fa_1_p), .C1(clu4_1_c1), .C3(clu4_1_c3), .G0(fa_4_g),
    .G1(fa_3_g), .G2(fa_2_g), .G3(fa_1_g), .C2(clu4_1_c2), .C4(Cout), .C0(Cin), .Pg(Pg), .Gg(Gg));
  FA fa_3 (.A(X[1]), .F(F[1]), .B(Y[1]), .P(fa_3_p), .Cin(clu4_1_c1), .G(fa_3_g));
  Hex_Digit_Display hex_digit_display_3 (.value(F));  // open: dp
  FA fa_4 (.A(X[0]), .F(F[0]), .B(Y[0]), .P(fa_4_p), .Cin(Cin), .G(fa_4_g));

  // Other names for the same wires on the sheet: Z[3:0] = F

  // Notes on the sheet:
  //   +
  //   =
  //   输出
  //   输入
  //   请勿修改引脚名称、电路名称及电路封装外观
  //   提示：使用全加器和CLU子电路实现四位先行进位加法器CLA4
endmodule

module CLU4 (
  input  P0,
  input  P1,
  input  P2,
  input  P3,
  input  G0,
  input  G1,
  input  G2,
  input  G3,
  input  C0,
  output C1,
  output C3,
  output C2,
  output C4,
  output Pg,
  output Gg
);

  wire and_2_out, and_3_out, and_4_out, and_5_out, and_6_out, and_7_out, and_8_out, and_9_out, and_10_out,
       and_11_out;

  and and_1 (Pg, P3, P2, P1, P0);
  and and_2 (and_2_out, P3, G2);
  or or_1 (Gg, G3, and_2_out, and_3_out, and_4_out);
  and and_3 (and_3_out, P3, P2, G1);
  or or_2 (C4, Gg, and_5_out);
  and and_4 (and_4_out, P3, P2, P1, G0);
  and and_5 (and_5_out, P3, P2, P1, P0, C0);
  or or_3 (C3, G2, and_6_out, and_7_out, and_8_out);
  and and_6 (and_6_out, P2, G1);
  and and_7 (and_7_out, P2, P1, G0);
  and and_8 (and_8_out, P2, P1, P0, C0);
  or or_4 (C2, G1, and_9_out, and_10_out);
  and and_9 (and_9_out, P1, G0);
  and and_10 (and_10_out, P1, P0, C0);
  or or_5 (C1, G0, and_11_out);
  and and_11 (and_11_out, P0, C0);

  // Notes on the sheet:
  //   输入引脚
  //   请勿修改引脚名称、电路名称及电路封装外观
  //   提示：使用逻辑门电路实现4位四位先行进位部件CLU，Pg、Gg为成组进位生成传递函数
  //   输出引脚
endmodule

module FA (
  input  A,
  input  B,
  input  Cin,
  output F,
  output P,
  output G
);

  wire xor_1_out;

  xor xor_1 (xor_1_out, Cin, B);
  xor xor_2 (F, xor_1_out, A);
  or or_1 (P, A, B);
  and and_1 (G, A, B);

  // Notes on the sheet:
  //   输入引脚
  //   请勿修改引脚名称、电路名称及电路封装外观
  //   输出引脚
endmodule

module \阻塞检测  (
  input  [6:0] IF_opcode,
  input  [4:0] EX_rd,
  input  [4:0] IF_rs1,
  input  EX_MemtoReg,
  input  [4:0] IF_rs2,
  output Stall
);

  wire and_1_out, and_2_out, B_type, comparator_5_eq, comparator_6_eq, comparator_7_eq, I_cal, I_jalr,
       I_load, or_1_out, or_2_out, or_3_out, R_type, S_type;

  Comparator #(.width(7), .mode("unsigned")) comparator_1 (.a(IF_opcode), .b(7'b0110011), .eq(R_type));  // open: gt, lt
  Comparator #(.width(7), .mode("unsigned")) comparator_2 (.a(IF_opcode), .b(7'b1100111), .eq(I_jalr));  // open: gt, lt
  or or_1 (or_1_out, R_type, I_load, I_cal, I_jalr, S_type, B_type);
  or or_2 (or_2_out, R_type, S_type, B_type);
  Comparator #(.width(7), .mode("unsigned")) comparator_3 (.a(IF_opcode), .b(7'b0000011), .eq(I_load));  // open: gt, lt
  Comparator #(.width(7), .mode("unsigned")) comparator_4 (.a(IF_opcode), .b(7'b0100011), .eq(S_type));  // open: gt, lt
  Comparator #(.width(5), .mode("unsigned")) comparator_5 (
    .a(EX_rd), .b(IF_rs1), .eq(comparator_5_eq));  // open: gt, lt
  Comparator #(.width(5), .mode("unsigned")) comparator_6 (
    .a(EX_rd), .b(IF_rs2), .eq(comparator_6_eq));  // open: gt, lt
  Comparator #(.width(5), .mode("unsigned")) comparator_7 (
    .a(EX_rd), .b({5{1'b0}}), .eq(comparator_7_eq));  // open: gt, lt
  and and_1 (and_1_out, comparator_5_eq, or_1_out);
  and and_2 (and_2_out, comparator_6_eq, or_2_out);
  Comparator #(.width(7), .mode("unsigned")) comparator_8 (.a(IF_opcode), .b(7'b0010011), .eq(I_cal));  // open: gt, lt
  Comparator #(.width(7), .mode("unsigned")) comparator_9 (.a(IF_opcode), .b(7'b1100011), .eq(B_type));  // open: gt, lt
  or or_3 (or_3_out, and_1_out, and_2_out);
  and and_3 (Stall, EX_MemtoReg, ~comparator_7_eq, or_3_out);  // AND_Gate

  // Notes on the sheet:
  //   EX_MemtoReg: pull=down
  //   EX_rd: pull=down
  //   输入信号
  //   输出信号
endmodule

module \转发检测  (
  input  [4:0] EX_rs1,
  input  [4:0] M_rd,
  input  [4:0] EX_rs2,
  input  [4:0] WB_rd,
  input  M_RegWr,
  input  WB_RegWr,
  output [1:0] BusAFW,
  output [1:0] BusBFW
);

  wire and_2_out, and_5_out, comparator_1_eq, comparator_2_eq, comparator_3_eq, comparator_4_eq,
       comparator_5_eq, comparator_6_eq, comparator_7_eq, comparator_8_eq;

  Comparator #(.width(5), .mode("unsigned")) comparator_1 (
    .a(M_rd), .b({5{1'b0}}), .eq(comparator_1_eq));  // open: gt, lt
  Comparator #(.width(5), .mode("unsigned")) comparator_2 (.a(M_rd), .b(EX_rs1), .eq(comparator_2_eq));  // open: gt, lt
  Comparator #(.width(5), .mode("unsigned")) comparator_3 (
    .a(WB_rd), .b({5{1'b0}}), .eq(comparator_3_eq));  // open: gt, lt
  Comparator #(.width(5), .mode("unsigned")) comparator_4 (
    .a(WB_rd), .b(EX_rs1), .eq(comparator_4_eq));  // open: gt, lt
  and and_1 (BusAFW[0], M_RegWr, ~comparator_1_eq, comparator_2_eq);  // AND_Gate
  and and_2 (and_2_out, WB_RegWr, ~comparator_3_eq, comparator_4_eq);  // AND_Gate
  and and_3 (BusAFW[1], ~BusAFW[0], and_2_out);  // AND_Gate
  Comparator #(.width(5), .mode("unsigned")) comparator_5 (
    .a(M_rd), .b({5{1'b0}}), .eq(comparator_5_eq));  // open: gt, lt
  Comparator #(.width(5), .mode("unsigned")) comparator_6 (.a(M_rd), .b(EX_rs2), .eq(comparator_6_eq));  // open: gt, lt
  Comparator #(.width(5), .mode("unsigned")) comparator_7 (
    .a(WB_rd), .b({5{1'b0}}), .eq(comparator_7_eq));  // open: gt, lt
  Comparator #(.width(5), .mode("unsigned")) comparator_8 (
    .a(WB_rd), .b(EX_rs2), .eq(comparator_8_eq));  // open: gt, lt
  and and_4 (BusBFW[0], M_RegWr, ~comparator_5_eq, comparator_6_eq);  // AND_Gate
  and and_5 (and_5_out, WB_RegWr, ~comparator_7_eq, comparator_8_eq);  // AND_Gate
  and and_6 (BusBFW[1], ~BusBFW[0], and_5_out);  // AND_Gate

  // Notes on the sheet:
  //   EX_rs2: pull=down
  //   EX_rs1: pull=down
  //   WB_rd: pull=down
  //   M_rd: pull=down
  //   输入信号
  //   输出信号
endmodule

module \流水段寄存器  (
  input  CLR,
  input  [31:0] PC,
  input  CLK,
  input  WE,
  input  Halt,
  input  [31:0] IR,
  input  [3:0] ALUctr,
  input  ALUASrc,
  input  [1:0] ALUBSrc,
  input  [31:0] BusA,
  input  [2:0] BandJ,
  input  [2:0] MemOp,
  input  MemWr,
  input  [31:0] BusB,
  input  RegWr,
  input  MemtoReg,
  input  [4:0] RD,
  input  [31:0] Imm,
  input  [4:0] RS1,
  input  [4:0] RS2,
  input  Zero,
  input  [31:0] Result,
  input  [31:0] PCTarget,
  input  [31:0] Dout,
  output [31:0] PCo,
  output Halto,
  output [31:0] IRo,
  output [3:0] ALUctro,
  output ALUASrco,
  output [1:0] ALUBSrco,
  output [31:0] BusAo,
  output [2:0] BandJo,
  output [2:0] MemOpo,
  output MemWro,
  output [31:0] BusBo,
  output RegWro,
  output MemtoRego,
  output [4:0] RDo,
  output [31:0] Immo,
  output [4:0] RS1o,
  output [4:0] RS2o,
  output Zeroo,
  output [31:0] Resulto,
  output [31:0] PCTargeto,
  output [31:0] Douto
);

  wire multiplexer_2_out, multiplexer_5_out, multiplexer_7_out, multiplexer_8_out, multiplexer_9_out,
       multiplexer_18_out, not_1_out;
  wire [1:0] multiplexer_3_out;
  wire [2:0] multiplexer_4_out, multiplexer_6_out;
  wire [3:0] multiplexer_1_out;
  wire [4:0] multiplexer_11_out, multiplexer_12_out, multiplexer_13_out;
  wire [31:0] multiplexer_10_out, multiplexer_14_out, multiplexer_15_out, multiplexer_16_out,
       multiplexer_17_out, multiplexer_19_out, multiplexer_20_out, multiplexer_21_out;

  not not_1 (not_1_out, CLK);
  Multiplexer #(.width(4), .enable("false")) multiplexer_1 (
    .in0(ALUctr), .in1(4'b0000), .out(multiplexer_1_out), .sel(CLR));
  Multiplexer #(.enable("false")) multiplexer_2 (.in0(ALUASrc), .in1(1'b0), .out(multiplexer_2_out), .sel(CLR));
  Multiplexer #(.width(2), .enable("false")) multiplexer_3 (
    .in0(ALUBSrc), .in1(2'b00), .out(multiplexer_3_out), .sel(CLR));
  Multiplexer #(.width(3), .enable("false")) multiplexer_4 (
    .in0(BandJ), .in1(3'b000), .out(multiplexer_4_out), .sel(CLR));
  Multiplexer #(.enable("false")) multiplexer_5 (.in0(MemWr), .in1(1'b0), .out(multiplexer_5_out), .sel(CLR));
  Multiplexer #(.width(3), .enable("false")) multiplexer_6 (
    .in0(MemOp), .in1(3'b000), .out(multiplexer_6_out), .sel(CLR));
  Register #(.width(4), .trigger("falling"), .Select("low")) register_1 (
    .D(multiplexer_1_out), .en(WE), .Q(ALUctro), .clk(not_1_out));  // open: clr
  Register #(.width(1), .trigger("falling"), .Select("low")) register_2 (
    .D(multiplexer_2_out), .en(WE), .Q(ALUASrco), .clk(not_1_out));  // open: clr
  Register #(.width(2), .trigger("falling"), .Select("low")) register_3 (
    .D(multiplexer_3_out), .en(WE), .Q(ALUBSrco), .clk(not_1_out));  // open: clr
  Register #(.width(3), .trigger("falling"), .Select("low")) register_4 (
    .D(multiplexer_4_out), .en(WE), .Q(BandJo), .clk(not_1_out));  // open: clr
  Register #(.width(1), .trigger("falling"), .Select("low")) register_5 (
    .D(multiplexer_5_out), .en(WE), .Q(MemWro), .clk(not_1_out));  // open: clr
  Register #(.width(3), .trigger("falling"), .Select("low")) register_6 (
    .D(multiplexer_6_out), .en(WE), .Q(MemOpo), .clk(not_1_out));  // open: clr
  Multiplexer #(.enable("false")) multiplexer_7 (.in0(MemtoReg), .in1(1'b0), .out(multiplexer_7_out), .sel(CLR));
  Multiplexer #(.enable("false")) multiplexer_8 (.in0(RegWr), .in1(1'b0), .out(multiplexer_8_out), .sel(CLR));
  Multiplexer #(.enable("false")) multiplexer_9 (.in0(Halt), .in1(1'b0), .out(multiplexer_9_out), .sel(CLR));
  Multiplexer #(.width(32), .enable("false")) multiplexer_10 (
    .in0(PC), .in1({32{1'b0}}), .out(multiplexer_10_out), .sel(CLR));
  Multiplexer #(.width(5), .enable("false")) multiplexer_11 (
    .in0(RD), .in1({5{1'b0}}), .out(multiplexer_11_out), .sel(CLR));
  Multiplexer #(.width(5), .enable("false")) multiplexer_12 (
    .in0(RS1), .in1({5{1'b0}}), .out(multiplexer_12_out), .sel(CLR));
  Multiplexer #(.width(5), .enable("false")) multiplexer_13 (
    .in0(RS2), .in1({5{1'b0}}), .out(multiplexer_13_out), .sel(CLR));
  Register #(.width(1), .trigger("falling"), .Select("low")) register_7 (
    .D(multiplexer_7_out), .en(WE), .Q(MemtoRego), .clk(not_1_out));  // open: clr
  Register #(.width(1), .trigger("falling"), .Select("low")) register_8 (
    .D(multiplexer_8_out), .en(WE), .Q(RegWro), .clk(not_1_out));  // open: clr
  Register #(.width(1), .trigger("falling"), .Select("low")) register_9 (
    .D(multiplexer_9_out), .en(WE), .Q(Halto), .clk(not_1_out));  // open: clr
  Register #(.width(32), .trigger("falling"), .Select("low")) register_10 (
    .D(multiplexer_10_out), .en(WE), .Q(PCo), .clk(not_1_out));  // open: clr
  Register #(.width(5), .trigger("falling"), .Select("low")) register_11 (
    .D(multiplexer_11_out), .en(WE), .Q(RDo), .clk(not_1_out));  // open: clr
  Register #(.width(5), .trigger("falling"), .Select("low")) register_12 (
    .D(multiplexer_12_out), .en(WE), .Q(RS1o), .clk(not_1_out));  // open: clr
  Register #(.width(5), .trigger("falling"), .Select("low")) register_13 (
    .D(multiplexer_13_out), .en(WE), .Q(RS2o), .clk(not_1_out));  // open: clr
  Multiplexer #(.width(32), .enable("false")) multiplexer_14 (
    .in0(IR), .in1({32{1'b0}}), .out(multiplexer_14_out), .sel(CLR));
  Multiplexer #(.width(32), .enable("false")) multiplexer_15 (
    .in0(Imm), .in1({32{1'b0}}), .out(multiplexer_15_out), .sel(CLR));
  Multiplexer #(.width(32), .enable("false")) multiplexer_16 (
    .in0(BusA), .in1({32{1'b0}}), .out(multiplexer_16_out), .sel(CLR));
  Multiplexer #(.width(32), .enable("false")) multiplexer_17 (
    .in0(BusB), .in1({32{1'b0}}), .out(multiplexer_17_out), .sel(CLR));
  Multiplexer #(.enable("false")) multiplexer_18 (.in0(Zero), .in1(1'b0), .out(multiplexer_18_out), .sel(CLR));
  Multiplexer #(.width(32), .enable("false")) multiplexer_19 (
    .in0(Result), .in1({32{1'b0}}), .out(multiplexer_19_out), .sel(CLR));
  Multiplexer #(.width(32), .enable("false")) multiplexer_20 (
    .in0(PCTarget), .in1({32{1'b0}}), .out(multiplexer_20_out), .sel(CLR));
  Multiplexer #(.width(32), .enable("false")) multiplexer_21 (
    .in0(Dout), .in1({32{1'b0}}), .out(multiplexer_21_out), .sel(CLR));
  Register #(.width(32), .trigger("falling"), .Select("low")) register_14 (
    .D(multiplexer_14_out), .en(WE), .Q(IRo), .clk(not_1_out));  // open: clr
  Register #(.width(32), .trigger("falling"), .Select("low")) register_15 (
    .D(multiplexer_15_out), .en(WE), .Q(Immo), .clk(not_1_out));  // open: clr
  Register #(.width(32), .trigger("falling"), .Select("low")) register_16 (
    .D(multiplexer_16_out), .en(WE), .Q(BusAo), .clk(not_1_out));  // open: clr
  Register #(.width(32), .trigger("falling"), .Select("low")) register_17 (
    .D(multiplexer_17_out), .en(WE), .Q(BusBo), .clk(not_1_out));  // open: clr
  Register #(.width(1), .trigger("falling"), .Select("low")) register_18 (
    .D(multiplexer_18_out), .en(WE), .Q(Zeroo), .clk(not_1_out));  // open: clr
  Register #(.width(32), .trigger("falling"), .Select("low")) register_19 (
    .D(multiplexer_19_out), .en(WE), .Q(Resulto), .clk(not_1_out));  // open: clr
  Register #(.width(32), .trigger("falling"), .Select("low")) register_20 (
    .D(multiplexer_20_out), .en(WE), .Q(PCTargeto), .clk(not_1_out));  // open: clr
  Register #(.width(32), .trigger("falling"), .Select("low")) register_21 (
    .D(multiplexer_21_out), .en(WE), .Q(Douto), .clk(not_1_out));  // open: clr

  // Notes on the sheet:
  //   输入引脚区
  //   输出引脚区
endmodule

module DM (
  input  [15:0] Addr,
  input  [31:0] Din,
  input  CLK,
  input  CLR,
  input  [2:0] MemOp,
  input  WE,
  input  SEL,
  output [31:0] DataOut
);


  // Other names for the same wires on the sheet: Dout[31:0] = DataOut

  // Notes on the sheet:
  //   输入引脚区
  //   32位数据存储器，按字节分4片存储，可按照字节、半字和字进行存储；读取字节或半字时，支持0扩展和符号位扩展。
  //   为了后续实验中的引用，不要修改MemOp的编码定义，以及引脚名称和在布局图中位置。
  //   输出引脚区
endmodule

module EU (
  input  [3:0] ALUctr,
  input  ALUASrc,
  input  [1:0] ALUBSrc,
  input  [31:0] PC,
  input  [31:0] BusA,
  input  [31:0] BusB,
  input  [31:0] Imm,
  input  [2:0] BandJ,
  output [31:0] PCTarget,
  output [31:0] Result,
  output Zero
);

  wire comparator_1_eq;
  wire [31:0] multiplexer_1_out, multiplexer_2_out, multiplexer_3_out;

  Comparator #(.width(3), .mode("unsigned")) comparator_1 (
    .a(BandJ), .b(3'b010), .eq(comparator_1_eq));  // open: gt, lt
  Multiplexer #(.width(32), .enable("false")) multiplexer_1 (
    .in0(PC), .in1(BusA), .out(multiplexer_1_out), .sel(comparator_1_eq));
  Multiplexer #(.width(32), .enable("false")) multiplexer_2 (
    .in0(BusA), .in1(PC), .out(multiplexer_2_out), .sel(ALUASrc));
  Multiplexer #(.select(2), .width(32), .enable("false")) multiplexer_3 (
    .in0(BusB), .in1(32'h4), .in2(Imm), .out(multiplexer_3_out), .sel(ALUBSrc));  // open: in3
  Adder32 adder32_1 (.X(multiplexer_1_out), .Y(Imm), .S(PCTarget));  // open: CF, OF, SF, ZF, Cin, Cout
  ALU alu_1 (.A(multiplexer_2_out), .B(multiplexer_3_out), .ALUctr(ALUctr), .S(Result), .Zero(Zero));

  // Notes on the sheet:
  //   ALUBSrc: pull=down
  //   PCTarget: pull=down
  //   ALUASrc: pull=down
  //   ALUctr: pull=down
  //   Result: pull=down
  //   BandJ: pull=down
  //   输入信号
  //   请勿修改引脚名称、电路名称及电路封装外观
  //   为了后续实验中的引用，不要修改控制信号编码定义。
  //   输出信号
endmodule
